// Logisim project cpu24 - 重定向流水线.circ as structural Verilog
// 单周期硬布线控制器
module \单周期硬布线控制器  (
  input  [5:0] OP,
  input  [5:0] Func,
  output [3:0] ALU_OP,
  output MemToReg,
  output MemWrite,
  output ALU_SRC,
  output RegWrite,
  output SysCALL,
  output SignedExt,
  output RegDst,
  output Beq,
  output Bne,
  output JR,
  output JMP,
  output JAL
);

  \运算控制器自动生成  \u_运算控制器自动生成_1  (
    .OP0(OP[0]), .OP1(OP[1]), .OP2(OP[2]), .OP3(OP[3]), .OP4(OP[4]), .OP5(OP[5]), .F0(Func[0]), .F1(Func[1]),
    .F2(Func[2]), .F3(Func[3]), .F4(Func[4]), .F5(Func[5]), .S0(ALU_OP[0]), .S1(ALU_OP[1]), .S2(ALU_OP[2]),
    .S3(ALU_OP[3]));
  \控制信号自动生成  \u_控制信号自动生成_1  (
    .OP0(OP[0]), .OP1(OP[1]), .OP2(OP[2]), .OP3(OP[3]), .OP4(OP[4]), .OP5(OP[5]), .F0(Func[0]), .F1(Func[1]),
    .F2(Func[2]), .F3(Func[3]), .F4(Func[4]), .F5(Func[5]), .MemToReg(MemToReg), .MemWrite(MemWrite),
    .ALU_SRC(ALU_SRC), .RegWrite(RegWrite), .SysCALL(SysCALL), .SignedExt(SignedExt), .RegDst(RegDst),
    .BEQ(Beq), .BNE(Bne), .JR(JR), .JUMP(JMP), .JAL(JAL));

  // Other names for the same wires on the sheet: OP_CODE[5:0] = OP

  // Notes on the sheet:
  //   运算器控制器，根据指令生成运算器功能选择信号
  //   控制信号生成，产生数据通路需要的其他控制信号
endmodule

// 运算器控制器
module \运算控制器自动生成  (
  input  OP0,
  input  OP1,
  input  OP2,
  input  OP3,
  input  OP4,
  input  OP5,
  input  F0,
  input  F1,
  input  F2,
  input  F3,
  input  F4,
  input  F5,
  output S0,
  output S1,
  output S2,
  output S3
);

  wire and_1_out, and_2_out, and_3_out, and_4_out, and_5_out, and_6_out, and_7_out, and_8_out, and_9_out,
       and_10_out, and_11_out, and_12_out, and_13_out, and_14_out, and_15_out, and_16_out, and_17_out,
       and_18_out, and_19_out, and_20_out, and_21_out, and_22_out, and_23_out, and_24_out, and_25_out,
       and_26_out, and_27_out, and_28_out, not_1_out, not_2_out, not_3_out, not_4_out, not_5_out, not_6_out,
       not_7_out, not_8_out, not_9_out, not_10_out, not_11_out, not_12_out, not_13_out, not_14_out,
       not_15_out, not_16_out, not_17_out, not_18_out, not_19_out, not_20_out, not_21_out, not_22_out,
       not_23_out, not_24_out, not_25_out, not_26_out, not_27_out, not_28_out, not_29_out, not_30_out,
       not_31_out, not_32_out, not_33_out, not_34_out, not_35_out, not_36_out, not_37_out, not_38_out,
       not_39_out, not_40_out, not_41_out, not_42_out, not_43_out, not_44_out, not_45_out, not_46_out,
       not_47_out, not_48_out, not_49_out, not_50_out, not_51_out, not_52_out, not_53_out, not_54_out,
       not_55_out, not_56_out, not_57_out, not_58_out, not_59_out, not_60_out, not_61_out, not_62_out,
       not_63_out, not_64_out, not_65_out, not_66_out, not_67_out, not_68_out, not_69_out, not_70_out,
       not_71_out, not_72_out, not_73_out, not_74_out, not_75_out, not_76_out, not_77_out, not_78_out,
       not_79_out, not_80_out, not_81_out, not_82_out, not_83_out, not_84_out, not_85_out, not_86_out,
       not_87_out, not_88_out, not_89_out, not_90_out, not_91_out, not_92_out, not_93_out, not_94_out,
       not_95_out, not_96_out, not_97_out, not_98_out, not_99_out, not_100_out, not_101_out, not_102_out,
       not_103_out, not_104_out, not_105_out, not_106_out, not_107_out, not_108_out, not_109_out,
       not_110_out, not_111_out, not_112_out, not_113_out, not_114_out, not_115_out, not_116_out,
       not_117_out, not_118_out, not_119_out, not_120_out, not_121_out, not_122_out, not_123_out,
       not_124_out, not_125_out, not_126_out, not_127_out, not_128_out, not_129_out, not_130_out,
       not_131_out, not_132_out, not_133_out, not_134_out, not_135_out, not_136_out, not_137_out,
       not_138_out, not_139_out, not_140_out, not_141_out, not_142_out, not_143_out, not_144_out,
       not_145_out, not_146_out, not_147_out, not_148_out, not_149_out, not_150_out, not_151_out,
       not_152_out, not_153_out, not_154_out, not_155_out, not_156_out, not_157_out, not_158_out,
       not_159_out, not_160_out, not_161_out, not_162_out, not_163_out, not_164_out, not_165_out,
       not_166_out, not_167_out, not_168_out, not_169_out, not_170_out, not_171_out, not_172_out,
       not_173_out, not_174_out, not_175_out, not_176_out, not_177_out, not_178_out, not_179_out,
       not_180_out, not_181_out, not_182_out, not_183_out, not_184_out;

  not not_1 (not_1_out, OP5);
  not not_2 (not_2_out, OP4);
  not not_3 (not_3_out, OP3);
  not not_4 (not_4_out, OP2);
  not not_5 (not_5_out, OP1);
  not not_6 (not_6_out, OP0);
  not not_7 (not_7_out, F5);
  not not_8 (not_8_out, F4);
  not not_9 (not_9_out, F3);
  not not_10 (not_10_out, F2);
  not not_11 (not_11_out, OP5);
  not not_12 (not_12_out, OP4);
  not not_13 (not_13_out, OP3);
  not not_14 (not_14_out, OP2);
  not not_15 (not_15_out, OP1);
  not not_16 (not_16_out, OP0);
  not not_17 (not_17_out, F4);
  not not_18 (not_18_out, F3);
  not not_19 (not_19_out, F2);
  not not_20 (not_20_out, F1);
  not not_21 (not_21_out, F0);
  not not_22 (not_22_out, OP5);
  not not_23 (not_23_out, OP4);
  not not_24 (not_24_out, OP3);
  not not_25 (not_25_out, OP2);
  not not_26 (not_26_out, OP1);
  not not_27 (not_27_out, OP0);
  not not_28 (not_28_out, F4);
  not not_29 (not_29_out, F3);
  not not_30 (not_30_out, F2);
  not not_31 (not_31_out, F1);
  not not_32 (not_32_out, OP5);
  not not_33 (not_33_out, OP4);
  not not_34 (not_34_out, OP3);
  not not_35 (not_35_out, OP2);
  not not_36 (not_36_out, OP1);
  not not_37 (not_37_out, OP0);
  not not_38 (not_38_out, F4);
  not not_39 (not_39_out, F3);
  not not_40 (not_40_out, F1);
  not not_41 (not_41_out, F0);
  not not_42 (not_42_out, OP5);
  not not_43 (not_43_out, OP4);
  not not_44 (not_44_out, OP3);
  not not_45 (not_45_out, OP2);
  not not_46 (not_46_out, OP1);
  not not_47 (not_47_out, OP0);
  not not_48 (not_48_out, F4);
  not not_49 (not_49_out, F2);
  not not_50 (not_50_out, F0);
  not not_51 (not_51_out, OP5);
  not not_52 (not_52_out, OP4);
  not not_53 (not_53_out, OP2);
  not not_54 (not_54_out, OP1);
  not not_55 (not_55_out, OP0);
  not not_56 (not_56_out, OP5);
  not not_57 (not_57_out, OP4);
  not not_58 (not_58_out, OP1);
  not not_59 (not_59_out, OP0);
  not not_60 (not_60_out, OP5);
  not not_61 (not_61_out, OP4);
  not not_62 (not_62_out, OP2);
  not not_63 (not_63_out, OP1);
  not not_64 (not_64_out, OP5);
  not not_65 (not_65_out, OP4);
  not not_66 (not_66_out, OP2);
  not not_67 (not_67_out, OP0);
  not not_68 (not_68_out, OP4);
  not not_69 (not_69_out, OP3);
  not not_70 (not_70_out, OP2);
  not not_71 (not_71_out, OP4);
  not not_72 (not_72_out, OP2);
  not not_73 (not_73_out, OP0);
  not not_74 (not_74_out, OP1);
  not not_75 (not_75_out, OP2);
  not not_76 (not_76_out, OP3);
  not not_77 (not_77_out, OP4);
  not not_78 (not_78_out, OP5);
  not not_79 (not_79_out, F0);
  not not_80 (not_80_out, F1);
  not not_81 (not_81_out, F3);
  not not_82 (not_82_out, F4);
  not not_83 (not_83_out, OP0);
  not not_84 (not_84_out, OP1);
  not not_85 (not_85_out, OP2);
  not not_86 (not_86_out, OP3);
  not not_87 (not_87_out, OP4);
  not not_88 (not_88_out, OP5);
  not not_89 (not_89_out, F0);
  not not_90 (not_90_out, F2);
  not not_91 (not_91_out, F3);
  not not_92 (not_92_out, F4);
  not not_93 (not_93_out, OP0);
  not not_94 (not_94_out, OP1);
  not not_95 (not_95_out, OP2);
  not not_96 (not_96_out, OP3);
  not not_97 (not_97_out, OP4);
  not not_98 (not_98_out, OP5);
  not not_99 (not_99_out, F0);
  not not_100 (not_100_out, F2);
  not not_101 (not_101_out, F4);
  not not_102 (not_102_out, OP0);
  not not_103 (not_103_out, OP1);
  not not_104 (not_104_out, OP2);
  not not_105 (not_105_out, OP3);
  not not_106 (not_106_out, OP4);
  not not_107 (not_107_out, OP5);
  not not_108 (not_108_out, F3);
  not not_109 (not_109_out, F4);
  not not_110 (not_110_out, OP0);
  not not_111 (not_111_out, OP1);
  not not_112 (not_112_out, OP4);
  not not_113 (not_113_out, OP5);
  not not_114 (not_114_out, OP0);
  not not_115 (not_115_out, OP2);
  not not_116 (not_116_out, OP4);
  not not_117 (not_117_out, OP5);
  not not_118 (not_118_out, OP0);
  not not_119 (not_119_out, OP1);
  not not_120 (not_120_out, OP2);
  not not_121 (not_121_out, OP4);
  not not_122 (not_122_out, OP5);
  not not_123 (not_123_out, F0);
  not not_124 (not_124_out, F1);
  not not_125 (not_125_out, F3);
  not not_126 (not_126_out, F4);
  not not_127 (not_127_out, OP0);
  not not_128 (not_128_out, OP1);
  not not_129 (not_129_out, OP2);
  not not_130 (not_130_out, OP4);
  not not_131 (not_131_out, OP5);
  not not_132 (not_132_out, F0);
  not not_133 (not_133_out, F2);
  not not_134 (not_134_out, F3);
  not not_135 (not_135_out, F4);
  not not_136 (not_136_out, OP0);
  not not_137 (not_137_out, OP1);
  not not_138 (not_138_out, OP2);
  not not_139 (not_139_out, OP4);
  not not_140 (not_140_out, OP5);
  not not_141 (not_141_out, F1);
  not not_142 (not_142_out, F2);
  not not_143 (not_143_out, F3);
  not not_144 (not_144_out, F4);
  not not_145 (not_145_out, OP0);
  not not_146 (not_146_out, OP1);
  not not_147 (not_147_out, OP2);
  not not_148 (not_148_out, OP4);
  not not_149 (not_149_out, OP5);
  not not_150 (not_150_out, F2);
  not not_151 (not_151_out, F4);
  not not_152 (not_152_out, OP0);
  not not_153 (not_153_out, OP1);
  not not_154 (not_154_out, OP4);
  not not_155 (not_155_out, OP5);
  not not_156 (not_156_out, OP1);
  not not_157 (not_157_out, OP2);
  not not_158 (not_158_out, OP4);
  not not_159 (not_159_out, OP5);
  not not_160 (not_160_out, OP2);
  not not_161 (not_161_out, OP4);
  not not_162 (not_162_out, OP0);
  not not_163 (not_163_out, OP1);
  not not_164 (not_164_out, OP2);
  not not_165 (not_165_out, OP3);
  not not_166 (not_166_out, OP4);
  not not_167 (not_167_out, OP5);
  not not_168 (not_168_out, F2);
  not not_169 (not_169_out, F4);
  not not_170 (not_170_out, OP0);
  not not_171 (not_171_out, OP1);
  not not_172 (not_172_out, OP2);
  not not_173 (not_173_out, OP3);
  not not_174 (not_174_out, OP4);
  not not_175 (not_175_out, OP5);
  not not_176 (not_176_out, F3);
  not not_177 (not_177_out, F4);
  not not_178 (not_178_out, OP0);
  not not_179 (not_179_out, OP2);
  not not_180 (not_180_out, OP4);
  not not_181 (not_181_out, OP5);
  not not_182 (not_182_out, OP1);
  not not_183 (not_183_out, OP4);
  not not_184 (not_184_out, OP5);
  and and_1 (and_1_out, not_1_out, not_2_out, not_3_out, not_4_out, not_5_out, not_6_out, not_7_out, not_8_out, not_9_out, not_10_out, F1, F0);
  and and_2 (and_2_out, not_11_out, not_12_out, not_13_out, not_14_out, not_15_out, not_16_out, F5, not_17_out, not_18_out, not_19_out, not_20_out, not_21_out);
  and and_3 (and_3_out, not_22_out, not_23_out, not_24_out, not_25_out, not_26_out, not_27_out, F5, not_28_out, not_29_out, not_30_out, not_31_out, F0);
  and and_4 (and_4_out, not_32_out, not_33_out, not_34_out, not_35_out, not_36_out, not_37_out, F5, not_38_out, not_39_out, F2, not_40_out, not_41_out);
  and and_5 (and_5_out, not_42_out, not_43_out, not_44_out, not_45_out, not_46_out, not_47_out, F5, not_48_out, F3, not_49_out, F1, not_50_out);
  and and_6 (and_6_out, not_51_out, not_52_out, OP3, not_53_out, not_54_out, not_55_out);
  and and_7 (and_7_out, not_56_out, not_57_out, OP3, OP2, not_58_out, not_59_out);
  and and_8 (and_8_out, not_60_out, not_61_out, OP3, not_62_out, not_63_out, OP0);
  and and_9 (and_9_out, not_64_out, not_65_out, OP3, not_66_out, OP1, not_67_out);
  and and_10 (and_10_out, OP5, not_68_out, not_69_out, not_70_out, OP1, OP0);
  and and_11 (and_11_out, OP5, not_71_out, OP3, not_72_out, OP1, OP0);
  and and_12 (and_12_out, not_73_out, not_74_out, not_75_out, not_76_out, not_77_out, not_78_out, not_79_out, not_80_out, F2, not_81_out, not_82_out, F5);
  and and_13 (and_13_out, not_83_out, not_84_out, not_85_out, not_86_out, not_87_out, not_88_out, not_89_out, F1, not_90_out, not_91_out, not_92_out);
  and and_14 (and_14_out, not_93_out, not_94_out, not_95_out, not_96_out, not_97_out, not_98_out, not_99_out, F1, not_100_out, not_101_out, F5);
  and and_15 (and_15_out, not_102_out, not_103_out, not_104_out, not_105_out, not_106_out, not_107_out, F0, F1, F2, not_108_out, not_109_out, F5);
  and and_16 (and_16_out, not_110_out, not_111_out, OP2, OP3, not_112_out, not_113_out);
  and and_17 (and_17_out, not_114_out, OP1, not_115_out, OP3, not_116_out, not_117_out);
  and and_18 (and_18_out, not_118_out, not_119_out, not_120_out, not_121_out, not_122_out, not_123_out, not_124_out, not_125_out, not_126_out, F5);
  and and_19 (and_19_out, not_127_out, not_128_out, not_129_out, not_130_out, not_131_out, not_132_out, not_133_out, not_134_out, not_135_out, F5);
  and and_20 (and_20_out, not_136_out, not_137_out, not_138_out, not_139_out, not_140_out, not_141_out, not_142_out, not_143_out, not_144_out, F5);
  and and_21 (and_21_out, not_145_out, not_146_out, not_147_out, not_148_out, not_149_out, F0, F1, not_150_out, F3, not_151_out, F5);
  and and_22 (and_22_out, not_152_out, not_153_out, OP3, not_154_out, not_155_out);
  and and_23 (and_23_out, not_156_out, not_157_out, OP3, not_158_out, not_159_out);
  and and_24 (and_24_out, OP0, OP1, not_160_out, not_161_out, OP5);
  and and_25 (and_25_out, not_162_out, not_163_out, not_164_out, not_165_out, not_166_out, not_167_out, F1, not_168_out, F3, not_169_out, F5);
  and and_26 (and_26_out, not_170_out, not_171_out, not_172_out, not_173_out, not_174_out, not_175_out, F0, F2, not_176_out, not_177_out, F5);
  and and_27 (and_27_out, not_178_out, OP1, not_179_out, OP3, not_180_out, not_181_out);
  and and_28 (and_28_out, OP0, not_182_out, OP2, OP3, not_183_out, not_184_out);
  or or_1 (S0, and_1_out, and_2_out, and_3_out, and_4_out, and_5_out, and_6_out, and_7_out, and_8_out, and_9_out, and_10_out, and_11_out);
  or or_2 (S1, and_12_out, and_13_out, and_14_out, and_15_out, and_16_out, and_17_out);
  or or_3 (S2, and_18_out, and_19_out, and_20_out, and_21_out, and_22_out, and_23_out, and_24_out);
  or or_4 (S3, and_25_out, and_26_out, and_27_out, and_28_out);
endmodule

module \单周期MIPS  (
  input  IR1,
  input  IR2,
  input  IR3,
  output RegWrite,
  output MemWrite,
  output [31:0] PC,
  output [31:0] IR,
  output [31:0] RDin,
  output [31:0] MDin,
  output [31:0] LedData
);

  wire and_1_out, and_2_out, beq, beq_bne, bne, CLK, Clock, clock_3_out, comparator_1_eq, comparator_1_lt,
       comparator_2_eq, d_ff_1_q, equal, Go, IR1_t, IR2_t, IR3_t, IRA, IRB, IRC, JAL, JMP, JR, nand_1_out,
       not_1_out, not_2_out, not_3_out, or_2_out, RegDst, SignedExt, Syscall, v0__34, v0__34_t, W1, W2, W3,
       \单周期硬布线控制器_1_memtoreg ;
  wire [1:1] \单周期硬布线控制器_1_alu_src ;
  wire [3:0] \单周期硬布线控制器_1_alu_op ;
  wire [4:0] multiplexer_2_out, multiplexer_3_out, multiplexer_4_out, multiplexer_5_out;
  wire [12:0] CNT_num;
  wire [15:0] \总周期数 ;
  wire [27:0] PC_4;
  wire [31:0] mips_alu_1_result, multiplexer_1_out, multiplexer_7_out, multiplexer_8_out, PC_4_Imm, R_rs,
       ram_1_data, shifter_1_out, SignImm, UnsignImm;
  wire [31:28] JmpAddr;

  Clock #(.highDuration(1), .lowDuration(1)) clock_1 (.out(CLK));
  Button _1 (.out(IRA));
  Button _2 (.out(IRB));
  Button _3 (.out(IRC));
  Button \u_继续运行  (.out(Go));
  LED #(.active("true")) led_1 (.in(W1));
  LED #(.active("true")) led_2 (.in(W2));
  LED #(.active("true")) led_3 (.in(W3));
  not not_1 (not_1_out, equal);
  Hex_Digit_Display hex_digit_display_1 (.value(LedData[31:28]));  // open: dp
  Adder #(.width(32)) adder_1 (.a(PC), .b(32'h4), .out({JmpAddr, PC_4}));  // open: cin, cout
  assign UnsignImm = {{16{1'b0}}, IR[15:0]};  // Bit_Extender bit_extender_1
  assign SignImm = {{16{IR[15]}}, IR[15:0]};  // Bit_Extender bit_extender_2
  and and_1 (and_1_out, beq, equal);
  and and_2 (and_2_out, not_1_out, bne);
  Hex_Digit_Display hex_digit_display_2 (.value(LedData[27:24]));  // open: dp
  Hex_Digit_Display hex_digit_display_3 (.value(LedData[23:20]));  // open: dp
  Shifter #(.width(32), .shift("ll")) shifter_1 (.in(SignImm), .\dist (5'b00010), .out(shifter_1_out));
  or or_1 (beq_bne, and_1_out, and_2_out);
  Multiplexer #(.select(3), .width(32), .disabled("Z"), .enable("false")) multiplexer_1 (
    .in0({JmpAddr, PC_4}), .in2({JmpAddr, IR[25:0], 2'b00}), .in3(R_rs), .in4(PC_4_Imm),
    .out(multiplexer_1_out), .sel({beq_bne, JMP, JR}));  // open: in1, in5, in6, in7
  // Probe on {beq_bne, JMP, JR}
  Hex_Digit_Display hex_digit_display_4 (.value(LedData[19:16]));  // open: dp
  Hex_Digit_Display hex_digit_display_5 (.value(LedData[15:12]));  // open: dp
  Adder #(.width(32)) adder_2 (.a({JmpAddr, PC_4}), .b(shifter_1_out), .out(PC_4_Imm));  // open: cin, cout
  or or_2 (or_2_out, Go, not_2_out);
  not not_2 (not_2_out, v0__34);
  Hex_Digit_Display hex_digit_display_6 (.value(LedData[7:4]));  // open: dp
  Hex_Digit_Display hex_digit_display_7 (.value(LedData[11:8]));  // open: dp
  // Probe on \总周期数 
  Register #(.width(32), .trigger("rising"), .Select("low")) u_PC (
    .D(multiplexer_1_out), .en(or_2_out), .Q(PC), .clk(Clock));  // open: clr
  Clock #(.highDuration(1), .lowDuration(1)) clock_2 (.out(Clock));
  D_Flip_Flop #(.trigger("high"), .Pre_Clr_Positions("LEGACY"), .NegatePresetClear("false"), .enable("true"), .NewFFLayout("false")) d_ff_1 (.Q(d_ff_1_q));  // open: clk, D, Qn, preset, en, reset
  // Probe on 13'hc
  Hex_Digit_Display hex_digit_display_8 (.value(LedData[3:0]));  // open: dp
  Comparator #(.width(13), .mode("twosComplement")) comparator_1 (
    .a(CNT_num), .b(13'hc), .eq(comparator_1_eq), .lt(comparator_1_lt));  // open: gt
  Clock #(.highDuration(1), .lowDuration(1)) clock_3 (.out(clock_3_out));
  nand nand_1 (nand_1_out, d_ff_1_q, comparator_1_eq);
  Counter #(.width(13), .max('h1fff), .ongoal("stay"), .trigger("rising"), .behavior("old")) counter_1 (
    .count(comparator_1_lt), .Q(CNT_num), .clk(clock_3_out));  // open: load, D, carry, clr, preset
  or or_3 (IR1_t, IR1, IRA);
  // Mips_Probe mips_probe_1: pin names not known; wires that end beside it: IR, IR[31:26]
  ROM #(.addrWidth(10), .dataWidth(32), .Select("high")) rom_1 (.addr(PC[11:2]), .data(IR));
  Comparator #(.width(32), .mode("twosComplement")) comparator_2 (
    .a(R_rs), .b(32'h22), .eq(comparator_2_eq));  // open: gt, lt
  // Probe on MDin
  Register #(.width(32), .trigger("rising"), .Select("low")) register_1 (
    .D(MDin), .en(v0__34_t), .Q(LedData), .clk(Clock));  // open: clr
  assign CLK = nand_1_out ? clock_3_out : 1'bz;  // Controlled_Buffer controlled_buffer_1
  or or_4 (IR2_t, IR2, IRB);
  not not_3 (not_3_out, comparator_2_eq);
  Pull_Resistor #(.pull(1)) pull_resistor_1 (.node(CLK));
  and and_3 (v0__34_t, Syscall, comparator_2_eq);
  and and_4 (v0__34, Syscall, not_3_out);
  or or_5 (IR3_t, IR3, IRC);
  Multiplexer #(.select(1), .width(5), .disabled("Z"), .enable("false")) multiplexer_2 (
    .in0(IR[20:16]), .in1(IR[15:11]), .out(multiplexer_2_out), .sel(RegDst));
  \单周期硬布线控制器  \u_单周期硬布线控制器_1  (
    .Func(IR[5:0]), .OP(IR[31:26]), .ALU_OP(\单周期硬布线控制器_1_alu_op ), .MemToReg(\单周期硬布线控制器_1_memtoreg ),
    .MemWrite(MemWrite), .ALU_SRC(\单周期硬布线控制器_1_alu_src [1]), .RegWrite(RegWrite), .SysCALL(Syscall),
    .SignedExt(SignedExt), .RegDst(RegDst), .JR(JR), .JMP(JMP), .Beq(beq), .JAL(JAL), .Bne(bne));
  Multiplexer #(.select(1), .width(5), .disabled("Z"), .enable("false")) multiplexer_3 (
    .in0(IR[25:21]), .in1(5'b00010), .out(multiplexer_3_out), .sel(Syscall));
  Multiplexer #(.select(1), .width(5), .disabled("Z"), .enable("false")) multiplexer_4 (
    .in0(multiplexer_2_out), .in1({5{1'b1}}), .out(multiplexer_4_out), .sel(JAL));
  Multiplexer #(.select(1), .width(5), .disabled("Z"), .enable("false")) multiplexer_5 (
    .in0(IR[20:16]), .in1(5'b00100), .out(multiplexer_5_out), .sel(Syscall));
  // Probe on multiplexer_5_out
  Multiplexer #(.select(1), .width(32), .disabled("Z"), .enable("false")) multiplexer_6 (
    .in0(multiplexer_8_out), .in1({JmpAddr, PC_4}), .out(RDin), .sel(JAL));
  MIPS_Regifile mips_regifile_1 (
    .Din(RDin), .Clk(Clock), .R1(R_rs), .R2(MDin), .WE(RegWrite), .W_num(multiplexer_4_out),
    .R1_num(multiplexer_3_out), .R2_num(multiplexer_5_out));
  Multiplexer #(.select(2), .width(32), .disabled("Z"), .enable("false")) multiplexer_7 (
    .in0(MDin), .in1(MDin), .in2(UnsignImm), .in3(SignImm), .out(multiplexer_7_out),
    .sel({\单周期硬布线控制器_1_alu_src [1], SignedExt}));
  MIPS_ALU mips_alu_1 (
    .X(R_rs), .Y(multiplexer_7_out), .AluOP(\单周期硬布线控制器_1_alu_op ), .Equal(equal), .Result(mips_alu_1_result),
    .shamt(IR[10:6]));  // open: Result_2
  RAM #(.addrWidth(10), .dataWidth(32), .bus("separate"), .Select("high")) ram_1 (
    .addr(mips_alu_1_result[11:2]), .din(MDin), .data(ram_1_data), .str(MemWrite), .clk(Clock));  // open: sel, ld, clr
  Multiplexer #(.select(1), .width(32), .disabled("Z"), .enable("false")) multiplexer_8 (
    .in0(mips_alu_1_result), .in1(ram_1_data), .out(multiplexer_8_out), .sel(\单周期硬布线控制器_1_memtoreg ));

  // Other names for the same wires on the sheet: a0[31:0] = MDin; Imm[15:0] = IR[15:0]; JmpAddr[27:2] = IR[25:0];
  //   shamt[4:0] = IR[10:6]; rd[4:0] = IR[15:11]; rt[4:0] = IR[20:16]; rs[4:0] = IR[25:21]; PC_4[31:28] = JmpAddr;
  //   v0[31:0] = R_rs

  // Notes on the sheet:
  //   中断源
  //   J     PC=JumpAddr
  //   Jr    PC=R[rs]
  //   中断等待指示
  //   总复位信号应将除ROM以外所有存储组件全部清零
  //   Jal R[31]=PC+8, PC=JumpAddr
  //   beq/bne  PC=PC+4+BranchAddr
  //   数码管输出
  //   控制位
  //   数码管输出应该用寄存器锁存，否则显示数据只能一闪而过
  //   暂停节拍，不能为0
  //   用这个时钟源需要去掉电路中的其他时钟源
  //   戳工具置1进入计数暂停模式，ctrl+k时钟自动运行到对应节拍暂停
  //   ctrl+k关闭时钟连续运行，将控制位置零，进入单步调试模式调试
  //   指令存储器
  //   指令字
  //   contents of rom_1 (hex, n*v repeats v):
  //   20110001 8000c05 20110001 20120002 20130003 8000c09 20110001 20120002 20130003 8000c0d 20110001
  //   20120002 20130003 8000c11 20110001 20120002 20130003 c000cb8 20100001 20110001 118fc0 112020
  //   20020022 c 118882 12200001 8000c15 112020 20020022 c 20110001 118880 112020 20020022 c 12200001
  //   8000c1f 20110001 118fc0 112020 20020022 c 1188c3 112020 20020022 c 118903 112020 20020022 c 118903
  //   112020 20020022 c 118903 112020 20020022 c 118903 112020 20020022 c 118903 112020 20020022 c 118903
  //   112020 20020022 c 118903 112020 20020022 c 20100001 109fc0 139fc3 8021 2012000c 24160003 26100001
  //   3210000f 20080008 20090001 139900 2709825 132020 20020022 c 1094022 1500fff9 22100001 2018000f
  //   2188024 108700 20080008 20090001 139902 2709825 132021 20020022 c 1094022 1500fff9 108702 2c9b022
  //   12c00001 8000c50 4020 1084027 84400 3508ffff 82021 20020022 c 2010ffff 20110000 ae300000 22100001
  //   22310004 ae300000 22100001 22310004 ae300000 22100001 22310004 ae300000 22100001 22310004 ae300000
  //   22100001 22310004 ae300000 22100001 22310004 ae300000 22100001 22310004 ae300000 22100001 22310004
  //   ae300000 22100001 22310004 ae300000 22100001 22310004 ae300000 22100001 22310004 ae300000 22100001
  //   22310004 ae300000 22100001 22310004 ae300000 22100001 22310004 ae300000 22100001 22310004 ae300000
  //   22100001 22310004 22100001 8020 2011003c 8e130000 8e340000 274402a 11000002 ae330000 ae140000
  //   2231fffc 1611fff8 102020 20020022 c 22100004 2011003c 1611fff2 20020032 c 20100000 22100001 102020
  //   20020022 c 22100002 102020 20020022 c 22100003 102020 20020022 c 22100004 102020 20020022 c 22100005
  //   102020 20020022 c 22100006 102020 20020022 c 22100007 102020 20020022 c 22100008 102020 20020022
  //   20020022 c 3e00008
  //   可计数暂停的时钟源
  //   OP
  //   Func
  //   rs
  //   rt
  //   rd
  //   JMP
  //   Beq
  //   JR
  //   Bne
  //   OP
  //   JAL
  //   Func
  //   Syscall
  //   为方便自动评测，需要输出PC，IR，寄存器堆写如数据RDin
  //   MemToReg
  //   MemWrite
  //   AluOP
  //   AluSrcB
  //   RegWrite
  //   RegDst
  //   RAM写使能MemWrite、RAM写入数据MDin等信号
endmodule

// 控制信号生成
module \控制信号自动生成  (
  input  OP0,
  input  OP1,
  input  OP2,
  input  OP3,
  input  OP4,
  input  OP5,
  input  F0,
  input  F1,
  input  F2,
  input  F3,
  input  F4,
  input  F5,
  output MemToReg,
  output MemWrite,
  output ALU_SRC,
  output RegWrite,
  output SysCALL,
  output SignedExt,
  output RegDst,
  output BEQ,
  output BNE,
  output JR,
  output JUMP,
  output JAL
);

  wire and_3_out, and_4_out, and_5_out, and_6_out, and_7_out, and_8_out, and_9_out, and_10_out, and_11_out,
       and_12_out, and_13_out, and_14_out, and_15_out, and_16_out, and_17_out, and_18_out, and_19_out,
       and_20_out, and_21_out, and_22_out, and_23_out, and_24_out, and_25_out, and_26_out, and_27_out,
       and_29_out, and_30_out, and_31_out, and_32_out, and_33_out, and_34_out, and_35_out, and_36_out,
       and_37_out, and_38_out, and_39_out, and_40_out, and_41_out, and_42_out, and_43_out, and_44_out,
       and_45_out, and_46_out, and_50_out, and_51_out, and_52_out, not_1_out, not_2_out, not_3_out,
       not_4_out, not_5_out, not_6_out, not_7_out, not_8_out, not_9_out, not_10_out, not_11_out, not_12_out,
       not_13_out, not_14_out, not_15_out, not_16_out, not_17_out, not_18_out, not_19_out, not_20_out,
       not_21_out, not_22_out, not_23_out, not_24_out, not_25_out, not_26_out, not_27_out, not_28_out,
       not_29_out, not_30_out, not_31_out, not_32_out, not_33_out, not_34_out, not_35_out, not_36_out,
       not_37_out, not_38_out, not_39_out, not_40_out, not_41_out, not_42_out, not_43_out, not_44_out,
       not_45_out, not_46_out, not_47_out, not_48_out, not_49_out, not_50_out, not_51_out, not_52_out,
       not_53_out, not_54_out, not_55_out, not_56_out, not_57_out, not_58_out, not_59_out, not_60_out,
       not_61_out, not_62_out, not_63_out, not_64_out, not_65_out, not_66_out, not_67_out, not_68_out,
       not_69_out, not_70_out, not_71_out, not_72_out, not_73_out, not_74_out, not_75_out, not_76_out,
       not_77_out, not_78_out, not_79_out, not_80_out, not_81_out, not_82_out, not_83_out, not_84_out,
       not_85_out, not_86_out, not_87_out, not_88_out, not_89_out, not_90_out, not_91_out, not_92_out,
       not_93_out, not_94_out, not_95_out, not_96_out, not_97_out, not_98_out, not_99_out, not_100_out,
       not_101_out, not_102_out, not_103_out, not_104_out, not_105_out, not_106_out, not_107_out,
       not_108_out, not_109_out, not_110_out, not_111_out, not_112_out, not_113_out, not_114_out,
       not_115_out, not_116_out, not_117_out, not_118_out, not_119_out, not_120_out, not_121_out,
       not_122_out, not_123_out, not_124_out, not_125_out, not_126_out, not_127_out, not_128_out,
       not_129_out, not_130_out, not_131_out, not_132_out, not_133_out, not_134_out, not_135_out,
       not_136_out, not_137_out, not_138_out, not_139_out, not_140_out, not_141_out, not_142_out,
       not_143_out, not_144_out, not_145_out, not_146_out, not_147_out, not_148_out, not_149_out,
       not_150_out, not_151_out, not_152_out, not_153_out, not_154_out, not_155_out, not_156_out,
       not_157_out, not_158_out, not_159_out, not_160_out, not_161_out, not_162_out, not_163_out,
       not_164_out, not_165_out, not_166_out, not_167_out, not_168_out, not_169_out, not_170_out,
       not_171_out, not_172_out, not_173_out, not_174_out, not_175_out, not_176_out, not_177_out,
       not_178_out, not_179_out, not_180_out, not_181_out, not_182_out, not_183_out, not_184_out,
       not_185_out, not_186_out, not_187_out, not_188_out, not_189_out, not_190_out, not_191_out,
       not_192_out, not_193_out, not_194_out, not_195_out, not_196_out, not_197_out, not_198_out,
       not_199_out, not_200_out, not_201_out, not_202_out, not_203_out, not_204_out, not_205_out,
       not_206_out, not_207_out, not_208_out, not_209_out, not_210_out, not_211_out, not_212_out,
       not_213_out, not_214_out, not_215_out, not_216_out, not_217_out, not_218_out, not_219_out,
       not_220_out, not_221_out, not_222_out, not_223_out, not_224_out, not_225_out, not_226_out,
       not_227_out, not_228_out, not_229_out, not_230_out, not_231_out, not_232_out, not_233_out,
       not_234_out, not_235_out, not_236_out, not_237_out, not_238_out, not_239_out, not_240_out,
       not_241_out, not_242_out, not_243_out, not_244_out, not_245_out, not_246_out, not_247_out,
       not_248_out, not_249_out, not_250_out, not_251_out, not_252_out, not_253_out, not_254_out,
       not_255_out, not_256_out, not_257_out, not_258_out, not_259_out, not_260_out, not_261_out,
       not_262_out, not_263_out, not_264_out, not_265_out, not_266_out, not_267_out, not_268_out,
       not_269_out, not_270_out, not_271_out, not_272_out, not_273_out, not_274_out, not_275_out,
       not_276_out, not_277_out, not_278_out, not_279_out, not_280_out, not_281_out, not_282_out,
       not_283_out, not_284_out, not_285_out, not_286_out, not_287_out, not_288_out, not_289_out,
       not_290_out, not_291_out, not_292_out, not_293_out, not_294_out, not_295_out, not_296_out,
       not_297_out, not_298_out, not_299_out, not_300_out, not_301_out, not_302_out, not_303_out,
       not_304_out, not_305_out, not_306_out, not_307_out, not_308_out, not_309_out, not_310_out,
       not_311_out, not_312_out, not_313_out, not_314_out, not_315_out, not_316_out, not_317_out,
       not_318_out, not_319_out, not_320_out, not_321_out, not_322_out, not_323_out, not_324_out,
       not_325_out, not_326_out, not_327_out, not_328_out, not_329_out, not_330_out, not_331_out,
       not_332_out, not_333_out, not_334_out, not_335_out, not_336_out, not_337_out, not_338_out,
       not_339_out, not_340_out, not_341_out, not_342_out, not_343_out, not_344_out, not_345_out,
       not_346_out, not_347_out, not_348_out, not_349_out, not_350_out, not_351_out, not_352_out,
       not_353_out, not_354_out, not_355_out, not_356_out, not_357_out, not_358_out, not_359_out,
       not_360_out, not_361_out, not_362_out, not_363_out, not_364_out, not_365_out, not_366_out;

  not not_1 (not_1_out, OP4);
  not not_2 (not_2_out, OP3);
  not not_3 (not_3_out, OP2);
  not not_4 (not_4_out, OP4);
  not not_5 (not_5_out, OP2);
  not not_6 (not_6_out, OP5);
  not not_7 (not_7_out, OP4);
  not not_8 (not_8_out, OP2);
  not not_9 (not_9_out, OP1);
  not not_10 (not_10_out, OP0);
  not not_11 (not_11_out, OP5);
  not not_12 (not_12_out, OP4);
  not not_13 (not_13_out, OP1);
  not not_14 (not_14_out, OP0);
  not not_15 (not_15_out, OP5);
  not not_16 (not_16_out, OP4);
  not not_17 (not_17_out, OP2);
  not not_18 (not_18_out, OP1);
  not not_19 (not_19_out, OP5);
  not not_20 (not_20_out, OP4);
  not not_21 (not_21_out, OP2);
  not not_22 (not_22_out, OP0);
  not not_23 (not_23_out, OP5);
  not not_24 (not_24_out, OP4);
  not not_25 (not_25_out, OP1);
  not not_26 (not_26_out, OP4);
  not not_27 (not_27_out, OP3);
  not not_28 (not_28_out, OP2);
  not not_29 (not_29_out, OP4);
  not not_30 (not_30_out, OP2);
  not not_31 (not_31_out, OP5);
  not not_32 (not_32_out, OP4);
  not not_33 (not_33_out, OP3);
  not not_34 (not_34_out, OP2);
  not not_35 (not_35_out, OP1);
  not not_36 (not_36_out, OP0);
  not not_37 (not_37_out, F5);
  not not_38 (not_38_out, F4);
  not not_39 (not_39_out, F3);
  not not_40 (not_40_out, F2);
  not not_41 (not_41_out, F1);
  not not_42 (not_42_out, F0);
  not not_43 (not_43_out, OP5);
  not not_44 (not_44_out, OP4);
  not not_45 (not_45_out, OP3);
  not not_46 (not_46_out, OP2);
  not not_47 (not_47_out, OP1);
  not not_48 (not_48_out, OP0);
  not not_49 (not_49_out, F5);
  not not_50 (not_50_out, F4);
  not not_51 (not_51_out, F3);
  not not_52 (not_52_out, F2);
  not not_53 (not_53_out, OP5);
  not not_54 (not_54_out, OP4);
  not not_55 (not_55_out, OP3);
  not not_56 (not_56_out, OP2);
  not not_57 (not_57_out, OP1);
  not not_58 (not_58_out, OP0);
  not not_59 (not_59_out, F5);
  not not_60 (not_60_out, F4);
  not not_61 (not_61_out, F3);
  not not_62 (not_62_out, F2);
  not not_63 (not_63_out, F0);
  not not_64 (not_64_out, OP5);
  not not_65 (not_65_out, OP4);
  not not_66 (not_66_out, OP3);
  not not_67 (not_67_out, OP2);
  not not_68 (not_68_out, OP1);
  not not_69 (not_69_out, OP0);
  not not_70 (not_70_out, F4);
  not not_71 (not_71_out, F3);
  not not_72 (not_72_out, F2);
  not not_73 (not_73_out, F1);
  not not_74 (not_74_out, F0);
  not not_75 (not_75_out, OP5);
  not not_76 (not_76_out, OP4);
  not not_77 (not_77_out, OP3);
  not not_78 (not_78_out, OP2);
  not not_79 (not_79_out, OP1);
  not not_80 (not_80_out, OP0);
  not not_81 (not_81_out, F4);
  not not_82 (not_82_out, F3);
  not not_83 (not_83_out, F2);
  not not_84 (not_84_out, F1);
  not not_85 (not_85_out, OP5);
  not not_86 (not_86_out, OP4);
  not not_87 (not_87_out, OP3);
  not not_88 (not_88_out, OP2);
  not not_89 (not_89_out, OP1);
  not not_90 (not_90_out, OP0);
  not not_91 (not_91_out, F4);
  not not_92 (not_92_out, F3);
  not not_93 (not_93_out, F2);
  not not_94 (not_94_out, F0);
  not not_95 (not_95_out, OP5);
  not not_96 (not_96_out, OP4);
  not not_97 (not_97_out, OP3);
  not not_98 (not_98_out, OP2);
  not not_99 (not_99_out, OP1);
  not not_100 (not_100_out, OP0);
  not not_101 (not_101_out, F4);
  not not_102 (not_102_out, F3);
  not not_103 (not_103_out, F1);
  not not_104 (not_104_out, F0);
  not not_105 (not_105_out, OP5);
  not not_106 (not_106_out, OP4);
  not not_107 (not_107_out, OP3);
  not not_108 (not_108_out, OP2);
  not not_109 (not_109_out, OP1);
  not not_110 (not_110_out, OP0);
  not not_111 (not_111_out, F4);
  not not_112 (not_112_out, F3);
  not not_113 (not_113_out, F1);
  not not_114 (not_114_out, OP5);
  not not_115 (not_115_out, OP4);
  not not_116 (not_116_out, OP3);
  not not_117 (not_117_out, OP2);
  not not_118 (not_118_out, OP1);
  not not_119 (not_119_out, OP0);
  not not_120 (not_120_out, F4);
  not not_121 (not_121_out, F3);
  not not_122 (not_122_out, OP5);
  not not_123 (not_123_out, OP4);
  not not_124 (not_124_out, OP3);
  not not_125 (not_125_out, OP2);
  not not_126 (not_126_out, OP1);
  not not_127 (not_127_out, OP0);
  not not_128 (not_128_out, F4);
  not not_129 (not_129_out, F2);
  not not_130 (not_130_out, F0);
  not not_131 (not_131_out, OP5);
  not not_132 (not_132_out, OP4);
  not not_133 (not_133_out, OP3);
  not not_134 (not_134_out, OP2);
  not not_135 (not_135_out, OP1);
  not not_136 (not_136_out, OP0);
  not not_137 (not_137_out, F4);
  not not_138 (not_138_out, F2);
  not not_139 (not_139_out, OP5);
  not not_140 (not_140_out, OP4);
  not not_141 (not_141_out, OP3);
  not not_142 (not_142_out, OP2);
  not not_143 (not_143_out, OP5);
  not not_144 (not_144_out, OP4);
  not not_145 (not_145_out, OP2);
  not not_146 (not_146_out, OP1);
  not not_147 (not_147_out, OP0);
  not not_148 (not_148_out, OP5);
  not not_149 (not_149_out, OP4);
  not not_150 (not_150_out, OP1);
  not not_151 (not_151_out, OP0);
  not not_152 (not_152_out, OP5);
  not not_153 (not_153_out, OP4);
  not not_154 (not_154_out, OP2);
  not not_155 (not_155_out, OP1);
  not not_156 (not_156_out, OP5);
  not not_157 (not_157_out, OP4);
  not not_158 (not_158_out, OP2);
  not not_159 (not_159_out, OP0);
  not not_160 (not_160_out, OP5);
  not not_161 (not_161_out, OP4);
  not not_162 (not_162_out, OP1);
  not not_163 (not_163_out, OP4);
  not not_164 (not_164_out, OP3);
  not not_165 (not_165_out, OP2);
  not not_166 (not_166_out, OP5);
  not not_167 (not_167_out, OP4);
  not not_168 (not_168_out, OP3);
  not not_169 (not_169_out, OP2);
  not not_170 (not_170_out, OP1);
  not not_171 (not_171_out, OP0);
  not not_172 (not_172_out, F5);
  not not_173 (not_173_out, F4);
  not not_174 (not_174_out, F1);
  not not_175 (not_175_out, F0);
  not not_176 (not_176_out, OP5);
  not not_177 (not_177_out, OP4);
  not not_178 (not_178_out, OP2);
  not not_179 (not_179_out, OP1);
  not not_180 (not_180_out, OP0);
  not not_181 (not_181_out, OP5);
  not not_182 (not_182_out, OP4);
  not not_183 (not_183_out, OP2);
  not not_184 (not_184_out, OP1);
  not not_185 (not_185_out, OP5);
  not not_186 (not_186_out, OP4);
  not not_187 (not_187_out, OP2);
  not not_188 (not_188_out, OP0);
  not not_189 (not_189_out, OP4);
  not not_190 (not_190_out, OP3);
  not not_191 (not_191_out, OP2);
  not not_192 (not_192_out, OP4);
  not not_193 (not_193_out, OP2);
  not not_194 (not_194_out, OP5);
  not not_195 (not_195_out, OP4);
  not not_196 (not_196_out, OP3);
  not not_197 (not_197_out, OP2);
  not not_198 (not_198_out, OP1);
  not not_199 (not_199_out, OP0);
  not not_200 (not_200_out, F5);
  not not_201 (not_201_out, F4);
  not not_202 (not_202_out, F3);
  not not_203 (not_203_out, F2);
  not not_204 (not_204_out, F1);
  not not_205 (not_205_out, F0);
  not not_206 (not_206_out, OP5);
  not not_207 (not_207_out, OP4);
  not not_208 (not_208_out, OP3);
  not not_209 (not_209_out, OP2);
  not not_210 (not_210_out, OP1);
  not not_211 (not_211_out, OP0);
  not not_212 (not_212_out, F5);
  not not_213 (not_213_out, F4);
  not not_214 (not_214_out, F3);
  not not_215 (not_215_out, F2);
  not not_216 (not_216_out, OP5);
  not not_217 (not_217_out, OP4);
  not not_218 (not_218_out, OP3);
  not not_219 (not_219_out, OP2);
  not not_220 (not_220_out, OP1);
  not not_221 (not_221_out, OP0);
  not not_222 (not_222_out, F5);
  not not_223 (not_223_out, F4);
  not not_224 (not_224_out, F3);
  not not_225 (not_225_out, F2);
  not not_226 (not_226_out, F0);
  not not_227 (not_227_out, OP5);
  not not_228 (not_228_out, OP4);
  not not_229 (not_229_out, OP3);
  not not_230 (not_230_out, OP2);
  not not_231 (not_231_out, OP1);
  not not_232 (not_232_out, OP0);
  not not_233 (not_233_out, F4);
  not not_234 (not_234_out, F3);
  not not_235 (not_235_out, F2);
  not not_236 (not_236_out, F1);
  not not_237 (not_237_out, F0);
  not not_238 (not_238_out, OP5);
  not not_239 (not_239_out, OP4);
  not not_240 (not_240_out, OP3);
  not not_241 (not_241_out, OP2);
  not not_242 (not_242_out, OP1);
  not not_243 (not_243_out, OP0);
  not not_244 (not_244_out, F4);
  not not_245 (not_245_out, F3);
  not not_246 (not_246_out, F2);
  not not_247 (not_247_out, F1);
  not not_248 (not_248_out, OP5);
  not not_249 (not_249_out, OP4);
  not not_250 (not_250_out, OP3);
  not not_251 (not_251_out, OP2);
  not not_252 (not_252_out, OP1);
  not not_253 (not_253_out, OP0);
  not not_254 (not_254_out, F4);
  not not_255 (not_255_out, F3);
  not not_256 (not_256_out, F2);
  not not_257 (not_257_out, F0);
  not not_258 (not_258_out, OP5);
  not not_259 (not_259_out, OP4);
  not not_260 (not_260_out, OP3);
  not not_261 (not_261_out, OP2);
  not not_262 (not_262_out, OP1);
  not not_263 (not_263_out, OP0);
  not not_264 (not_264_out, F4);
  not not_265 (not_265_out, F3);
  not not_266 (not_266_out, F1);
  not not_267 (not_267_out, F0);
  not not_268 (not_268_out, OP5);
  not not_269 (not_269_out, OP4);
  not not_270 (not_270_out, OP3);
  not not_271 (not_271_out, OP2);
  not not_272 (not_272_out, OP1);
  not not_273 (not_273_out, OP0);
  not not_274 (not_274_out, F4);
  not not_275 (not_275_out, F3);
  not not_276 (not_276_out, F1);
  not not_277 (not_277_out, OP5);
  not not_278 (not_278_out, OP4);
  not not_279 (not_279_out, OP3);
  not not_280 (not_280_out, OP2);
  not not_281 (not_281_out, OP1);
  not not_282 (not_282_out, OP0);
  not not_283 (not_283_out, F4);
  not not_284 (not_284_out, F3);
  not not_285 (not_285_out, OP5);
  not not_286 (not_286_out, OP4);
  not not_287 (not_287_out, OP3);
  not not_288 (not_288_out, OP2);
  not not_289 (not_289_out, OP1);
  not not_290 (not_290_out, OP0);
  not not_291 (not_291_out, F4);
  not not_292 (not_292_out, F2);
  not not_293 (not_293_out, F0);
  not not_294 (not_294_out, OP5);
  not not_295 (not_295_out, OP4);
  not not_296 (not_296_out, OP3);
  not not_297 (not_297_out, OP2);
  not not_298 (not_298_out, OP1);
  not not_299 (not_299_out, OP0);
  not not_300 (not_300_out, F4);
  not not_301 (not_301_out, F2);
  not not_302 (not_302_out, OP5);
  not not_303 (not_303_out, OP4);
  not not_304 (not_304_out, OP3);
  not not_305 (not_305_out, OP2);
  not not_306 (not_306_out, OP1);
  not not_307 (not_307_out, OP0);
  not not_308 (not_308_out, F5);
  not not_309 (not_309_out, F4);
  not not_310 (not_310_out, F2);
  not not_311 (not_311_out, F1);
  not not_312 (not_312_out, F0);
  not not_313 (not_313_out, OP5);
  not not_314 (not_314_out, OP4);
  not not_315 (not_315_out, OP3);
  not not_316 (not_316_out, OP2);
  not not_317 (not_317_out, OP1);
  not not_318 (not_318_out, OP0);
  not not_319 (not_319_out, F5);
  not not_320 (not_320_out, F4);
  not not_321 (not_321_out, F1);
  not not_322 (not_322_out, F0);
  not not_323 (not_323_out, OP5);
  not not_324 (not_324_out, OP4);
  not not_325 (not_325_out, OP3);
  not not_326 (not_326_out, OP1);
  not not_327 (not_327_out, OP0);
  not not_328 (not_328_out, OP5);
  not not_329 (not_329_out, OP4);
  not not_330 (not_330_out, OP3);
  not not_331 (not_331_out, OP1);
  not not_332 (not_332_out, OP5);
  not not_333 (not_333_out, OP4);
  not not_334 (not_334_out, OP3);
  not not_335 (not_335_out, OP2);
  not not_336 (not_336_out, OP1);
  not not_337 (not_337_out, OP0);
  not not_338 (not_338_out, F5);
  not not_339 (not_339_out, F4);
  not not_340 (not_340_out, F2);
  not not_341 (not_341_out, F1);
  not not_342 (not_342_out, F0);
  not not_343 (not_343_out, OP5);
  not not_344 (not_344_out, OP4);
  not not_345 (not_345_out, OP3);
  not not_346 (not_346_out, OP2);
  not not_347 (not_347_out, OP1);
  not not_348 (not_348_out, OP0);
  not not_349 (not_349_out, F5);
  not not_350 (not_350_out, F4);
  not not_351 (not_351_out, F2);
  not not_352 (not_352_out, F1);
  not not_353 (not_353_out, F0);
  not not_354 (not_354_out, OP5);
  not not_355 (not_355_out, OP4);
  not not_356 (not_356_out, OP3);
  not not_357 (not_357_out, OP2);
  not not_358 (not_358_out, OP0);
  not not_359 (not_359_out, OP5);
  not not_360 (not_360_out, OP4);
  not not_361 (not_361_out, OP3);
  not not_362 (not_362_out, OP2);
  not not_363 (not_363_out, OP5);
  not not_364 (not_364_out, OP4);
  not not_365 (not_365_out, OP3);
  not not_366 (not_366_out, OP2);
  and and_1 (MemToReg, OP5, not_1_out, not_2_out, not_3_out, OP1, OP0);
  and and_2 (MemWrite, OP5, not_4_out, OP3, not_5_out, OP1, OP0);
  and and_3 (and_3_out, not_6_out, not_7_out, OP3, not_8_out, not_9_out, not_10_out);
  and and_4 (and_4_out, not_11_out, not_12_out, OP3, OP2, not_13_out, not_14_out);
  and and_5 (and_5_out, not_15_out, not_16_out, OP3, not_17_out, not_18_out, OP0);
  and and_6 (and_6_out, not_19_out, not_20_out, OP3, not_21_out, OP1, not_22_out);
  and and_7 (and_7_out, not_23_out, not_24_out, OP3, OP2, not_25_out, OP0);
  and and_8 (and_8_out, OP5, not_26_out, not_27_out, not_28_out, OP1, OP0);
  and and_9 (and_9_out, OP5, not_29_out, OP3, not_30_out, OP1, OP0);
  and and_10 (and_10_out, not_31_out, not_32_out, not_33_out, not_34_out, not_35_out, not_36_out, not_37_out, not_38_out, not_39_out, not_40_out, not_41_out, not_42_out);
  and and_11 (and_11_out, not_43_out, not_44_out, not_45_out, not_46_out, not_47_out, not_48_out, not_49_out, not_50_out, not_51_out, not_52_out, F1, F0);
  and and_12 (and_12_out, not_53_out, not_54_out, not_55_out, not_56_out, not_57_out, not_58_out, not_59_out, not_60_out, not_61_out, not_62_out, F1, not_63_out);
  and and_13 (and_13_out, not_64_out, not_65_out, not_66_out, not_67_out, not_68_out, not_69_out, F5, not_70_out, not_71_out, not_72_out, not_73_out, not_74_out);
  and and_14 (and_14_out, not_75_out, not_76_out, not_77_out, not_78_out, not_79_out, not_80_out, F5, not_81_out, not_82_out, not_83_out, not_84_out, F0);
  and and_15 (and_15_out, not_85_out, not_86_out, not_87_out, not_88_out, not_89_out, not_90_out, F5, not_91_out, not_92_out, not_93_out, F1, not_94_out);
  and and_16 (and_16_out, not_95_out, not_96_out, not_97_out, not_98_out, not_99_out, not_100_out, F5, not_101_out, not_102_out, F2, not_103_out, not_104_out);
  and and_17 (and_17_out, not_105_out, not_106_out, not_107_out, not_108_out, not_109_out, not_110_out, F5, not_111_out, not_112_out, F2, not_113_out, F0);
  and and_18 (and_18_out, not_114_out, not_115_out, not_116_out, not_117_out, not_118_out, not_119_out, F5, not_120_out, not_121_out, F2, F1, F0);
  and and_19 (and_19_out, not_122_out, not_123_out, not_124_out, not_125_out, not_126_out, not_127_out, F5, not_128_out, F3, not_129_out, F1, not_130_out);
  and and_20 (and_20_out, not_131_out, not_132_out, not_133_out, not_134_out, not_135_out, not_136_out, F5, not_137_out, F3, not_138_out, F1, F0);
  and and_21 (and_21_out, not_139_out, not_140_out, not_141_out, not_142_out, OP1, OP0);
  and and_22 (and_22_out, not_143_out, not_144_out, OP3, not_145_out, not_146_out, not_147_out);
  and and_23 (and_23_out, not_148_out, not_149_out, OP3, OP2, not_150_out, not_151_out);
  and and_24 (and_24_out, not_152_out, not_153_out, OP3, not_154_out, not_155_out, OP0);
  and and_25 (and_25_out, not_156_out, not_157_out, OP3, not_158_out, OP1, not_159_out);
  and and_26 (and_26_out, not_160_out, not_161_out, OP3, OP2, not_162_out, OP0);
  and and_27 (and_27_out, OP5, not_163_out, not_164_out, not_165_out, OP1, OP0);
  and and_28 (SysCALL, not_166_out, not_167_out, not_168_out, not_169_out, not_170_out, not_171_out, not_172_out, not_173_out, F3, F2, not_174_out, not_175_out);
  and and_29 (and_29_out, not_176_out, not_177_out, OP3, not_178_out, not_179_out, not_180_out);
  and and_30 (and_30_out, not_181_out, not_182_out, OP3, not_183_out, not_184_out, OP0);
  and and_31 (and_31_out, not_185_out, not_186_out, OP3, not_187_out, OP1, not_188_out);
  and and_32 (and_32_out, OP5, not_189_out, not_190_out, not_191_out, OP1, OP0);
  and and_33 (and_33_out, OP5, not_192_out, OP3, not_193_out, OP1, OP0);
  and and_34 (and_34_out, not_194_out, not_195_out, not_196_out, not_197_out, not_198_out, not_199_out, not_200_out, not_201_out, not_202_out, not_203_out, not_204_out, not_205_out);
  and and_35 (and_35_out, not_206_out, not_207_out, not_208_out, not_209_out, not_210_out, not_211_out, not_212_out, not_213_out, not_214_out, not_215_out, F1, F0);
  and and_36 (and_36_out, not_216_out, not_217_out, not_218_out, not_219_out, not_220_out, not_221_out, not_222_out, not_223_out, not_224_out, not_225_out, F1, not_226_out);
  and and_37 (and_37_out, not_227_out, not_228_out, not_229_out, not_230_out, not_231_out, not_232_out, F5, not_233_out, not_234_out, not_235_out, not_236_out, not_237_out);
  and and_38 (and_38_out, not_238_out, not_239_out, not_240_out, not_241_out, not_242_out, not_243_out, F5, not_244_out, not_245_out, not_246_out, not_247_out, F0);
  and and_39 (and_39_out, not_248_out, not_249_out, not_250_out, not_251_out, not_252_out, not_253_out, F5, not_254_out, not_255_out, not_256_out, F1, not_257_out);
  and and_40 (and_40_out, not_258_out, not_259_out, not_260_out, not_261_out, not_262_out, not_263_out, F5, not_264_out, not_265_out, F2, not_266_out, not_267_out);
  and and_41 (and_41_out, not_268_out, not_269_out, not_270_out, not_271_out, not_272_out, not_273_out, F5, not_274_out, not_275_out, F2, not_276_out, F0);
  and and_42 (and_42_out, not_277_out, not_278_out, not_279_out, not_280_out, not_281_out, not_282_out, F5, not_283_out, not_284_out, F2, F1, F0);
  and and_43 (and_43_out, not_285_out, not_286_out, not_287_out, not_288_out, not_289_out, not_290_out, F5, not_291_out, F3, not_292_out, F1, not_293_out);
  and and_44 (and_44_out, not_294_out, not_295_out, not_296_out, not_297_out, not_298_out, not_299_out, F5, not_300_out, F3, not_301_out, F1, F0);
  and and_45 (and_45_out, not_302_out, not_303_out, not_304_out, not_305_out, not_306_out, not_307_out, not_308_out, not_309_out, F3, not_310_out, not_311_out, not_312_out);
  and and_46 (and_46_out, not_313_out, not_314_out, not_315_out, not_316_out, not_317_out, not_318_out, not_319_out, not_320_out, F3, F2, not_321_out, not_322_out);
  and and_47 (BEQ, not_323_out, not_324_out, not_325_out, OP2, not_326_out, not_327_out);
  and and_48 (BNE, not_328_out, not_329_out, not_330_out, OP2, not_331_out, OP0);
  and and_49 (JR, not_332_out, not_333_out, not_334_out, not_335_out, not_336_out, not_337_out, not_338_out, not_339_out, F3, not_340_out, not_341_out, not_342_out);
  and and_50 (and_50_out, not_343_out, not_344_out, not_345_out, not_346_out, not_347_out, not_348_out, not_349_out, not_350_out, F3, not_351_out, not_352_out, not_353_out);
  and and_51 (and_51_out, not_354_out, not_355_out, not_356_out, not_357_out, OP1, not_358_out);
  and and_52 (and_52_out, not_359_out, not_360_out, not_361_out, not_362_out, OP1, OP0);
  and and_53 (JAL, not_363_out, not_364_out, not_365_out, not_366_out, OP1, OP0);
  or or_1 (ALU_SRC, and_3_out, and_4_out, and_5_out, and_6_out, and_7_out, and_8_out, and_9_out);
  or or_2 (SignedExt, and_29_out, and_30_out, and_31_out, and_32_out, and_33_out);
  or or_3 (JUMP, and_50_out, and_51_out, and_52_out);
  or or_4 (RegWrite, and_10_out, and_11_out, and_12_out, and_13_out, and_14_out, and_15_out, and_16_out, and_17_out, and_18_out, and_19_out, and_20_out, and_21_out, and_22_out, and_23_out, and_24_out, and_25_out, and_26_out, and_27_out);
  or or_5 (RegDst, and_34_out, and_35_out, and_36_out, and_37_out, and_38_out, and_39_out, and_40_out, and_41_out, and_42_out, and_43_out, and_44_out, and_45_out, and_46_out);
endmodule

// ALU
module MIPS_ALU (
  input  [4:0] shamt,
  input  [31:0] X,
  input  [31:0] Y,
  input  [3:0] AluOP,
  output Equal,
  output [31:0] Result,
  output [31:0] Result_2
);

  wire [0:0] comparator_1_lt, comparator_2_lt;
  wire [31:0] adder_1_out, AND_out, divider_1_out, divider_1_rem, multiplier_1_cout, multiplier_1_out,
       NOR_out, OR_out, shifter_1_out, shifter_2_out, shifter_3_out, subtractor_1_out, XOR_out;

  assign AND_out = X & Y;  // AND_Gate AND, 32 bits wide
  assign OR_out = X | Y;  // OR_Gate OR, 32 bits wide
  Shifter #(.width(32), .shift("ll")) shifter_1 (.in(Y), .\dist (shamt), .out(shifter_1_out));
  Shifter #(.width(32), .shift("ar")) shifter_2 (.in(Y), .\dist (shamt), .out(shifter_2_out));
  Shifter #(.width(32), .shift("lr")) shifter_3 (.in(Y), .\dist (shamt), .out(shifter_3_out));
  Multiplier #(.width(32)) multiplier_1 (.a(X), .b(Y), .out(multiplier_1_out), .cout(multiplier_1_cout));  // open: cin
  Divider #(.width(32)) divider_1 (.a(X), .b(Y), .out(divider_1_out), .rem(divider_1_rem));  // open: upper
  Adder #(.width(32)) adder_1 (.a(X), .b(Y), .out(adder_1_out));  // open: cin, cout
  Subtractor #(.width(32)) subtractor_1 (.a(X), .b(Y), .out(subtractor_1_out));  // open: bin, bout
  assign XOR_out = X ^ Y;  // XOR_Gate XOR, 32 bits wide
  assign NOR_out = ~(X | Y);  // NOR_Gate NOR, 32 bits wide
  Comparator #(.width(32), .mode("twosComplement")) comparator_1 (
    .a(X), .b(Y), .eq(Equal), .lt(comparator_1_lt[0]));  // open: gt
  Comparator #(.width(32), .mode("unsigned")) comparator_2 (.a(X), .b(Y), .lt(comparator_2_lt[0]));  // open: gt, eq
  Multiplexer #(.select(4), .width(32), .disabled("Z"), .enable("false")) multiplexer_1 (
    .in0(shifter_1_out), .in1(shifter_2_out), .in2(shifter_3_out), .in3(multiplier_1_out),
    .in4(divider_1_out), .in5(adder_1_out), .in6(subtractor_1_out), .in7(AND_out), .in8(OR_out),
    .in9(XOR_out), .in10(NOR_out), .in11({{31{1'b0}}, comparator_1_lt[0]}),
    .in12({{31{1'b0}}, comparator_2_lt[0]}), .in13({32{1'b0}}), .in14({32{1'b0}}), .in15({32{1'b0}}),
    .out(Result), .sel(AluOP));
  Multiplexer #(.select(4), .width(32), .disabled("Z"), .enable("false")) multiplexer_2 (
    .in0({32{1'b0}}), .in1({32{1'b0}}), .in2({32{1'b0}}), .in3(multiplier_1_cout), .in4(divider_1_rem),
    .in5({32{1'b0}}), .in6({32{1'b0}}), .in7({32{1'b0}}), .in8({32{1'b0}}), .in9({32{1'b0}}),
    .in10({32{1'b0}}), .in11({32{1'b0}}), .in12({32{1'b0}}), .in13({32{1'b0}}), .in14({32{1'b0}}),
    .in15({32{1'b0}}), .out(Result_2), .sel(AluOP));

  // Other names for the same wires on the sheet: Result2[31:0] = Result_2; S[3:0] = AluOP

  // Notes on the sheet:
  //   不要改变此引脚区域内容，也不要改变ALU封装形式
  //   输入引脚
  //   输出引脚
endmodule

module MIPS_Regifile (
  input  [31:0] Din,
  input  Clk,
  input  WE,
  input  [4:0] R1_num,
  input  [4:0] W_num,
  input  [4:0] R2_num,
  output [31:0] R1,
  output [31:0] R2
);

  // RegisterFile registerfile_1: pin names not known; wires that end beside it: Din, Clk, WE, W_num, R1_num, R2_num, R1, R2
endmodule

module \理想流水线  (
  output RegWrite,
  output MemWrite,
  output [31:0] IF_PC,
  output [31:0] ID_PC,
  output [31:0] EX_PC,
  output [31:0] M_PC,
  output [31:0] WB_PC,
  output [31:0] RDin,
  output [31:0] MDin,
  output [31:0] LedData
);

  wire and_1_out, and_2_out, beq, beq_bne, bne, CLK, clock_1_out, clock_2_out, comparator_1_eq,
       comparator_2_eq, comparator_2_lt, d_ff_1_q, equal, ex_mem_1_jal_2, ex_mem_1_memtoreg_2,
       ex_mem_1_regwrite_2, Go, id_ex_1_jal_2, id_ex_1_memtoreg_2, id_ex_1_memwrite_2, id_ex_1_regwrite_2,
       IR1, IR2, IR3, JMP, JR, mem_wb_1_jal_2, mem_wb_1_memtoreg_2, nand_1_out, not_1_out, not_2_out,
       not_3_out, or_1_out, RegDst, RST, SignedExt, Syscall, v0__34, v0__34_t, W1, W2, W3,
       \单周期硬布线控制器_1_alu_src , \单周期硬布线控制器_1_beq , \单周期硬布线控制器_1_bne , \单周期硬布线控制器_1_jal , \单周期硬布线控制器_1_jmp ,
       \单周期硬布线控制器_1_jr , \单周期硬布线控制器_1_memtoreg , \单周期硬布线控制器_1_memwrite , \单周期硬布线控制器_1_regwrite ;
  wire [1:0] id_ex_1_signext_2;
  wire [3:0] id_ex_1_aluop_2, \单周期硬布线控制器_1_alu_op ;
  wire [4:0] ex_mem_1_writereg_num_2, id_ex_1_writereg_num_2, mem_wb_1_writereg_num_2, multiplexer_2_out,
       multiplexer_3_out, multiplexer_4_out, multiplexer_5_out;
  wire [12:0] CNT_num;
  wire [15:0] Imm, \LoadUse次数 , \总周期数 , \插入气泡数 , \无条件分支数 , \条件分支成功数 ;
  wire [31:0] a0, adder_2_out, EX_IR, ex_mem_1_aluresult_2, ex_mem_1_pc_4_2, id_ex_1_pc_4_2,
       \id_ex_1_无符号拓展_2 , \id_ex_1_符号拓展_2 , ID_IR, if_id_1_pc_4_2, IF_IR, MEM_IR, mem_wb_1_aluresult_2,
       mem_wb_1_rd_2, mips_alu_1_p6, mips_regifile_1_r1, mips_regifile_1_r2, multiplexer_1_out,
       multiplexer_7_out, multiplexer_8_out, PC_4, PC_4_Imm, R_rs, ram_1_data, rom_1_data, shifter_1_out,
       SignImm, UnsignImm, WB_IR;
  wire [31:16] IR;

  Button \u_总复位  (.out(RST));
  Button _1 (.out(IR1));
  Button _2 (.out(IR2));
  Button _3 (.out(IR3));
  // Probe on \总周期数 
  // Probe on \总周期数 
  Button \u_继续运行  (.out(Go));
  LED #(.active("true")) led_1 (.in(W1));
  LED #(.active("true")) led_2 (.in(W2));
  LED #(.active("true")) led_3 (.in(W3));
  Hex_Digit_Display hex_digit_display_1 (.value(LedData[31:28]));  // open: dp
  // Probe on IF_PC[19:0]
  // Mips_Probe mips_probe_1: pin names not known; wires that end beside it: IF_IR
  Multiplexer #(.select(3), .width(32), .disabled("Z"), .enable("false")) multiplexer_1 (
    .in0(adder_2_out), .in2({ID_PC[31:28], IR[25:16], Imm, 2'b00}), .in3(R_rs), .in4(PC_4_Imm),
    .out(multiplexer_1_out), .sel({beq_bne, JMP, JR}));  // open: in1, in5, in6, in7
  // Probe on {beq_bne, JMP, JR}
  assign UnsignImm = {{16{1'b0}}, Imm};  // Bit_Extender bit_extender_1
  assign SignImm = {{16{Imm[15]}}, Imm};  // Bit_Extender bit_extender_2
  and and_1 (and_1_out, beq, equal);
  not not_1 (not_1_out, equal);
  and and_2 (and_2_out, not_1_out, bne);
  Hex_Digit_Display hex_digit_display_2 (.value(LedData[23:20]));  // open: dp
  Hex_Digit_Display hex_digit_display_3 (.value(LedData[27:24]));  // open: dp
  // Probe on ID_PC[19:0]
  // Mips_Probe mips_probe_2: pin names not known; wires that end beside it: ID_IR
  or or_1 (or_1_out, Go, not_2_out);
  not not_2 (not_2_out, v0__34);
  or or_2 (beq_bne, and_1_out, and_2_out);
  Hex_Digit_Display hex_digit_display_4 (.value(LedData[19:16]));  // open: dp
  Hex_Digit_Display hex_digit_display_5 (.value(LedData[15:12]));  // open: dp
  Register #(.width(32), .trigger("rising"), .Select("low")) PC (
    .D(multiplexer_1_out), .en(or_1_out), .Q(IF_PC), .clk(CLK));  // open: clr
  Adder #(.width(32)) adder_1 (.a(ID_PC), .b(shifter_1_out), .out(PC_4_Imm));  // open: cin, cout
  Shifter #(.width(32), .shift("ll")) shifter_1 (.in(SignImm), .\dist (5'b00010), .out(shifter_1_out));
  Hex_Digit_Display hex_digit_display_6 (.value(LedData[11:8]));  // open: dp
  Hex_Digit_Display hex_digit_display_7 (.value(LedData[7:4]));  // open: dp
  Clock #(.highDuration(1), .lowDuration(1)) clock_1 (.out(clock_1_out));
  // Probe on EX_PC[19:0]
  // Mips_Probe mips_probe_3: pin names not known; wires that end beside it: clock_1_out, EX_IR, CLK
  Hex_Digit_Display hex_digit_display_8 (.value(LedData[3:0]));  // open: dp
  Adder #(.width(32)) adder_2 (.a(IF_PC), .b(32'h4), .out(adder_2_out));  // open: cin, cout
  // Probe on \总周期数 
  // Probe on M_PC[19:0]
  // Mips_Probe mips_probe_4: pin names not known; wires that end beside it: MEM_IR
  ROM #(.addrWidth(10), .dataWidth(32), .Select("high")) rom_1 (.addr(IF_PC[11:2]), .data(rom_1_data));
  // Probe on \总周期数 
  // Probe on \无条件分支数 
  // Probe on \条件分支成功数 
  // Probe on \插入气泡数 
  // Probe on \LoadUse次数 
  IF_ID if_id_1 (
    .PC_4(adder_2_out), .CLK(CLK), .PC_4_2(if_id_1_pc_4_2), .\同步清零 (RST), .IR(rom_1_data), .IR_2({IR, Imm}),
    .PC(IF_PC), .PC_2(ID_PC));  // open: 使能端, 传输out, 传输in
  // Probe on IF_PC[11:0]
  // Probe on WB_PC[19:0]
  // Mips_Probe mips_probe_5: pin names not known; wires that end beside it: WB_IR
  // Mips_Probe mips_probe_6: pin names not known; wires that end beside it: {IR, Imm}, IR[31:26]
  // Probe on a0
  // Probe on EX_PC[11:0]
  // Probe on ID_PC[11:0]
  Comparator #(.width(32), .mode("twosComplement")) comparator_1 (
    .a(R_rs), .b(32'h22), .eq(comparator_1_eq));  // open: gt, lt
  Register #(.width(32), .trigger("rising"), .Select("low")) register_1 (
    .D(a0), .en(v0__34_t), .Q(LedData), .clk(CLK));  // open: clr
  // Probe on M_PC[11:0]
  and and_3 (v0__34_t, Syscall, comparator_1_eq);
  and and_4 (v0__34, Syscall, not_3_out);
  not not_3 (not_3_out, comparator_1_eq);
  // Probe on WB_PC[11:0]
  Multiplexer #(.select(1), .width(5), .disabled("Z"), .enable("false")) multiplexer_2 (
    .in0(IR[20:16]), .in1(Imm[15:11]), .out(multiplexer_2_out), .sel(RegDst));
  \单周期硬布线控制器  \u_单周期硬布线控制器_1  (
    .Func(Imm[5:0]), .OP(IR[31:26]), .ALU_OP(\单周期硬布线控制器_1_alu_op ), .MemToReg(\单周期硬布线控制器_1_memtoreg ),
    .MemWrite(\单周期硬布线控制器_1_memwrite ), .ALU_SRC(\单周期硬布线控制器_1_alu_src ), .RegWrite(\单周期硬布线控制器_1_regwrite ),
    .SysCALL(Syscall), .SignedExt(SignedExt), .RegDst(RegDst), .JR(\单周期硬布线控制器_1_jr ),
    .JMP(\单周期硬布线控制器_1_jmp ), .Beq(\单周期硬布线控制器_1_beq ), .JAL(\单周期硬布线控制器_1_jal ), .Bne(\单周期硬布线控制器_1_bne ));
  Multiplexer #(.select(1), .width(5), .disabled("Z"), .enable("false")) multiplexer_3 (
    .in0(IR[25:21]), .in1(5'b00010), .out(multiplexer_3_out), .sel(Syscall));
  Multiplexer #(.select(1), .width(5), .disabled("Z"), .enable("false")) multiplexer_4 (
    .in0(multiplexer_2_out), .in1({5{1'b1}}), .out(multiplexer_4_out), .sel(\单周期硬布线控制器_1_jal ));
  Multiplexer #(.select(1), .width(5), .disabled("Z"), .enable("false")) multiplexer_5 (
    .in0(IR[20:16]), .in1(5'b00100), .out(multiplexer_5_out), .sel(Syscall));
  // Probe on multiplexer_5_out
  Multiplexer #(.select(1), .width(32), .disabled("Z"), .enable("false")) multiplexer_6 (
    .in0(multiplexer_8_out), .in1(PC_4), .out(RDin), .sel(mem_wb_1_jal_2));
  MIPS_Regifile mips_regifile_1 (
    .Din(RDin), .Clk(CLK), .R1(mips_regifile_1_r1), .R2(mips_regifile_1_r2), .WE(RegWrite),
    .W_num(mem_wb_1_writereg_num_2), .R1_num(multiplexer_3_out), .R2_num(multiplexer_5_out));
  ID_EX id_ex_1 (
    .RegWrite(\单周期硬布线控制器_1_regwrite ), .MemToReg(\单周期硬布线控制器_1_memtoreg ), .MemWrite(\单周期硬布线控制器_1_memwrite ),
    .AluOp(\单周期硬布线控制器_1_alu_op ), .AluSrc(\单周期硬布线控制器_1_alu_src ), .PC_4(if_id_1_pc_4_2),
    .RS(mips_regifile_1_r1), .RT(mips_regifile_1_r2), .WriteReg_num(multiplexer_4_out), .\符号拓展 (SignImm),
    .CLK(CLK), .RegWrite_2(id_ex_1_regwrite_2), .MemToReg_2(id_ex_1_memtoreg_2),
    .MemWrite_2(id_ex_1_memwrite_2), .AluOp_2(id_ex_1_aluop_2), .AluSrc_2(id_ex_1_signext_2[1]),
    .PC_4_2(id_ex_1_pc_4_2), .RS_2(R_rs), .RT_2(a0), .WriteReg_num_2(id_ex_1_writereg_num_2),
    .\符号拓展_2 (\id_ex_1_符号拓展_2 ), .\同步清零 (RST), .JMP(\单周期硬布线控制器_1_jmp ), .JMP_2(JMP), .JAL(\单周期硬布线控制器_1_jal ),
    .JAL_2(id_ex_1_jal_2), .JR(\单周期硬布线控制器_1_jr ), .JR_2(JR), .beq(\单周期硬布线控制器_1_beq ), .beq_2(bne),
    .bne(\单周期硬布线控制器_1_bne ), .bne_2(beq), .\无符号拓展_2 (\id_ex_1_无符号拓展_2 ), .\无符号拓展 (UnsignImm), .PC(ID_PC),
    .PC_2(EX_PC), .SignExt(SignedExt), .SignExt_2(id_ex_1_signext_2[0]));  // open: 传输in, 传输out, 使能端, IR, IR_2, Syscall, Syscall_2
  Multiplexer #(.select(2), .width(32), .disabled("Z"), .enable("false")) multiplexer_7 (
    .in0(a0), .in1(a0), .in2(\id_ex_1_无符号拓展_2 ), .in3(\id_ex_1_符号拓展_2 ), .out(multiplexer_7_out),
    .sel(id_ex_1_signext_2));
  // MIPS_ALU mips_alu_1: pin names not known; wires that end beside it: R_rs, multiplexer_7_out, id_ex_1_aluop_2, Imm[10:6], equal, mips_alu_1_p6
  EX_MEM ex_mem_1 (
    .RegWrite(id_ex_1_regwrite_2), .MemToReg(id_ex_1_memtoreg_2), .MemWrite(id_ex_1_memwrite_2),
    .PC_4(id_ex_1_pc_4_2), .AluResult(mips_alu_1_p6), .WriteData(a0), .WriteReg_num(id_ex_1_writereg_num_2),
    .CLK(CLK), .RegWrite_2(ex_mem_1_regwrite_2), .MemToReg_2(ex_mem_1_memtoreg_2), .MemWrite_2(MemWrite),
    .PC_4_2(ex_mem_1_pc_4_2), .AluResult_2(ex_mem_1_aluresult_2), .WriteData_2(MDin),
    .WriteReg_num_2(ex_mem_1_writereg_num_2), .\同步清零 (RST), .JAL(id_ex_1_jal_2), .JAL_2(ex_mem_1_jal_2),
    .PC(EX_PC), .PC_2(M_PC));  // open: 传输in, 传输out, 使能端, Syscall, Syscall_2, v0, v0_2
  D_Flip_Flop #(.trigger("high"), .Pre_Clr_Positions("LEGACY"), .NegatePresetClear("false"), .enable("true"), .NewFFLayout("false")) d_ff_1 (.Q(d_ff_1_q));  // open: clk, D, Qn, preset, en, reset
  // Probe on 13'hc
  RAM #(.addrWidth(10), .dataWidth(32), .bus("separate"), .Select("high")) ram_1 (
    .addr(ex_mem_1_aluresult_2[11:2]), .din(MDin), .data(ram_1_data), .str(MemWrite), .clk(CLK));  // open: sel, ld, clr
  Comparator #(.width(13), .mode("twosComplement")) comparator_2 (
    .a(CNT_num), .b(13'hc), .eq(comparator_2_eq), .lt(comparator_2_lt));  // open: gt
  Clock #(.highDuration(1), .lowDuration(1)) clock_2 (.out(clock_2_out));
  nand nand_1 (nand_1_out, d_ff_1_q, comparator_2_eq);
  Counter #(.width(13), .max('h1fff), .ongoal("stay"), .trigger("rising"), .behavior("old")) counter_1 (
    .count(comparator_2_lt), .Q(CNT_num), .clk(clock_2_out));  // open: load, D, carry, clr, preset
  MEM_WB mem_wb_1 (
    .RegWrite(ex_mem_1_regwrite_2), .MemToReg(ex_mem_1_memtoreg_2), .PC_4(ex_mem_1_pc_4_2),
    .AluResult(ex_mem_1_aluresult_2), .RD(ram_1_data), .CLK(CLK), .RegWrite_2(RegWrite),
    .MemToReg_2(mem_wb_1_memtoreg_2), .PC_4_2(PC_4), .AluResult_2(mem_wb_1_aluresult_2),
    .RD_2(mem_wb_1_rd_2), .\同步清零 (RST), .WriteReg_num(ex_mem_1_writereg_num_2),
    .WriteReg_num_2(mem_wb_1_writereg_num_2), .JAL(ex_mem_1_jal_2), .JAL_2(mem_wb_1_jal_2), .PC(M_PC),
    .PC_2(WB_PC));  // open: 传输in, 传输out, 使能端, Syscall, Syscall_2, v0, v0_2
  Multiplexer #(.select(1), .width(32), .disabled("Z"), .enable("false")) multiplexer_8 (
    .in0(mem_wb_1_aluresult_2), .in1(mem_wb_1_rd_2), .out(multiplexer_8_out), .sel(mem_wb_1_memtoreg_2));
  assign CLK = nand_1_out ? clock_2_out : 1'bz;  // Controlled_Buffer controlled_buffer_1
  Pull_Resistor #(.pull(1)) pull_resistor_1 (.node(CLK));

  // Other names for the same wires on the sheet: IR[15:0] = Imm; JmpAddr[31:2] = {ID_PC[31:28], IR[25:16], Imm};
  //   shamt[4:0] = Imm[10:6]; rd[4:0] = Imm[15:11]; rt[4:0] = IR[20:16]; rs[4:0] = IR[25:21]; MEM_PC[31:0] = M_PC;
  //   PC[31:0] = IF_PC; v0[31:0] = R_rs

  // Notes on the sheet:
  //   中断源
  //   时空图监测，可删除
  //   中断等待指示
  //   数码管输出
  //   指令存储器
  //   contents of rom_1 (hex, n*v repeats v):
  //   20100000 20110000 20120000 20130000 36100000 36310001 36520002 36730003 ae100000 ae110004 ae120008
  //   ae13000c 2002000a 20110000 20120000 20130000 c
  //   指令字
  //   OP
  //   Func
  //   rs
  //   rt
  //   rd
  //   流水调试日志用
  //   ctrl+k关闭时钟连续运行，将控制位置零，进入单步调试模式调试
  //   JMP
  //   JR
  //   OP
  //   Func
  //   Beq
  //   Bne
  //   AluOP
  //   AluSrcB
  //   RegWrite
  //   JAL
  //   RegDst
  //   Syscall
  //   MemToReg
  //   MemWrite
  //   为方便自动评测，需要输出流水线各段保存的PC值，注意是PC不是PC+4，另外ID段寄存器写入信息，Mem段内存写入信息也要输出
  //   控制位
  //   暂停节拍，不能为0
  //   戳工具置1进入计数暂停模式，ctrl+k时钟自动运行到对应节拍暂停
  //   ctrl+k关闭时钟连续运行，将控制位置零，进入单步调试模式调试
  //   用这个时钟源需要去掉电路中的其他时钟源
  //   可计数暂停的时钟源
endmodule

module \气泡流水线  (
  output RegWrite,
  output MemWrite,
  output [31:0] IF_PC,
  output [31:0] ID_PC,
  output [31:0] EX_PC,
  output [31:0] M_PC,
  output [31:0] WB_PC,
  output [31:0] RDin,
  output [31:0] MDin,
  output [31:0] LedData
);

  wire and_1_out, and_2_out, and_4_out, and_5_out, beq, beq_bne, bne, CLK, comparator_1_eq, DataDizzard,
       equal, EX_CONFILCT, ex_mem_1_jal_2, ex_mem_1_memtoreg_2, ex_mem_1_syscall_2, \ex_mem_1_传输out ,
       EX_RegWrite, Go, id_ex_1_jal_2, id_ex_1_memtoreg_2, id_ex_1_memwrite_2, id_ex_1_syscall_2,
       \id_ex_1_传输out , \if_id_1_传输out , IR1, IR2, IR3, JMP, JR, MEM_CONFILCT, MEM_RegWrite, mem_wb_1_jal_2,
       mem_wb_1_memtoreg_2, mem_wb_1_syscall_2, not_1_out, not_2_out, not_3_out, not_4_out, not_5_out,
       not_6_out, or_1_out, or_2_out, or_3_out, R1_USED, R2_USED, RegDst, RST, SignedExt, Syscall, undriven,
       v0__34, v0__34_t, W1, W2, W3, \分支清零 , \单周期硬布线控制器_1_alu_src , \单周期硬布线控制器_1_beq , \单周期硬布线控制器_1_bne ,
       \单周期硬布线控制器_1_jal , \单周期硬布线控制器_1_jmp , \单周期硬布线控制器_1_jr , \单周期硬布线控制器_1_memtoreg ,
       \单周期硬布线控制器_1_memwrite , \单周期硬布线控制器_1_regwrite ;
  wire [1:0] id_ex_1_signext_2;
  wire [3:0] id_ex_1_aluop_2, \单周期硬布线控制器_1_alu_op ;
  wire [4:0] EX_WriteReg_num, mem_wb_1_writereg_num_2, MEM_WriteReg_num, multiplexer_3_out,
       multiplexer_5_out, R1_num, R2_num;
  wire [15:0] Imm, \LoadUse次数 , \总周期数 , \插入气泡数 , \无条件分支数 , \条件分支成功数 ;
  wire [27:0] id_ex_1_pc_4_2;
  wire [31:0] a0, adder_1_out, EX_IR, ex_mem_1_aluresult_2, ex_mem_1_pc_4_2, ex_mem_1_v0_2,
       \id_ex_1_无符号拓展_2 , \id_ex_1_符号拓展_2 , ID_IR, if_id_1_pc_4_2, IF_IR, MEM_IR, mem_wb_1_aluresult_2,
       mem_wb_1_rd_2, mips_alu_1_result, mips_regifile_1_r1, mips_regifile_1_r2, multiplexer_1_out,
       multiplexer_7_out, multiplexer_8_out, PC_4, PC_4_Imm, R_rs, ram_1_data, rom_1_data, shifter_1_out,
       SignImm, UnsignImm, v0, WB_IR;
  wire [31:2] JmpAddr;
  wire [31:16] IR;
  wire [31:26] id_ex_1_ir_2;

  Button \u_总复位  (.out(RST));
  Button _1 (.out(IR1));
  Button _2 (.out(IR2));
  Button _3 (.out(IR3));
  // Probe on \总周期数 
  // Probe on \总周期数 
  Button \u_继续运行  (.out(Go));
  LED #(.active("true")) led_1 (.in(W1));
  LED #(.active("true")) led_2 (.in(W2));
  LED #(.active("true")) led_3 (.in(W3));
  Hex_Digit_Display hex_digit_display_1 (.value(LedData[31:28]));  // open: dp
  // Probe on IF_PC[19:0]
  // Mips_Probe mips_probe_1: pin names not known; wires that end beside it: IF_IR
  Multiplexer #(.select(3), .width(32), .disabled("Z"), .enable("false")) multiplexer_1 (
    .in0(adder_1_out), .in2({JmpAddr, 2'b00}), .in3(R_rs), .in4(PC_4_Imm), .out(multiplexer_1_out),
    .sel({beq_bne, JMP, JR}));  // open: in1, in5, in6, in7
  // Probe on {beq_bne, JMP, JR}
  Hex_Digit_Display hex_digit_display_2 (.value(LedData[23:20]));  // open: dp
  Hex_Digit_Display hex_digit_display_3 (.value(LedData[27:24]));  // open: dp
  // Probe on ID_PC[19:0]
  // Mips_Probe mips_probe_2: pin names not known; wires that end beside it: ID_IR
  or or_1 (or_1_out, Go, not_2_out);
  Hex_Digit_Display hex_digit_display_4 (.value(LedData[19:16]));  // open: dp
  Hex_Digit_Display hex_digit_display_5 (.value(LedData[15:12]));  // open: dp
  Counter #(.width(16), .max('hffff), .ongoal("stay"), .trigger("rising"), .behavior("new")) counter_1 (
    .D({16{1'b0}}), .count(undriven), .Q(\总周期数 ), .clk(CLK), .clr(RST), .preset(undriven));  // open: load, carry, down
  Register #(.width(32), .trigger("rising"), .Select("low")) PC (
    .D(multiplexer_1_out), .en(and_1_out), .Q(IF_PC), .clk(CLK));  // open: clr
  and and_1 (and_1_out, or_1_out, not_1_out);
  not not_1 (not_1_out, DataDizzard);
  not not_2 (not_2_out, v0__34);
  Hex_Digit_Display hex_digit_display_6 (.value(LedData[11:8]));  // open: dp
  Hex_Digit_Display hex_digit_display_7 (.value(LedData[7:4]));  // open: dp
  Clock #(.highDuration(1), .lowDuration(1)) clock_1 (.out(CLK));
  // Probe on EX_PC[19:0]
  // Mips_Probe mips_probe_3: pin names not known; wires that end beside it: EX_IR
  Hex_Digit_Display hex_digit_display_8 (.value(LedData[3:0]));  // open: dp
  // Probe on \总周期数 
  // Probe on M_PC[19:0]
  // Mips_Probe mips_probe_4: pin names not known; wires that end beside it: MEM_IR
  ROM #(.addrWidth(10), .dataWidth(32), .Select("high")) rom_1 (.addr(IF_PC[11:2]), .data(rom_1_data));
  Adder #(.width(32)) adder_1 (.a(IF_PC), .b(32'h4), .out(adder_1_out));  // open: cin, cout
  // Probe on \总周期数 
  // Probe on \无条件分支数 
  // Probe on \条件分支成功数 
  // Probe on \插入气泡数 
  // Probe on \LoadUse次数 
  IF_ID if_id_1 (
    .PC_4(adder_1_out), .CLK(CLK), .PC_4_2(if_id_1_pc_4_2), .\同步清零 (\分支清零 ), .IR(rom_1_data),
    .IR_2({IR, Imm}), .\使能端 (and_2_out), .\传输out (\if_id_1_传输out ), .\传输in (1'b1), .PC(IF_PC), .PC_2(ID_PC));
  and and_2 (and_2_out, DataDizzard, not_3_out);
  not not_3 (not_3_out, \分支清零 );
  // Probe on IF_PC[11:0]
  // Probe on WB_PC[19:0]
  // Mips_Probe mips_probe_5: pin names not known; wires that end beside it: WB_IR
  // Probe on ID_PC[11:0]
  // Probe on EX_PC[11:0]
  // Mips_Probe mips_probe_6: pin names not known; wires that end beside it: {IR, Imm}, IR[31:26]
  // Probe on M_PC[11:0]
  // Probe on WB_PC[11:0]
  R1_R2_USED r1_r2_used_1 (
    .OP0(IR[26]), .OP1(IR[27]), .OP2(IR[28]), .OP3(IR[29]), .OP4(IR[30]), .OP5(IR[31]), .F0(Imm[0]),
    .F1(Imm[1]), .F2(Imm[2]), .F3(Imm[3]), .F4(Imm[4]), .F5(Imm[5]), .R1_USED(R1_USED), .R2_USED(R2_USED));
  Multiplexer #(.select(1), .width(5), .disabled("Z"), .enable("false")) multiplexer_2 (
    .in0(IR[25:21]), .in1(5'b00010), .out(R1_num), .sel(Syscall));
  Multiplexer #(.select(1), .width(5), .disabled("Z"), .enable("false")) multiplexer_3 (
    .in0(IR[20:16]), .in1(Imm[15:11]), .out(multiplexer_3_out), .sel(RegDst));
  \单周期硬布线控制器  \u_单周期硬布线控制器_1  (
    .Func(Imm[5:0]), .OP(IR[31:26]), .ALU_OP(\单周期硬布线控制器_1_alu_op ), .MemToReg(\单周期硬布线控制器_1_memtoreg ),
    .MemWrite(\单周期硬布线控制器_1_memwrite ), .ALU_SRC(\单周期硬布线控制器_1_alu_src ), .RegWrite(\单周期硬布线控制器_1_regwrite ),
    .SysCALL(Syscall), .SignedExt(SignedExt), .RegDst(RegDst), .JR(\单周期硬布线控制器_1_jr ),
    .JMP(\单周期硬布线控制器_1_jmp ), .Beq(\单周期硬布线控制器_1_beq ), .JAL(\单周期硬布线控制器_1_jal ), .Bne(\单周期硬布线控制器_1_bne ));
  Multiplexer #(.select(1), .width(5), .disabled("Z"), .enable("false")) multiplexer_4 (
    .in0(IR[20:16]), .in1(5'b00100), .out(R2_num), .sel(Syscall));
  // Probe on R2_num
  Multiplexer #(.select(1), .width(5), .disabled("Z"), .enable("false")) multiplexer_5 (
    .in0(multiplexer_3_out), .in1({5{1'b1}}), .out(multiplexer_5_out), .sel(\单周期硬布线控制器_1_jal ));
  Multiplexer #(.select(1), .width(32), .disabled("Z"), .enable("false")) multiplexer_6 (
    .in0(multiplexer_8_out), .in1(PC_4), .out(RDin), .sel(mem_wb_1_jal_2));
  not not_4 (not_4_out, CLK);
  or or_2 (or_2_out, DataDizzard, \分支清零 );
  and and_3 (\分支清零 , \id_ex_1_传输out , or_3_out);
  MIPS_Regifile mips_regifile_1 (
    .Din(RDin), .Clk(not_4_out), .R1(mips_regifile_1_r1), .R2(mips_regifile_1_r2), .WE(RegWrite),
    .W_num(mem_wb_1_writereg_num_2), .R1_num(R1_num), .R2_num(R2_num));
  or or_3 (or_3_out, id_ex_1_jal_2, JMP, JR, beq_bne);
  assign UnsignImm = {{16{1'b0}}, Imm};  // Bit_Extender bit_extender_1
  assign SignImm = {{16{Imm[15]}}, Imm};  // Bit_Extender bit_extender_2
  \数据检测  \u_数据检测_1  (
    .EX_WriteReg_num(EX_WriteReg_num), .R1_USED(R1_USED), .R1_num(R1_num), .EX_RegWrite(EX_RegWrite),
    .R2_USED(R2_USED), .R2_num(R2_num), .MEM_WriteReg_num(MEM_WriteReg_num), .MEM_RegWrite(MEM_RegWrite),
    .EX_CONFLICT(EX_CONFILCT), .DataHazzard(DataDizzard), .MEM_CONFLICT(MEM_CONFILCT));
  ID_EX id_ex_1 (
    .RegWrite(\单周期硬布线控制器_1_regwrite ), .MemToReg(\单周期硬布线控制器_1_memtoreg ), .MemWrite(\单周期硬布线控制器_1_memwrite ),
    .AluOp(\单周期硬布线控制器_1_alu_op ), .AluSrc(\单周期硬布线控制器_1_alu_src ), .PC_4(if_id_1_pc_4_2),
    .RS(mips_regifile_1_r1), .RT(mips_regifile_1_r2), .WriteReg_num(multiplexer_5_out), .\符号拓展 (SignImm),
    .\传输in (\if_id_1_传输out ), .CLK(CLK), .RegWrite_2(EX_RegWrite), .MemToReg_2(id_ex_1_memtoreg_2),
    .MemWrite_2(id_ex_1_memwrite_2), .AluOp_2(id_ex_1_aluop_2), .AluSrc_2(id_ex_1_signext_2[1]),
    .PC_4_2({JmpAddr[31:28], id_ex_1_pc_4_2}), .RS_2(R_rs), .RT_2(a0), .WriteReg_num_2(EX_WriteReg_num),
    .\符号拓展_2 (\id_ex_1_符号拓展_2 ), .\传输out (\id_ex_1_传输out ), .\同步清零 (or_2_out), .JMP(\单周期硬布线控制器_1_jmp ),
    .JMP_2(JMP), .JAL(\单周期硬布线控制器_1_jal ), .JAL_2(id_ex_1_jal_2), .JR(\单周期硬布线控制器_1_jr ), .JR_2(JR),
    .beq(\单周期硬布线控制器_1_beq ), .beq_2(beq), .bne(\单周期硬布线控制器_1_bne ), .bne_2(bne),
    .\无符号拓展_2 (\id_ex_1_无符号拓展_2 ), .\无符号拓展 (UnsignImm), .PC(ID_PC), .PC_2(EX_PC), .SignExt(SignedExt),
    .SignExt_2(id_ex_1_signext_2[0]), .IR({IR, Imm}), .IR_2({id_ex_1_ir_2, JmpAddr[27:2]}),
    .Syscall(Syscall), .Syscall_2(id_ex_1_syscall_2));  // open: 使能端
  Shifter #(.width(32), .shift("ll")) shifter_1 (.in(\id_ex_1_符号拓展_2 ), .\dist (5'b00010), .out(shifter_1_out));
  not not_5 (not_5_out, equal);
  Multiplexer #(.select(2), .width(32), .disabled("Z"), .enable("false")) multiplexer_7 (
    .in0(a0), .in1(a0), .in2(\id_ex_1_无符号拓展_2 ), .in3(\id_ex_1_符号拓展_2 ), .out(multiplexer_7_out),
    .sel(id_ex_1_signext_2));
  Adder #(.width(32)) adder_2 (
    .a({JmpAddr[31:28], id_ex_1_pc_4_2}), .b(shifter_1_out), .out(PC_4_Imm));  // open: cin, cout
  and and_4 (and_4_out, beq, equal);
  and and_5 (and_5_out, not_5_out, bne);
  // Probe on mips_alu_1_result
  MIPS_ALU mips_alu_1 (
    .X(R_rs), .Y(multiplexer_7_out), .AluOP(id_ex_1_aluop_2), .Equal(equal), .Result(mips_alu_1_result),
    .shamt(JmpAddr[12:8]));  // open: Result_2
  or or_4 (beq_bne, and_4_out, and_5_out);
  EX_MEM ex_mem_1 (
    .RegWrite(EX_RegWrite), .MemToReg(id_ex_1_memtoreg_2), .MemWrite(id_ex_1_memwrite_2),
    .PC_4({JmpAddr[31:28], id_ex_1_pc_4_2}), .AluResult(mips_alu_1_result), .WriteData(a0),
    .WriteReg_num(EX_WriteReg_num), .\传输in (\id_ex_1_传输out ), .CLK(CLK), .RegWrite_2(MEM_RegWrite),
    .MemToReg_2(ex_mem_1_memtoreg_2), .MemWrite_2(MemWrite), .PC_4_2(ex_mem_1_pc_4_2),
    .AluResult_2(ex_mem_1_aluresult_2), .WriteData_2(MDin), .WriteReg_num_2(MEM_WriteReg_num),
    .\传输out (\ex_mem_1_传输out ), .\同步清零 (RST), .JAL(id_ex_1_jal_2), .JAL_2(ex_mem_1_jal_2), .PC(EX_PC),
    .PC_2(M_PC), .Syscall(id_ex_1_syscall_2), .Syscall_2(ex_mem_1_syscall_2), .v0(R_rs), .v0_2(ex_mem_1_v0_2));  // open: 使能端
  // Probe on ex_mem_1_aluresult_2
  RAM #(.addrWidth(10), .dataWidth(32), .bus("separate"), .Select("high")) ram_1 (
    .addr(ex_mem_1_aluresult_2[11:2]), .din(MDin), .data(ram_1_data), .str(MemWrite), .clk(CLK));  // open: sel, ld, clr
  MEM_WB mem_wb_1 (
    .RegWrite(MEM_RegWrite), .MemToReg(ex_mem_1_memtoreg_2), .PC_4(ex_mem_1_pc_4_2),
    .AluResult(ex_mem_1_aluresult_2), .RD(ram_1_data), .\传输in (\ex_mem_1_传输out ), .CLK(CLK),
    .RegWrite_2(RegWrite), .MemToReg_2(mem_wb_1_memtoreg_2), .PC_4_2(PC_4),
    .AluResult_2(mem_wb_1_aluresult_2), .RD_2(mem_wb_1_rd_2), .\同步清零 (RST), .WriteReg_num(MEM_WriteReg_num),
    .WriteReg_num_2(mem_wb_1_writereg_num_2), .JAL(ex_mem_1_jal_2), .JAL_2(mem_wb_1_jal_2), .PC(M_PC),
    .PC_2(WB_PC), .Syscall(ex_mem_1_syscall_2), .Syscall_2(mem_wb_1_syscall_2), .v0(ex_mem_1_v0_2), .v0_2(v0));  // open: 传输out, 使能端
  Comparator #(.width(32), .mode("twosComplement")) comparator_1 (
    .a(v0), .b(32'h22), .eq(comparator_1_eq));  // open: gt, lt
  Register #(.width(32), .trigger("rising"), .Select("low")) register_1 (
    .D(a0), .en(v0__34_t), .Q(LedData), .clk(CLK));  // open: clr
  Multiplexer #(.select(1), .width(32), .disabled("Z"), .enable("false")) multiplexer_8 (
    .in0(mem_wb_1_aluresult_2), .in1(mem_wb_1_rd_2), .out(multiplexer_8_out), .sel(mem_wb_1_memtoreg_2));
  not not_6 (not_6_out, comparator_1_eq);
  and and_6 (v0__34_t, mem_wb_1_syscall_2, comparator_1_eq);
  and and_7 (v0__34, mem_wb_1_syscall_2, not_6_out);

  // Other names for the same wires on the sheet: IR[15:0] = Imm; rd[4:0] = Imm[15:11]; rt[4:0] = IR[20:16];
  //   rs[4:0] = IR[25:21]; shamt[4:0] = JmpAddr[12:8]; MEM_PC[31:0] = M_PC; PC[31:0] = IF_PC

  // Notes on the sheet:
  //   中断源
  //   时空图监测，可删除
  //   中断等待指示
  //   数码管输出
  //   IF
  //   指令存储器
  //   contents of rom_1 (hex, n*v repeats v):
  //   20110001 8000c05 20110001 20120002 20130003 8000c09 20110001 20120002 20130003 8000c0d 20110001
  //   20120002 20130003 8000c11 20110001 20120002 20130003 c000cb8 20100001 20110001 118fc0 112020
  //   20020022 c 118882 12200001 8000c15 112020 20020022 c 20110001 118880 112020 20020022 c 12200001
  //   8000c1f 20110001 118fc0 112020 20020022 c 1188c3 112020 20020022 c 118903 112020 20020022 c 118903
  //   112020 20020022 c 118903 112020 20020022 c 118903 112020 20020022 c 118903 112020 20020022 c 118903
  //   112020 20020022 c 118903 112020 20020022 c 20100001 109fc0 139fc3 8021 2012000c 24160003 26100001
  //   3210000f 20080008 20090001 139900 2709825 132020 20020022 c 1094022 1500fff9 22100001 2018000f
  //   2188024 108700 20080008 20090001 139902 2709825 132021 20020022 c 1094022 1500fff9 108702 2c9b022
  //   12c00001 8000c50 4020 1084027 84400 3508ffff 82021 20020022 c 2010ffff 20110000 ae300000 22100001
  //   22310004 ae300000 22100001 22310004 ae300000 22100001 22310004 ae300000 22100001 22310004 ae300000
  //   22100001 22310004 ae300000 22100001 22310004 ae300000 22100001 22310004 ae300000 22100001 22310004
  //   ae300000 22100001 22310004 ae300000 22100001 22310004 ae300000 22100001 22310004 ae300000 22100001
  //   22310004 ae300000 22100001 22310004 ae300000 22100001 22310004 ae300000 22100001 22310004 ae300000
  //   22100001 22310004 22100001 8020 2011003c 8e130000 8e340000 274402a 11000002 ae330000 ae140000
  //   2231fffc 1611fff8 102020 20020022 c 22100004 2011003c 1611fff2 20020032 c 20100000 22100001 102020
  //   20020022 c 22100002 102020 20020022 c 22100003 102020 20020022 c 22100004 102020 20020022 c 22100005
  //   102020 20020022 c 22100006 102020 20020022 c 22100007 102020 20020022 c 22100008 102020 20020022
  //   20020022 c 3e00008
  //   OP
  //   Func
  //   rs
  //   指令字
  //   rt
  //   rd
  //   流水调试日志用
  //   Beq
  //   JMP
  //   JR
  //   OP
  //   Func
  //   ID
  //   Bne
  //   MemToReg
  //   MemWrite
  //   AluOP
  //   AluSrcB
  //   RegWrite
  //   JAL
  //   RegDst
  //   Syscall
  //   为方便自动评测，需要输出流水线各段保存的PC值，注意是PC不是PC+4，另外ID段寄存器写入信息，Mem段内存写入信息也要输出
  //   EX
  //   MEM
  //   WB
endmodule

module \重定向流水线  (
  output RegWrite,
  output MemWrite,
  output [31:0] IF_PC,
  output [31:0] ID_PC,
  output [31:0] EX_PC,
  output [31:0] M_PC,
  output [31:0] WB_PC,
  output [31:0] RDin,
  output [31:0] MDin,
  output [31:0] LedData
);

  wire and_1_out, and_2_out, and_4_out, and_5_out, beq, beq_bne, bne, CLK, comparator_1_eq, equal,
       ex_mem_1_jal_2, ex_mem_1_memtoreg_2, ex_mem_1_syscall_2, \ex_mem_1_传输out , EX_MemToReg, EX_RegWrite,
       Go, id_ex_1_jal_2, id_ex_1_memwrite_2, id_ex_1_syscall_2, \id_ex_1_传输out , \if_id_1_传输out , IR1, IR2,
       IR3, JMP, JR, LoadUse, MEM_RegWrite, mem_wb_1_jal_2, mem_wb_1_memtoreg_2, mem_wb_1_syscall_2,
       not_1_out, not_2_out, not_3_out, not_4_out, not_5_out, not_6_out, or_1_out, or_2_out, or_3_out,
       R1_USED, R2_USED, RegDst, RST, SignedExt, Syscall, undriven, v0__34, v0__34_t, W1, W2, W3, \分支清零 ,
       \单周期硬布线控制器_1_alu_src , \单周期硬布线控制器_1_beq , \单周期硬布线控制器_1_bne , \单周期硬布线控制器_1_jal , \单周期硬布线控制器_1_jmp ,
       \单周期硬布线控制器_1_jr , \单周期硬布线控制器_1_memtoreg , \单周期硬布线控制器_1_memwrite , \单周期硬布线控制器_1_regwrite ;
  wire [1:0] id_ex_1_signext_2, register_1_q, register_2_q, RsForward, RtForward;
  wire [3:0] id_ex_1_aluop_2, \单周期硬布线控制器_1_alu_op ;
  wire [4:0] EX_WriteReg_num, mem_wb_1_writereg_num_2, MEM_WriteReg_num, multiplexer_2_out,
       multiplexer_5_out, R1_num, R2_num;
  wire [15:0] Imm, \LoadUse次数 , \总周期数 , \插入气泡数 , \无条件分支数 , \条件分支成功数 ;
  wire [27:0] id_ex_1_pc_4_2;
  wire [31:0] a0, adder_1_out, EX_IR, ex_mem_1_aluresult_2, ex_mem_1_pc_4_2, ex_mem_1_v0_2, id_ex_1_rs_2,
       id_ex_1_rt_2, \id_ex_1_无符号拓展_2 , \id_ex_1_符号拓展_2 , ID_IR, if_id_1_pc_4_2, IF_IR, MEM_IR,
       mem_wb_1_aluresult_2, mem_wb_1_rd_2, mips_alu_1_result, mips_regifile_1_r1, mips_regifile_1_r2,
       multiplexer_1_out, multiplexer_7_out, multiplexer_10_out, PC_4, PC_4_Imm, R_rs, ram_1_data,
       rom_1_data, shifter_1_out, SignImm, UnsignImm, v0, WB_IR;
  wire [31:2] JmpAddr;
  wire [31:16] IR;
  wire [31:26] id_ex_1_ir_2;

  Button \u_总复位  (.out(RST));
  Button _1 (.out(IR1));
  Button _2 (.out(IR2));
  Button _3 (.out(IR3));
  // Probe on \总周期数 
  // Probe on \总周期数 
  Button \u_继续运行  (.out(Go));
  LED #(.active("true")) led_1 (.in(W1));
  LED #(.active("true")) led_2 (.in(W2));
  LED #(.active("true")) led_3 (.in(W3));
  Hex_Digit_Display hex_digit_display_1 (.value(LedData[31:28]));  // open: dp
  // Probe on IF_PC[19:0]
  // Mips_Probe mips_probe_1: pin names not known; wires that end beside it: IF_IR
  Hex_Digit_Display hex_digit_display_2 (.value(LedData[27:24]));  // open: dp
  Hex_Digit_Display hex_digit_display_3 (.value(LedData[23:20]));  // open: dp
  // Probe on ID_PC[19:0]
  // Mips_Probe mips_probe_2: pin names not known; wires that end beside it: ID_IR
  Multiplexer #(.select(3), .width(32), .disabled("Z"), .enable("false")) multiplexer_1 (
    .in0(adder_1_out), .in2({JmpAddr, 2'b00}), .in3(R_rs), .in4(PC_4_Imm), .out(multiplexer_1_out),
    .sel({beq_bne, JMP, JR}));  // open: in1, in5, in6, in7
  // Probe on {beq_bne, JMP, JR}
  Hex_Digit_Display hex_digit_display_4 (.value(LedData[15:12]));  // open: dp
  Hex_Digit_Display hex_digit_display_5 (.value(LedData[19:16]));  // open: dp
  Counter #(.width(16), .max('hffff), .ongoal("stay"), .trigger("rising"), .behavior("new")) counter_1 (
    .D({16{1'b0}}), .count(undriven), .Q(\总周期数 ), .clk(CLK), .clr(RST), .preset(undriven));  // open: load, carry, down
  and and_1 (and_1_out, or_1_out, not_1_out);
  not not_1 (not_1_out, LoadUse);
  or or_1 (or_1_out, Go, not_2_out);
  not not_2 (not_2_out, v0__34);
  Hex_Digit_Display hex_digit_display_6 (.value(LedData[11:8]));  // open: dp
  Hex_Digit_Display hex_digit_display_7 (.value(LedData[7:4]));  // open: dp
  Clock #(.highDuration(1), .lowDuration(1)) clock_1 (.out(CLK));
  // Probe on EX_PC[19:0]
  // Mips_Probe mips_probe_3: pin names not known; wires that end beside it: EX_IR
  Register #(.width(32), .trigger("rising"), .Select("low")) PC (
    .D(multiplexer_1_out), .en(and_1_out), .Q(IF_PC), .clk(CLK));  // open: clr
  Hex_Digit_Display hex_digit_display_8 (.value(LedData[3:0]));  // open: dp
  // Probe on \总周期数 
  // Probe on M_PC[19:0]
  // Mips_Probe mips_probe_4: pin names not known; wires that end beside it: MEM_IR
  ROM #(.addrWidth(10), .dataWidth(32), .Select("high")) rom_1 (.addr(IF_PC[11:2]), .data(rom_1_data));
  Adder #(.width(32)) adder_1 (.a(IF_PC), .b(32'h4), .out(adder_1_out));  // open: cin, cout
  // Probe on \总周期数 
  // Probe on \无条件分支数 
  // Probe on \条件分支成功数 
  // Probe on \插入气泡数 
  // Probe on \LoadUse次数 
  IF_ID if_id_1 (
    .PC_4(adder_1_out), .CLK(CLK), .PC_4_2(if_id_1_pc_4_2), .\同步清零 (\分支清零 ), .IR(rom_1_data),
    .IR_2({IR, Imm}), .\使能端 (and_2_out), .\传输out (\if_id_1_传输out ), .\传输in (1'b1), .PC(IF_PC), .PC_2(ID_PC));
  and and_2 (and_2_out, LoadUse, not_3_out);
  not not_3 (not_3_out, \分支清零 );
  // Probe on IF_PC[11:0]
  // Probe on WB_PC[19:0]
  // Mips_Probe mips_probe_5: pin names not known; wires that end beside it: WB_IR
  // Probe on EX_PC[11:0]
  // Probe on ID_PC[11:0]
  // Mips_Probe mips_probe_6: pin names not known; wires that end beside it: {IR, Imm}, IR[31:26]
  // Probe on M_PC[11:0]
  // Probe on WB_PC[11:0]
  R1_R2_USED r1_r2_used_1 (
    .OP0(IR[26]), .OP1(IR[27]), .OP2(IR[28]), .OP3(IR[29]), .OP4(IR[30]), .OP5(IR[31]), .F0(Imm[0]),
    .F1(Imm[1]), .F2(Imm[2]), .F3(Imm[3]), .F4(Imm[4]), .F5(Imm[5]), .R1_USED(R1_USED), .R2_USED(R2_USED));
  Multiplexer #(.select(1), .width(5), .disabled("Z"), .enable("false")) multiplexer_2 (
    .in0(IR[20:16]), .in1(Imm[15:11]), .out(multiplexer_2_out), .sel(RegDst));
  \单周期硬布线控制器  \u_单周期硬布线控制器_1  (
    .Func(Imm[5:0]), .OP(IR[31:26]), .ALU_OP(\单周期硬布线控制器_1_alu_op ), .MemToReg(\单周期硬布线控制器_1_memtoreg ),
    .MemWrite(\单周期硬布线控制器_1_memwrite ), .ALU_SRC(\单周期硬布线控制器_1_alu_src ), .RegWrite(\单周期硬布线控制器_1_regwrite ),
    .SysCALL(Syscall), .SignedExt(SignedExt), .RegDst(RegDst), .JR(\单周期硬布线控制器_1_jr ),
    .JMP(\单周期硬布线控制器_1_jmp ), .Beq(\单周期硬布线控制器_1_beq ), .JAL(\单周期硬布线控制器_1_jal ), .Bne(\单周期硬布线控制器_1_bne ));
  Multiplexer #(.select(1), .width(5), .disabled("Z"), .enable("false")) multiplexer_3 (
    .in0(IR[25:21]), .in1(5'b00010), .out(R1_num), .sel(Syscall));
  Multiplexer #(.select(1), .width(5), .disabled("Z"), .enable("false")) multiplexer_4 (
    .in0(IR[20:16]), .in1(5'b00100), .out(R2_num), .sel(Syscall));
  // Probe on R2_num
  Multiplexer #(.select(1), .width(5), .disabled("Z"), .enable("false")) multiplexer_5 (
    .in0(multiplexer_2_out), .in1({5{1'b1}}), .out(multiplexer_5_out), .sel(\单周期硬布线控制器_1_jal ));
  Multiplexer #(.select(1), .width(32), .disabled("Z"), .enable("false")) multiplexer_6 (
    .in0(multiplexer_10_out), .in1(PC_4), .out(RDin), .sel(mem_wb_1_jal_2));
  and and_3 (\分支清零 , \id_ex_1_传输out , or_3_out);
  not not_4 (not_4_out, CLK);
  MIPS_Regifile mips_regifile_1 (
    .Din(RDin), .Clk(not_4_out), .R1(mips_regifile_1_r1), .R2(mips_regifile_1_r2), .WE(RegWrite),
    .W_num(mem_wb_1_writereg_num_2), .R1_num(R1_num), .R2_num(R2_num));
  or or_2 (or_2_out, LoadUse, \分支清零 );
  or or_3 (or_3_out, id_ex_1_jal_2, JMP, JR, beq_bne);
  assign UnsignImm = {{16{1'b0}}, Imm};  // Bit_Extender bit_extender_1
  assign SignImm = {{16{Imm[15]}}, Imm};  // Bit_Extender bit_extender_2
  ID_EX id_ex_1 (
    .RegWrite(\单周期硬布线控制器_1_regwrite ), .MemToReg(\单周期硬布线控制器_1_memtoreg ), .MemWrite(\单周期硬布线控制器_1_memwrite ),
    .AluOp(\单周期硬布线控制器_1_alu_op ), .AluSrc(\单周期硬布线控制器_1_alu_src ), .PC_4(if_id_1_pc_4_2),
    .RS(mips_regifile_1_r1), .RT(mips_regifile_1_r2), .WriteReg_num(multiplexer_5_out), .\符号拓展 (SignImm),
    .\传输in (\if_id_1_传输out ), .CLK(CLK), .RegWrite_2(EX_RegWrite), .MemToReg_2(EX_MemToReg),
    .MemWrite_2(id_ex_1_memwrite_2), .AluOp_2(id_ex_1_aluop_2), .AluSrc_2(id_ex_1_signext_2[1]),
    .PC_4_2({JmpAddr[31:28], id_ex_1_pc_4_2}), .RS_2(id_ex_1_rs_2), .RT_2(id_ex_1_rt_2),
    .WriteReg_num_2(EX_WriteReg_num), .\符号拓展_2 (\id_ex_1_符号拓展_2 ), .\传输out (\id_ex_1_传输out ),
    .\同步清零 (or_2_out), .JMP(\单周期硬布线控制器_1_jmp ), .JMP_2(JMP), .JAL(\单周期硬布线控制器_1_jal ), .JAL_2(id_ex_1_jal_2),
    .JR(\单周期硬布线控制器_1_jr ), .JR_2(JR), .beq(\单周期硬布线控制器_1_beq ), .beq_2(beq), .bne(\单周期硬布线控制器_1_bne ),
    .bne_2(bne), .\无符号拓展_2 (\id_ex_1_无符号拓展_2 ), .\无符号拓展 (UnsignImm), .PC(ID_PC), .PC_2(EX_PC),
    .SignExt(SignedExt), .SignExt_2(id_ex_1_signext_2[0]), .IR({IR, Imm}),
    .IR_2({id_ex_1_ir_2, JmpAddr[27:2]}), .Syscall(Syscall), .Syscall_2(id_ex_1_syscall_2));  // open: 使能端
  LoadUse_RsRTForward loaduse_rsrtforward_1 (
    .R1_USED(R1_USED), .R1_num(R1_num), .EX_WriteReg_num(EX_WriteReg_num), .EX_MemToReg(EX_MemToReg),
    .R2_USED(R2_USED), .R2_num(R2_num), .EX_RegWrite(EX_RegWrite), .MEM_WriteReg_num(MEM_WriteReg_num),
    .MEM_RegWrite(MEM_RegWrite), .LoadUse(LoadUse), .RsForward(RsForward), .RtForward(RtForward));
  Shifter #(.width(32), .shift("ll")) shifter_1 (.in(\id_ex_1_符号拓展_2 ), .\dist (5'b00010), .out(shifter_1_out));
  not not_5 (not_5_out, equal);
  Multiplexer #(.select(2), .width(32), .disabled("Z"), .enable("false")) multiplexer_7 (
    .in0(a0), .in1(a0), .in2(\id_ex_1_无符号拓展_2 ), .in3(\id_ex_1_符号拓展_2 ), .out(multiplexer_7_out),
    .sel(id_ex_1_signext_2));
  Adder #(.width(32)) adder_2 (
    .a({JmpAddr[31:28], id_ex_1_pc_4_2}), .b(shifter_1_out), .out(PC_4_Imm));  // open: cin, cout
  and and_4 (and_4_out, beq, equal);
  and and_5 (and_5_out, not_5_out, bne);
  // Probe on mips_alu_1_result
  MIPS_ALU mips_alu_1 (
    .X(R_rs), .Y(multiplexer_7_out), .AluOP(id_ex_1_aluop_2), .Equal(equal), .Result(mips_alu_1_result),
    .shamt(JmpAddr[12:8]));  // open: Result_2
  or or_4 (beq_bne, and_4_out, and_5_out);
  EX_MEM ex_mem_1 (
    .RegWrite(EX_RegWrite), .MemToReg(EX_MemToReg), .MemWrite(id_ex_1_memwrite_2),
    .PC_4({JmpAddr[31:28], id_ex_1_pc_4_2}), .AluResult(mips_alu_1_result), .WriteData(a0),
    .WriteReg_num(EX_WriteReg_num), .\传输in (\id_ex_1_传输out ), .CLK(CLK), .RegWrite_2(MEM_RegWrite),
    .MemToReg_2(ex_mem_1_memtoreg_2), .MemWrite_2(MemWrite), .PC_4_2(ex_mem_1_pc_4_2),
    .AluResult_2(ex_mem_1_aluresult_2), .WriteData_2(MDin), .WriteReg_num_2(MEM_WriteReg_num),
    .\传输out (\ex_mem_1_传输out ), .\同步清零 (RST), .JAL(id_ex_1_jal_2), .JAL_2(ex_mem_1_jal_2), .PC(EX_PC),
    .PC_2(M_PC), .Syscall(id_ex_1_syscall_2), .Syscall_2(ex_mem_1_syscall_2), .v0(R_rs), .v0_2(ex_mem_1_v0_2));  // open: 使能端
  Multiplexer #(.select(2), .width(32), .disabled("Z"), .enable("false")) multiplexer_8 (
    .in0(id_ex_1_rs_2), .in1(multiplexer_10_out), .in2(ex_mem_1_aluresult_2), .out(R_rs), .sel(register_2_q));  // open: in3
  Register #(.width(2), .trigger("rising"), .Select("low")) register_1 (
    .D(RtForward), .Q(register_1_q), .clk(CLK), .clr(Go));  // open: en
  Multiplexer #(.select(2), .width(32), .disabled("Z"), .enable("false")) multiplexer_9 (
    .in0(id_ex_1_rt_2), .in1(multiplexer_10_out), .in2(ex_mem_1_aluresult_2), .out(a0), .sel(register_1_q));  // open: in3
  // Probe on ex_mem_1_aluresult_2
  Register #(.width(2), .trigger("rising"), .Select("low")) register_2 (
    .D(RsForward), .Q(register_2_q), .clk(CLK), .clr(Go));  // open: en
  RAM #(.addrWidth(10), .dataWidth(32), .bus("separate"), .Select("high")) ram_1 (
    .addr(ex_mem_1_aluresult_2[11:2]), .din(MDin), .data(ram_1_data), .str(MemWrite), .clk(CLK));  // open: sel, ld, clr
  MEM_WB mem_wb_1 (
    .RegWrite(MEM_RegWrite), .MemToReg(ex_mem_1_memtoreg_2), .PC_4(ex_mem_1_pc_4_2),
    .AluResult(ex_mem_1_aluresult_2), .RD(ram_1_data), .\传输in (\ex_mem_1_传输out ), .CLK(CLK),
    .RegWrite_2(RegWrite), .MemToReg_2(mem_wb_1_memtoreg_2), .PC_4_2(PC_4),
    .AluResult_2(mem_wb_1_aluresult_2), .RD_2(mem_wb_1_rd_2), .\同步清零 (RST), .WriteReg_num(MEM_WriteReg_num),
    .WriteReg_num_2(mem_wb_1_writereg_num_2), .JAL(ex_mem_1_jal_2), .JAL_2(mem_wb_1_jal_2), .PC(M_PC),
    .PC_2(WB_PC), .Syscall(ex_mem_1_syscall_2), .Syscall_2(mem_wb_1_syscall_2), .v0(ex_mem_1_v0_2), .v0_2(v0));  // open: 传输out, 使能端
  Register #(.width(32), .trigger("rising"), .Select("low")) register_3 (
    .D(a0), .en(v0__34_t), .Q(LedData), .clk(CLK));  // open: clr
  Multiplexer #(.select(1), .width(32), .disabled("Z"), .enable("false")) multiplexer_10 (
    .in0(mem_wb_1_aluresult_2), .in1(mem_wb_1_rd_2), .out(multiplexer_10_out), .sel(mem_wb_1_memtoreg_2));
  Comparator #(.width(32), .mode("twosComplement")) comparator_1 (
    .a(v0), .b(32'h22), .eq(comparator_1_eq));  // open: gt, lt
  not not_6 (not_6_out, comparator_1_eq);
  and and_6 (v0__34_t, mem_wb_1_syscall_2, comparator_1_eq);
  and and_7 (v0__34, mem_wb_1_syscall_2, not_6_out);

  // Other names for the same wires on the sheet: IR[15:0] = Imm; rd[4:0] = Imm[15:11]; rt[4:0] = IR[20:16];
  //   rs[4:0] = IR[25:21]; shamt[4:0] = JmpAddr[12:8]; MEM_PC[31:0] = M_PC; PC[31:0] = IF_PC

  // Notes on the sheet:
  //   中断源
  //   时空图监测，可删除
  //   中断等待指示
  //   数码管输出
  //   IF
  //   指令存储器
  //   contents of rom_1 (hex, n*v repeats v):
  //   20110001 8000c05 20110001 20120002 20130003 8000c09 20110001 20120002 20130003 8000c0d 20110001
  //   20120002 20130003 8000c11 20110001 20120002 20130003 c000cb8 20100001 20110001 118fc0 112020
  //   20020022 c 118882 12200001 8000c15 112020 20020022 c 20110001 118880 112020 20020022 c 12200001
  //   8000c1f 20110001 118fc0 112020 20020022 c 1188c3 112020 20020022 c 118903 112020 20020022 c 118903
  //   112020 20020022 c 118903 112020 20020022 c 118903 112020 20020022 c 118903 112020 20020022 c 118903
  //   112020 20020022 c 118903 112020 20020022 c 20100001 109fc0 139fc3 8021 2012000c 24160003 26100001
  //   3210000f 20080008 20090001 139900 2709825 132020 20020022 c 1094022 1500fff9 22100001 2018000f
  //   2188024 108700 20080008 20090001 139902 2709825 132021 20020022 c 1094022 1500fff9 108702 2c9b022
  //   12c00001 8000c50 4020 1084027 84400 3508ffff 82021 20020022 c 2010ffff 20110000 ae300000 22100001
  //   22310004 ae300000 22100001 22310004 ae300000 22100001 22310004 ae300000 22100001 22310004 ae300000
  //   22100001 22310004 ae300000 22100001 22310004 ae300000 22100001 22310004 ae300000 22100001 22310004
  //   ae300000 22100001 22310004 ae300000 22100001 22310004 ae300000 22100001 22310004 ae300000 22100001
  //   22310004 ae300000 22100001 22310004 ae300000 22100001 22310004 ae300000 22100001 22310004 ae300000
  //   22100001 22310004 22100001 8020 2011003c 8e130000 8e340000 274402a 11000002 ae330000 ae140000
  //   2231fffc 1611fff8 102020 20020022 c 22100004 2011003c 1611fff2 20020032 c 20100000 22100001 102020
  //   20020022 c 22100002 102020 20020022 c 22100003 102020 20020022 c 22100004 102020 20020022 c 22100005
  //   102020 20020022 c 22100006 102020 20020022 c 22100007 102020 20020022 c 22100008 102020 20020022
  //   20020022 c 3e00008
  //   OP
  //   rs
  //   指令字
  //   rt
  //   rd
  //   流水调试日志用
  //   Func
  //   JMP
  //   JR
  //   OP
  //   Func
  //   ID
  //   Beq
  //   Bne
  //   MemToReg
  //   MemWrite
  //   AluOP
  //   AluSrcB
  //   RegWrite
  //   JAL
  //   RegDst
  //   Syscall
  //   为方便自动评测，需要输出流水线各段保存的PC值，注意是PC不是PC+4，另外ID段寄存器写入信息，Mem段内存写入信息也要输出
  //   EX
  //   MEM
  //   WB
endmodule

module \中断按键参考电路  (
  input  \同步清零信号 ,
  output \与中断屏蔽位与 
);

  wire \_1号中断_out , and_1_out, clock_1_out, d_ff_1_q, or_1_out, or_2_out;

  Clock #(.highDuration(1), .lowDuration(1)) clock_1 (.out(clock_1_out));
  Button \_1号中断  (.out(\_1号中断_out ));
  LED #(.active("true")) \_1号中断等待指示灯  (.in(or_1_out));
  or or_1 (or_1_out, \与中断屏蔽位与 , d_ff_1_q);
  D_Flip_Flop #(.trigger("rising"), .Pre_Clr_Positions("LEGACY"), .NegatePresetClear("false"), .enable("true"), .NewFFLayout("false")) d_ff_1 (
    .clk(\_1号中断_out ), .D(1'b1), .Q(d_ff_1_q), .reset(\与中断屏蔽位与 ));  // open: Qn, preset, en
  or or_2 (or_2_out, d_ff_1_q, \与中断屏蔽位与 );
  and and_1 (and_1_out, or_2_out, ~\同步清零信号 );  // AND_Gate
  D_Flip_Flop #(.trigger("rising"), .Pre_Clr_Positions("LEGACY"), .NegatePresetClear("false"), .enable("true"), .NewFFLayout("false")) IR1 (
    .clk(clock_1_out), .D(and_1_out), .Q(\与中断屏蔽位与 ));  // open: Qn, preset, en, reset

  // Notes on the sheet:
  //   中断信号采样参考电路
  //   Reset 
endmodule
module \单周期MIPS_单级中断  (
  input  IR1,
  input  IR2,
  input  IR3,
  output RegWrite,
  output MemWrite,
  output [31:0] PC,
  output [31:0] IR,
  output [31:0] RDin,
  output [31:0] MDin,
  output [31:0] LedData
);

  wire and_1_out, and_2_out, and_3_out, and_4_out, and_5_out, beq, beq_bne, bne, CLK, Clr1, Clr2, Clr3,
       comparator_1_eq, comparator_2_eq, comparator_3_eq, comparator_4_eq, comparator_5_eq, d_ff_1_q,
       d_ff_2_q, d_ff_3_q, d_ff_4_q, equal, eret, Go, INT1, INT2, INT3, IntR, IR1_t, IR2_t, IR3_t, IRA, IRB,
       IRC, JAL, JMP, JR, not_1_out, not_2_out, not_3_out, not_4_out, or_1_out, or_5_out, or_6_out, or_7_out,
       or_11_out, RegDst, RST, SignedExt, Syscall, v0__34, v0__34_t, W1, W2, W3, \中断请求 ,
       \单周期硬布线控制器_1_memtoreg ;
  wire [1:0] IntNo;
  wire [1:1] \单周期硬布线控制器_1_alu_src ;
  wire [3:0] \单周期硬布线控制器_1_alu_op ;
  wire [4:0] multiplexer_3_out, multiplexer_4_out, multiplexer_5_out, multiplexer_6_out;
  wire [15:0] \总周期数 ;
  wire [27:0] PC_4;
  wire [31:0] IntAddr, mips_alu_1_result, multiplexer_1_out, multiplexer_8_out, multiplexer_9_out, PC_4_Imm,
       R_rs, ram_1_data, shifter_1_out, SignImm, UnsignImm;
  wire [31:28] JmpAddr;

  Clock #(.highDuration(1), .lowDuration(1)) clock_1 (.out(CLK));
  Button _1 (.out(IRA));
  Button _2 (.out(IRB));
  Button _3 (.out(IRC));
  Button \u_继续运行  (.out(Go));
  LED #(.active("true")) led_1 (.in(W1));
  LED #(.active("true")) led_2 (.in(W2));
  LED #(.active("true")) led_3 (.in(W3));
  Hex_Digit_Display hex_digit_display_1 (.value(LedData[31:28]));  // open: dp
  Comparator #(.width(16), .mode("twosComplement")) comparator_1 (
    .a(16'h23b), .b(\总周期数 ), .eq(comparator_1_eq));  // open: gt, lt
  Comparator #(.width(16), .mode("twosComplement")) comparator_2 (
    .a(\总周期数 ), .b(16'h1), .eq(comparator_2_eq));  // open: gt, lt
  Comparator #(.width(16), .mode("twosComplement")) comparator_3 (
    .a(\总周期数 ), .b(16'h4), .eq(comparator_3_eq));  // open: gt, lt
  Comparator #(.width(16), .mode("twosComplement")) comparator_4 (
    .a(\总周期数 ), .b(16'h7), .eq(comparator_4_eq));  // open: gt, lt
  Hex_Digit_Display hex_digit_display_2 (.value(LedData[27:24]));  // open: dp
  Hex_Digit_Display hex_digit_display_3 (.value(LedData[23:20]));  // open: dp
  or or_1 (or_1_out, comparator_1_eq, comparator_2_eq);
  assign IRA = or_1_out ? ~CLK : 1'bz;  // Controlled_Inverter controlled_inverter_1
  assign IRB = comparator_3_eq ? ~CLK : 1'bz;  // Controlled_Inverter controlled_inverter_2
  assign IRC = comparator_4_eq ? ~CLK : 1'bz;  // Controlled_Inverter controlled_inverter_3
  not not_1 (not_1_out, v0__34);
  Counter #(.width(16), .max('hffff), .ongoal("wrap"), .trigger("rising"), .behavior("new")) counter_1 (
    .count(not_1_out), .Q(\总周期数 ), .clk(CLK), .clr(RST), .preset(not_1_out));  // open: load, D, carry, down
  or or_2 (W1, INT1, d_ff_1_q);
  or or_3 (W2, INT2, d_ff_2_q);
  or or_4 (W3, INT3, d_ff_3_q);
  Hex_Digit_Display hex_digit_display_4 (.value(LedData[19:16]));  // open: dp
  Hex_Digit_Display hex_digit_display_5 (.value(LedData[15:12]));  // open: dp
  Pull_Resistor #(.pull(0)) pull_resistor_1 (.node(IRA));
  Pull_Resistor #(.pull(0)) pull_resistor_2 (.node(IRB));
  Pull_Resistor #(.pull(0)) pull_resistor_3 (.node(IRC));
  D_Flip_Flop #(.trigger("rising"), .Pre_Clr_Positions("LEGACY"), .NegatePresetClear("false"), .enable("true"), .NewFFLayout("false")) d_ff_1 (
    .clk(IR1_t), .D(1'b1), .Q(d_ff_1_q), .reset(INT1));  // open: Qn, preset, en
  D_Flip_Flop #(.trigger("rising"), .Pre_Clr_Positions("LEGACY"), .NegatePresetClear("false"), .enable("true"), .NewFFLayout("false")) d_ff_2 (
    .clk(IR2_t), .D(1'b1), .Q(d_ff_2_q), .reset(INT2));  // open: Qn, preset, en
  D_Flip_Flop #(.trigger("rising"), .Pre_Clr_Positions("LEGACY"), .NegatePresetClear("false"), .enable("true"), .NewFFLayout("false")) d_ff_3 (
    .clk(IR3_t), .D(1'b1), .Q(d_ff_3_q), .reset(INT3));  // open: Qn, preset, en
  Hex_Digit_Display hex_digit_display_6 (.value(LedData[11:8]));  // open: dp
  Hex_Digit_Display hex_digit_display_7 (.value(LedData[7:4]));  // open: dp
  // Probe on \总周期数 
  Button \u_复位信号  (.out(RST));
  or or_5 (or_5_out, d_ff_1_q, INT1);
  or or_6 (or_6_out, d_ff_2_q, INT2);
  or or_7 (or_7_out, d_ff_3_q, INT3);
  Hex_Digit_Display hex_digit_display_8 (.value(LedData[3:0]));  // open: dp
  and and_1 (and_1_out, or_5_out, ~Clr1);  // AND_Gate
  and and_2 (and_2_out, or_6_out, ~Clr2);  // AND_Gate
  and and_3 (and_3_out, or_7_out, ~Clr3);  // AND_Gate
  Adder #(.width(32)) adder_1 (.a(PC), .b(32'h4), .out({JmpAddr, PC_4}));  // open: cin, cout
  assign UnsignImm = {{16{1'b0}}, IR[15:0]};  // Bit_Extender bit_extender_1
  assign SignImm = {{16{IR[15]}}, IR[15:0]};  // Bit_Extender bit_extender_2
  and and_4 (and_4_out, beq, equal);
  not not_2 (not_2_out, equal);
  and and_5 (and_5_out, not_2_out, bne);
  D_Flip_Flop #(.trigger("rising"), .Pre_Clr_Positions("LEGACY"), .NegatePresetClear("false"), .enable("true"), .NewFFLayout("false")) u_IR1 (
    .clk(CLK), .D(and_1_out), .Q(INT1));  // open: Qn, preset, en, reset
  D_Flip_Flop #(.trigger("rising"), .Pre_Clr_Positions("LEGACY"), .NegatePresetClear("false"), .enable("true"), .NewFFLayout("false")) u_IR2 (
    .clk(CLK), .D(and_2_out), .Q(INT2));  // open: Qn, preset, en, reset
  D_Flip_Flop #(.trigger("rising"), .Pre_Clr_Positions("LEGACY"), .NegatePresetClear("false"), .enable("true"), .NewFFLayout("false")) u_IR3 (
    .clk(CLK), .D(and_3_out), .Q(INT3));  // open: Qn, preset, en, reset
  or or_8 (IR1_t, IR1, IRA);
  Shifter #(.width(32), .shift("ll")) shifter_1 (.in(SignImm), .\dist (5'b00010), .out(shifter_1_out));
  or or_9 (beq_bne, and_4_out, and_5_out);
  Multiplexer #(.select(3), .width(32), .disabled("Z"), .enable("false")) multiplexer_1 (
    .in0({JmpAddr, PC_4}), .in2({JmpAddr, IR[25:0], 2'b00}), .in3(R_rs), .in4(PC_4_Imm),
    .out(multiplexer_1_out), .sel({beq_bne, JMP, JR}));  // open: in1, in5, in6, in7
  // Probe on {beq_bne, JMP, JR}
  or or_10 (IR2_t, IR2, IRB);
  Adder #(.width(32)) adder_2 (.a({JmpAddr, PC_4}), .b(shifter_1_out), .out(PC_4_Imm));  // open: cin, cout
  or or_11 (or_11_out, Go, not_3_out);
  not not_3 (not_3_out, v0__34);
  Register #(.width(32), .trigger("rising"), .Select("low")) u_PC (
    .D(multiplexer_1_out), .en(or_11_out), .Q(PC), .clk(CLK), .clr(RST));
  or or_12 (IR3_t, IR3, IRC);
  Priority_Encoder #(.select(2), .disabled("Z")) priority_encoder_1 (
    .in1(INT1), .in2(INT2), .in3(INT3), .out(IntNo), .gs(IntR));  // open: in0, en_out, en_in
  ROM #(.addrWidth(10), .dataWidth(32), .Select("high")) rom_1 (.addr(PC[11:2]), .data(IR));
  // Probe on MDin
  Register #(.width(32), .trigger("rising"), .Select("low")) register_1 (
    .D(MDin), .en(v0__34_t), .Q(LedData), .clk(CLK), .clr(RST));
  Decoder #(.select(2), .tristate("false"), .disabled("Z"), .enable("true")) decoder_1 (
    .out1(Clr1), .out2(Clr2), .out3(Clr3), .sel(IntNo), .en(RST));  // open: out0
  // Mips_Probe mips_probe_1: pin names not known; wires that end beside it: IR, IR[31:26]
  Comparator #(.width(32), .mode("twosComplement")) comparator_5 (
    .a(R_rs), .b(32'h22), .eq(comparator_5_eq));  // open: gt, lt
  not not_4 (not_4_out, comparator_5_eq);
  and and_6 (v0__34_t, Syscall, comparator_5_eq);
  and and_7 (v0__34, Syscall, not_4_out);
  Multiplexer #(.select(2), .width(32), .disabled("Z"), .enable("false")) multiplexer_2 (
    .in0(32'h30ac), .in1(32'h3150), .in2(32'h31f4), .out(IntAddr), .sel(IntNo));  // open: in3
  Multiplexer #(.select(1), .width(5), .disabled("Z"), .enable("false")) multiplexer_3 (
    .in0(IR[20:16]), .in1(IR[15:11]), .out(multiplexer_3_out), .sel(RegDst));
  Multiplexer #(.select(1), .width(5), .disabled("Z"), .enable("false")) multiplexer_4 (
    .in0(IR[25:21]), .in1(5'b00010), .out(multiplexer_4_out), .sel(Syscall));
  Multiplexer #(.select(1), .width(5), .disabled("Z"), .enable("false")) multiplexer_5 (
    .in0(multiplexer_3_out), .in1({5{1'b1}}), .out(multiplexer_5_out), .sel(JAL));
  \单周期硬布线控制器  \u_单周期硬布线控制器_1  (
    .Func(IR[5:0]), .OP(IR[31:26]), .ALU_OP(\单周期硬布线控制器_1_alu_op ), .MemToReg(\单周期硬布线控制器_1_memtoreg ),
    .MemWrite(MemWrite), .ALU_SRC(\单周期硬布线控制器_1_alu_src [1]), .RegWrite(RegWrite), .SysCALL(Syscall),
    .SignedExt(SignedExt), .RegDst(RegDst), .JR(JR), .JMP(JMP), .Beq(beq), .JAL(JAL), .Bne(bne));
  Multiplexer #(.select(1), .width(5), .disabled("Z"), .enable("false")) multiplexer_6 (
    .in0(IR[20:16]), .in1(5'b00100), .out(multiplexer_6_out), .sel(Syscall));
  // Probe on multiplexer_6_out
  Multiplexer #(.select(1), .width(32), .disabled("Z"), .enable("false")) multiplexer_7 (
    .in0(multiplexer_9_out), .in1({JmpAddr, PC_4}), .out(RDin), .sel(JAL));
  MIPS_Regifile mips_regifile_1 (
    .Din(RDin), .Clk(CLK), .R1(R_rs), .R2(MDin), .WE(RegWrite), .W_num(multiplexer_5_out),
    .R1_num(multiplexer_4_out), .R2_num(multiplexer_6_out));
  D_Flip_Flop #(.trigger("rising"), .Pre_Clr_Positions("LEGACY"), .NegatePresetClear("false"), .enable("true"), .NewFFLayout("false")) d_ff_4 (
    .clk(CLK), .Q(d_ff_4_q), .reset(eret));  // open: D, Qn, preset, en
  MIPS_ALU mips_alu_1 (
    .X(R_rs), .Y(multiplexer_8_out), .AluOP(\单周期硬布线控制器_1_alu_op ), .Equal(equal), .Result(mips_alu_1_result),
    .shamt(IR[10:6]));  // open: Result_2
  Multiplexer #(.select(2), .width(32), .disabled("Z"), .enable("false")) multiplexer_8 (
    .in0(MDin), .in1(MDin), .in2(UnsignImm), .in3(SignImm), .out(multiplexer_8_out),
    .sel({\单周期硬布线控制器_1_alu_src [1], SignedExt}));
  and and_8 (\中断请求 , d_ff_4_q, IntR);
  RAM #(.addrWidth(10), .dataWidth(32), .bus("separate"), .Select("high")) ram_1 (
    .addr(mips_alu_1_result[11:2]), .din(MDin), .data(ram_1_data), .str(MemWrite), .clk(CLK), .clr(RST));  // open: sel, ld
  Multiplexer #(.select(1), .width(32), .disabled("Z"), .enable("false")) multiplexer_9 (
    .in0(mips_alu_1_result), .in1(ram_1_data), .out(multiplexer_9_out), .sel(\单周期硬布线控制器_1_memtoreg ));

  // Other names for the same wires on the sheet: a0[31:0] = MDin; Imm[15:0] = IR[15:0]; JmpAddr[27:2] = IR[25:0];
  //   shamt[4:0] = IR[10:6]; rd[4:0] = IR[15:11]; rt[4:0] = IR[20:16]; rs[4:0] = IR[25:21]; PC_4[31:28] = JmpAddr;
  //   v0[31:0] = R_rs

  // Notes on the sheet:
  //   中断源
  //   中断等待指示
  //   总复位信号应将除ROM以外所有存储组件全部清零
  //   单级中断测试信号模拟器
  //   数码管输出
  //   数码管输出应该用寄存器锁存，否则显示数据只能一闪而过
  //   指令存储器
  //   contents of rom_1 (hex, n*v repeats v):
  //   201d07d0 20100001 109fc0 139fc3 8021 2012000c 24160008 26100001 3210000f 20080008 20090001 139900
  //   2709825 132020 20020022 c 1094022 1500fff9 22100001 2018000f 2188024 108700 20080008 20090001 139902
  //   2709825 132021 20020022 c 1094022 1500fff9 108702 2c9b022 12c00001 8000c07 4020 1084027 84400
  //   3508ffff 82021 20020022 c 8000c01 afa20000 23bd0004 afa40000 23bd0004 afb00000 23bd0004 afb30000
  //   23bd0004 afb40000 23bd0004 afb50000 23bd0004 afb60000 23bd0004 20160001 20140003 20150001 168020
  //   108100 2149825 132020 20020022 c 1600fffa 295a022 1680fff7 23bdfffc 8fb60000 23bdfffc 8fb50000
  //   23bdfffc 8fb40000 23bdfffc 8fb30000 23bdfffc 8fb00000 23bdfffc 8fa40000 23bdfffc 8fa20000 42000018
  //   afa20000 23bd0004 afa40000 23bd0004 afb00000 23bd0004 afb30000 23bd0004 afb40000 23bd0004 afb50000
  //   23bd0004 afb60000 23bd0004 20160002 20140003 20150001 168020 108100 2149825 132020 20020022 c
  //   1600fffa 295a022 1680fff7 23bdfffc 8fb60000 23bdfffc 8fb50000 23bdfffc 8fb40000 23bdfffc 8fb30000
  //   23bdfffc 8fb00000 23bdfffc 8fa40000 23bdfffc 8fa20000 42000018 afa20000 23bd0004 afa40000 23bd0004
  //   afb00000 23bd0004 afb30000 23bd0004 afb40000 23bd0004 afb50000 23bd0004 afb60000 23bd0004 20160003
  //   20140003 20150001 168020 108100 2149825 132020 20020022 c 1600fffa 295a022 1680fff7 23bdfffc
  //   8fb60000 23bdfffc 8fb50000 23bdfffc 8fb40000 23bdfffc 8fb30000 23bdfffc 8fb00000 23bdfffc 8fa40000
  //   23bdfffc 8fa20000 42000018
  //   为方便自动评测，需要输出PC，IR，寄存器堆写如数据RDin
  //   OP
  //   Func
  //   rs
  //   指令字
  //   rt
  //   rd
  //   RAM写使能MemWrite、RAM写入数据MDin等信号
  //   JMP
  //   JR
  //   OP
  //   Func
  //   Beq
  //   Bne
  //   MemToReg
  //   MemWrite
  //   AluOP
  //   AluSrcB
  //   RegWrite
  //   JAL
  //   RegDst
  //   Syscall
endmodule

module \单周期MIPS_多级中断  (
  input  IR1,
  input  IR2,
  input  IR3,
  output RegWrite,
  output MemWrite,
  output [31:0] PC,
  output [31:0] IR,
  output [31:0] RDin,
  output [31:0] MDin,
  output [31:0] LedData
);

  wire CLK, comparator_1_eq, comparator_2_eq, comparator_3_eq, comparator_4_eq, comparator_5_eq, Go, IR1_t,
       IR2_t, IR3_t, IRA, IRB, IRC, or_1_out, or_2_out, W1, W2, W3;
  wire [15:0] \总周期数 ;

  Clock #(.highDuration(1), .lowDuration(1)) clock_1 (.out(CLK));
  Button _1 ();  // open: out
  Button _2 ();  // open: out
  Button _3 ();  // open: out
  Button \u_继续运行  (.out(Go));
  LED #(.active("true")) led_1 (.in(W1));
  LED #(.active("true")) led_2 (.in(W2));
  LED #(.active("true")) led_3 (.in(W3));
  Hex_Digit_Display hex_digit_display_1 (.value(LedData[31:28]));  // open: dp
  Comparator #(.width(16), .mode("twosComplement")) comparator_1 (
    .a(\总周期数 ), .b(16'h7), .eq(comparator_1_eq));  // open: gt, lt
  Comparator #(.width(16), .mode("twosComplement")) comparator_2 (
    .a(\总周期数 ), .b(16'h241), .eq(comparator_2_eq));  // open: gt, lt
  Hex_Digit_Display hex_digit_display_2 (.value(LedData[23:20]));  // open: dp
  Hex_Digit_Display hex_digit_display_3 (.value(LedData[27:24]));  // open: dp
  Comparator #(.width(16), .mode("twosComplement")) comparator_3 (
    .a(16'h258), .b(\总周期数 ), .eq(comparator_3_eq));  // open: gt, lt
  or or_1 (or_1_out, comparator_3_eq, comparator_4_eq);
  Comparator #(.width(16), .mode("twosComplement")) comparator_4 (
    .a(\总周期数 ), .b(16'h1), .eq(comparator_4_eq));  // open: gt, lt
  Comparator #(.width(16), .mode("twosComplement")) comparator_5 (
    .a(\总周期数 ), .b(16'h4), .eq(comparator_5_eq));  // open: gt, lt
  or or_2 (or_2_out, comparator_1_eq, comparator_2_eq);
  Hex_Digit_Display hex_digit_display_4 (.value(LedData[19:16]));  // open: dp
  Hex_Digit_Display hex_digit_display_5 (.value(LedData[15:12]));  // open: dp
  Pull_Resistor #(.pull(0)) pull_resistor_1 (.node(IRA));
  assign IRA = or_1_out ? ~CLK : 1'bz;  // Controlled_Inverter controlled_inverter_1
  Pull_Resistor #(.pull(0)) pull_resistor_2 (.node(IRB));
  assign IRB = comparator_5_eq ? ~CLK : 1'bz;  // Controlled_Inverter controlled_inverter_2
  Pull_Resistor #(.pull(0)) pull_resistor_3 (.node(IRC));
  assign IRC = or_2_out ? ~CLK : 1'bz;  // Controlled_Inverter controlled_inverter_3
  Hex_Digit_Display hex_digit_display_6 (.value(LedData[7:4]));  // open: dp
  Hex_Digit_Display hex_digit_display_7 (.value(LedData[11:8]));  // open: dp
  // Probe on \总周期数 
  Hex_Digit_Display hex_digit_display_8 (.value(LedData[3:0]));  // open: dp
  or or_3 (IR1_t, IR1, IRA);
  or or_4 (IR2_t, IR2, IRB);
  or or_5 (IR3_t, IR3, IRC);

  // Notes on the sheet:
  //   中断源
  //   中断等待指示
  //   总复位信号应将除ROM以外所有存储组件全部清零
  //   多级中断测试信号模拟器
  //   数码管输出
  //   数码管输出应该用寄存器锁存，否则显示数据只能一闪而过
  //   为方便自动评测，需要输出PC，IR，寄存器堆写如数据RDin
  //   RAM写使能MemWrite、RAM写入数据MDin等信号
endmodule

module \封装正确性测试  (
);

  wire IR1, IR2, IR3, MemW, RegW;
  wire [31:0] EX_PC, ID_PC, IF_PC, IR, LED, MDin, MDinr, MEM_PC, PC, RDin, RDinr, WB_PC;

  \单周期MIPS  \u_单周期mips_1  (
    .RegWrite(RegW), .MemWrite(MemW), .PC(PC), .IR(IR), .RDin(RDin), .MDin(MDin), .LedData(LED));  // open: IR1, IR2, IR3
  \气泡流水线  \u_气泡流水线_1  (
    .RegWrite(RegW), .MemWrite(MemW), .IF_PC(IF_PC), .ID_PC(ID_PC), .EX_PC(EX_PC), .M_PC(MEM_PC),
    .WB_PC(WB_PC), .RDin(RDinr), .MDin(MDinr), .LedData(LED));
  \单周期MIPS_单级中断  \u_单周期mips_单级中断_1  (
    .IR1(IR1), .IR2(IR2), .IR3(IR3), .RegWrite(RegW), .MemWrite(MemW), .PC(PC), .IR(IR), .RDin(RDin),
    .MDin(MDin), .LedData(LED));
  \理想流水线  \u_理想流水线_1  (
    .RegWrite(RegW), .MemWrite(MemW), .IF_PC(IF_PC), .ID_PC(ID_PC), .EX_PC(EX_PC), .M_PC(MEM_PC),
    .WB_PC(WB_PC), .RDin(RDinr), .MDin(MDinr), .LedData(LED));
  \重定向流水线  \u_重定向流水线_1  (
    .RegWrite(RegW), .MemWrite(MemW), .IF_PC(IF_PC), .ID_PC(ID_PC), .EX_PC(EX_PC), .M_PC(MEM_PC),
    .WB_PC(WB_PC), .RDin(RDinr), .MDin(MDinr), .LedData(LED));
  \单周期MIPS_多级中断  \u_单周期mips_多级中断_1  (
    .IR1(IR1), .IR2(IR2), .IR3(IR3), .RegWrite(RegW), .MemWrite(MemW), .PC(PC), .IR(IR), .RDin(RDin),
    .MDin(MDin), .LedData(LED));

  // Notes on the sheet:
  //   单周期封装测试
  //   气泡流水封装测试
  //   单周期+单级中断封装测试
  //   请检查上面封装有无位宽不匹配，引脚标签是否和连接的标签相对应，否则无法在educoder平台上正确测试
  //   理想流水封装测试
  //   重定向流水封装测试
  //   单周期+多级中断封装测试
endmodule

module IF_ID (
  input  [31:0] PC,
  input  [31:0] IR,
  input  [31:0] PC_4,
  input  \传输in ,
  input  CLK,
  input  \同步清零 ,
  input  \使能端 ,
  output [31:0] PC_2,
  output [31:0] IR_2,
  output [31:0] PC_4_2,
  output \传输out 
);

  wire multiplexer_4_out, not_1_out;
  wire [31:0] multiplexer_1_out, multiplexer_2_out, multiplexer_3_out;

  Multiplexer #(.select(1), .width(32), .disabled("Z"), .enable("false")) multiplexer_1 (
    .in0(PC), .in1({32{1'b0}}), .out(multiplexer_1_out), .sel(\同步清零 ));
  Multiplexer #(.select(1), .width(32), .disabled("Z"), .enable("false")) multiplexer_2 (
    .in0(IR), .in1({32{1'b0}}), .out(multiplexer_2_out), .sel(\同步清零 ));
  Multiplexer #(.select(1), .width(32), .disabled("Z"), .enable("false")) multiplexer_3 (
    .in0(PC_4), .in1({32{1'b0}}), .out(multiplexer_3_out), .sel(\同步清零 ));
  Multiplexer #(.select(1), .width(1), .disabled("Z"), .enable("false")) multiplexer_4 (
    .in0(\传输in ), .in1(1'b0), .out(multiplexer_4_out), .sel(\同步清零 ));
  Pull_Resistor #(.pull(0)) pull_resistor_1 (.node(\同步清零 ));
  not not_1 (not_1_out, \使能端 );
  Register #(.width(32), .trigger("rising"), .Select("low")) register_1 (
    .D(multiplexer_1_out), .en(not_1_out), .Q(PC_2), .clk(CLK));  // open: clr
  Register #(.width(32), .trigger("rising"), .Select("low")) register_2 (
    .D(multiplexer_2_out), .en(not_1_out), .Q(IR_2), .clk(CLK));  // open: clr
  Register #(.width(32), .trigger("rising"), .Select("low")) register_3 (
    .D(multiplexer_3_out), .en(not_1_out), .Q(PC_4_2), .clk(CLK));  // open: clr
  Register #(.width(1), .trigger("rising"), .Select("low")) register_4 (
    .D(multiplexer_4_out), .en(not_1_out), .Q(\传输out ), .clk(CLK));  // open: clr
  Pull_Resistor #(.pull(0)) pull_resistor_2 (.node(not_1_out));

  // Notes on the sheet:
  //   传输状态in，表明当前传输状态有效
  //   内部为组合逻辑电路
  //   同步清零，气泡，高电平有效
  //   IF/ID流水寄存器所存指令字中的OP和FUNCT字段
  //   输出为7个控制信号，其中RegDst为ID段使用，后面六个输出到ID/EX中
  //   使能端，低电平有效，stall，高电平有效
  //   传输状态out，表明当前传输状态有效
endmodule

module ID_EX (
  input  RegWrite,
  input  MemToReg,
  input  MemWrite,
  input  [3:0] AluOp,
  input  AluSrc,
  input  [31:0] IR,
  input  [31:0] \无符号拓展 ,
  input  SignExt,
  input  [31:0] PC_4,
  input  [31:0] PC,
  input  [31:0] RS,
  input  JMP,
  input  [31:0] RT,
  input  JAL,
  input  [4:0] WriteReg_num,
  input  JR,
  input  [31:0] \符号拓展 ,
  input  beq,
  input  Syscall,
  input  \传输in ,
  input  bne,
  input  CLK,
  input  \同步清零 ,
  input  \使能端 ,
  output RegWrite_2,
  output MemToReg_2,
  output MemWrite_2,
  output [3:0] AluOp_2,
  output AluSrc_2,
  output [31:0] IR_2,
  output [31:0] \无符号拓展_2 ,
  output SignExt_2,
  output [31:0] PC_4_2,
  output [31:0] PC_2,
  output [31:0] RS_2,
  output JMP_2,
  output [31:0] RT_2,
  output JAL_2,
  output [4:0] WriteReg_num_2,
  output JR_2,
  output [31:0] \符号拓展_2 ,
  output beq_2,
  output Syscall_2,
  output \传输out ,
  output bne_2
);

  wire multiplexer_1_out, multiplexer_2_out, multiplexer_3_out, multiplexer_5_out, multiplexer_12_out,
       multiplexer_14_out, multiplexer_16_out, multiplexer_17_out, multiplexer_18_out, multiplexer_19_out,
       multiplexer_20_out, multiplexer_21_out, pull_resistor_2_node;
  wire [3:0] multiplexer_4_out;
  wire [4:0] multiplexer_10_out;
  wire [31:0] multiplexer_6_out, multiplexer_7_out, multiplexer_8_out, multiplexer_9_out, multiplexer_11_out,
       multiplexer_13_out, multiplexer_15_out;

  Pull_Resistor #(.pull(0)) pull_resistor_1 (.node(\同步清零 ));
  Multiplexer #(.select(1), .width(1), .disabled("Z"), .enable("false")) multiplexer_1 (
    .in0(RegWrite), .in1(1'b0), .out(multiplexer_1_out), .sel(\同步清零 ));
  Multiplexer #(.select(1), .width(1), .disabled("Z"), .enable("false")) multiplexer_2 (
    .in0(MemToReg), .in1(1'b0), .out(multiplexer_2_out), .sel(\同步清零 ));
  Multiplexer #(.select(1), .width(1), .disabled("Z"), .enable("false")) multiplexer_3 (
    .in0(MemWrite), .in1(1'b0), .out(multiplexer_3_out), .sel(\同步清零 ));
  Multiplexer #(.select(1), .width(4), .disabled("Z"), .enable("false")) multiplexer_4 (
    .in0(AluOp), .in1(4'b0000), .out(multiplexer_4_out), .sel(\同步清零 ));
  Multiplexer #(.select(1), .width(1), .disabled("Z"), .enable("false")) multiplexer_5 (
    .in0(AluSrc), .in1(1'b0), .out(multiplexer_5_out), .sel(\同步清零 ));
  Multiplexer #(.select(1), .width(32), .disabled("Z"), .enable("false")) multiplexer_6 (
    .in0(\无符号拓展 ), .in1({32{1'b0}}), .out(multiplexer_6_out), .sel(\同步清零 ));
  Multiplexer #(.select(1), .width(32), .disabled("Z"), .enable("false")) multiplexer_7 (
    .in0(PC_4), .in1({32{1'b0}}), .out(multiplexer_7_out), .sel(\同步清零 ));
  Multiplexer #(.select(1), .width(32), .disabled("Z"), .enable("false")) multiplexer_8 (
    .in0(RS), .in1({32{1'b0}}), .out(multiplexer_8_out), .sel(\同步清零 ));
  Multiplexer #(.select(1), .width(32), .disabled("Z"), .enable("false")) multiplexer_9 (
    .in0(RT), .in1({32{1'b0}}), .out(multiplexer_9_out), .sel(\同步清零 ));
  Multiplexer #(.select(1), .width(5), .disabled("Z"), .enable("false")) multiplexer_10 (
    .in0(WriteReg_num), .in1({5{1'b0}}), .out(multiplexer_10_out), .sel(\同步清零 ));
  Multiplexer #(.select(1), .width(32), .disabled("Z"), .enable("false")) multiplexer_11 (
    .in0(\符号拓展 ), .in1({32{1'b0}}), .out(multiplexer_11_out), .sel(\同步清零 ));
  Multiplexer #(.select(1), .width(1), .disabled("Z"), .enable("false")) multiplexer_12 (
    .in0(\传输in ), .in1(1'b0), .out(multiplexer_12_out), .sel(\同步清零 ));
  Register #(.width(1), .trigger("rising"), .Select("low")) register_1 (
    .D(multiplexer_1_out), .en(pull_resistor_2_node), .Q(RegWrite_2), .clk(CLK));  // open: clr
  Register #(.width(1), .trigger("rising"), .Select("low")) register_2 (
    .D(multiplexer_2_out), .en(pull_resistor_2_node), .Q(MemToReg_2), .clk(CLK));  // open: clr
  Register #(.width(1), .trigger("rising"), .Select("low")) register_3 (
    .D(multiplexer_3_out), .en(pull_resistor_2_node), .Q(MemWrite_2), .clk(CLK));  // open: clr
  Register #(.width(4), .trigger("rising"), .Select("low")) register_4 (
    .D(multiplexer_4_out), .en(pull_resistor_2_node), .Q(AluOp_2), .clk(CLK));  // open: clr
  Register #(.width(1), .trigger("rising"), .Select("low")) register_5 (
    .D(multiplexer_5_out), .en(pull_resistor_2_node), .Q(AluSrc_2), .clk(CLK));  // open: clr
  Register #(.width(32), .trigger("rising"), .Select("low")) register_6 (
    .D(multiplexer_6_out), .en(pull_resistor_2_node), .Q(\无符号拓展_2 ), .clk(CLK));  // open: clr
  Register #(.width(32), .trigger("rising"), .Select("low")) register_7 (
    .D(multiplexer_7_out), .en(pull_resistor_2_node), .Q(PC_4_2), .clk(CLK));  // open: clr
  Register #(.width(32), .trigger("rising"), .Select("low")) register_8 (
    .D(multiplexer_8_out), .en(pull_resistor_2_node), .Q(RS_2), .clk(CLK));  // open: clr
  Register #(.width(32), .trigger("rising"), .Select("low")) register_9 (
    .D(multiplexer_9_out), .en(pull_resistor_2_node), .Q(RT_2), .clk(CLK));  // open: clr
  Register #(.width(5), .trigger("rising"), .Select("low")) register_10 (
    .D(multiplexer_10_out), .en(pull_resistor_2_node), .Q(WriteReg_num_2), .clk(CLK));  // open: clr
  Register #(.width(32), .trigger("rising"), .Select("low")) register_11 (
    .D(multiplexer_11_out), .en(pull_resistor_2_node), .Q(\符号拓展_2 ), .clk(CLK));  // open: clr
  Register #(.width(1), .trigger("rising"), .Select("low")) register_12 (
    .D(multiplexer_12_out), .en(pull_resistor_2_node), .Q(\传输out ), .clk(CLK));  // open: clr
  Pull_Resistor #(.pull(0)) pull_resistor_2 (.node(pull_resistor_2_node));
  not not_1 (pull_resistor_2_node, \使能端 );
  Multiplexer #(.select(1), .width(32), .disabled("Z"), .enable("false")) multiplexer_13 (
    .in0(IR), .in1({32{1'b0}}), .out(multiplexer_13_out), .sel(\同步清零 ));
  Multiplexer #(.select(1), .width(1), .disabled("Z"), .enable("false")) multiplexer_14 (
    .in0(SignExt), .in1(1'b0), .out(multiplexer_14_out), .sel(\同步清零 ));
  Multiplexer #(.select(1), .width(32), .disabled("Z"), .enable("false")) multiplexer_15 (
    .in0(PC), .in1({32{1'b0}}), .out(multiplexer_15_out), .sel(\同步清零 ));
  Multiplexer #(.select(1), .width(1), .disabled("Z"), .enable("false")) multiplexer_16 (
    .in0(JMP), .in1(1'b0), .out(multiplexer_16_out), .sel(\同步清零 ));
  Multiplexer #(.select(1), .width(1), .disabled("Z"), .enable("false")) multiplexer_17 (
    .in0(JAL), .in1(1'b0), .out(multiplexer_17_out), .sel(\同步清零 ));
  Multiplexer #(.select(1), .width(1), .disabled("Z"), .enable("false")) multiplexer_18 (
    .in0(JR), .in1(1'b0), .out(multiplexer_18_out), .sel(\同步清零 ));
  Multiplexer #(.select(1), .width(1), .disabled("Z"), .enable("false")) multiplexer_19 (
    .in0(beq), .in1(1'b0), .out(multiplexer_19_out), .sel(\同步清零 ));
  Multiplexer #(.select(1), .width(1), .disabled("Z"), .enable("false")) multiplexer_20 (
    .in0(bne), .in1(1'b0), .out(multiplexer_20_out), .sel(\同步清零 ));
  Register #(.width(32), .trigger("rising"), .Select("low")) register_13 (
    .D(multiplexer_13_out), .en(pull_resistor_2_node), .Q(IR_2), .clk(CLK));  // open: clr
  Register #(.width(1), .trigger("rising"), .Select("low")) register_14 (
    .D(multiplexer_14_out), .en(pull_resistor_2_node), .Q(SignExt_2), .clk(CLK));  // open: clr
  Register #(.width(32), .trigger("rising"), .Select("low")) register_15 (
    .D(multiplexer_15_out), .en(pull_resistor_2_node), .Q(PC_2), .clk(CLK));  // open: clr
  Register #(.width(1), .trigger("rising"), .Select("low")) register_16 (
    .D(multiplexer_16_out), .en(pull_resistor_2_node), .Q(JMP_2), .clk(CLK));  // open: clr
  Register #(.width(1), .trigger("rising"), .Select("low")) register_17 (
    .D(multiplexer_17_out), .en(pull_resistor_2_node), .Q(JAL_2), .clk(CLK));  // open: clr
  Register #(.width(1), .trigger("rising"), .Select("low")) register_18 (
    .D(multiplexer_18_out), .en(pull_resistor_2_node), .Q(JR_2), .clk(CLK));  // open: clr
  Register #(.width(1), .trigger("rising"), .Select("low")) register_19 (
    .D(multiplexer_19_out), .en(pull_resistor_2_node), .Q(beq_2), .clk(CLK));  // open: clr
  Register #(.width(1), .trigger("rising"), .Select("low")) register_20 (
    .D(multiplexer_20_out), .en(pull_resistor_2_node), .Q(bne_2), .clk(CLK));  // open: clr
  Multiplexer #(.select(1), .width(1), .disabled("Z"), .enable("false")) multiplexer_21 (
    .in0(Syscall), .in1(1'b0), .out(multiplexer_21_out), .sel(\同步清零 ));
  Register #(.width(1), .trigger("rising"), .Select("low")) register_21 (
    .D(multiplexer_21_out), .en(pull_resistor_2_node), .Q(Syscall_2), .clk(CLK));  // open: clr

  // Notes on the sheet:
  //   传输状态in，表明当前传输状态有效
  //   同步清零，气泡，高电平有效
  //   使能端，低电平有效，stall，高电平有效
  //   传输状态out，表明当前传输状态有效
endmodule

module EX_MEM (
  input  RegWrite,
  input  MemToReg,
  input  MemWrite,
  input  JAL,
  input  [31:0] PC_4,
  input  [31:0] AluResult,
  input  [31:0] v0,
  input  [31:0] WriteData,
  input  Syscall,
  input  [31:0] PC,
  input  [4:0] WriteReg_num,
  input  \传输in ,
  input  CLK,
  input  \同步清零 ,
  input  \使能端 ,
  output RegWrite_2,
  output MemToReg_2,
  output MemWrite_2,
  output JAL_2,
  output [31:0] PC_4_2,
  output [31:0] AluResult_2,
  output [31:0] v0_2,
  output [31:0] WriteData_2,
  output Syscall_2,
  output [31:0] PC_2,
  output [4:0] WriteReg_num_2,
  output \传输out 
);

  wire multiplexer_1_out, multiplexer_2_out, multiplexer_3_out, multiplexer_4_out, multiplexer_9_out,
       multiplexer_11_out, not_1_out;
  wire [4:0] multiplexer_8_out;
  wire [31:0] multiplexer_5_out, multiplexer_6_out, multiplexer_7_out, multiplexer_10_out, multiplexer_12_out;

  Multiplexer #(.select(1), .width(1), .disabled("Z"), .enable("false")) multiplexer_1 (
    .in0(RegWrite), .in1(1'b0), .out(multiplexer_1_out), .sel(\同步清零 ));
  Multiplexer #(.select(1), .width(1), .disabled("Z"), .enable("false")) multiplexer_2 (
    .in0(MemToReg), .in1(1'b0), .out(multiplexer_2_out), .sel(\同步清零 ));
  Multiplexer #(.select(1), .width(1), .disabled("Z"), .enable("false")) multiplexer_3 (
    .in0(MemWrite), .in1(1'b0), .out(multiplexer_3_out), .sel(\同步清零 ));
  Multiplexer #(.select(1), .width(1), .disabled("Z"), .enable("false")) multiplexer_4 (
    .in0(JAL), .in1(1'b0), .out(multiplexer_4_out), .sel(\同步清零 ));
  Multiplexer #(.select(1), .width(32), .disabled("Z"), .enable("false")) multiplexer_5 (
    .in0(PC_4), .in1({32{1'b0}}), .out(multiplexer_5_out), .sel(\同步清零 ));
  Multiplexer #(.select(1), .width(32), .disabled("Z"), .enable("false")) multiplexer_6 (
    .in0(AluResult), .in1({32{1'b0}}), .out(multiplexer_6_out), .sel(\同步清零 ));
  Multiplexer #(.select(1), .width(32), .disabled("Z"), .enable("false")) multiplexer_7 (
    .in0(WriteData), .in1({32{1'b0}}), .out(multiplexer_7_out), .sel(\同步清零 ));
  Multiplexer #(.select(1), .width(5), .disabled("Z"), .enable("false")) multiplexer_8 (
    .in0(WriteReg_num), .in1({5{1'b0}}), .out(multiplexer_8_out), .sel(\同步清零 ));
  Multiplexer #(.select(1), .width(1), .disabled("Z"), .enable("false")) multiplexer_9 (
    .in0(\传输in ), .in1(1'b0), .out(multiplexer_9_out), .sel(\同步清零 ));
  Pull_Resistor #(.pull(0)) pull_resistor_1 (.node(\同步清零 ));
  not not_1 (not_1_out, \使能端 );
  Register #(.width(1), .trigger("rising"), .Select("low")) register_1 (
    .D(multiplexer_1_out), .en(not_1_out), .Q(RegWrite_2), .clk(CLK));  // open: clr
  Register #(.width(1), .trigger("rising"), .Select("low")) register_2 (
    .D(multiplexer_2_out), .en(not_1_out), .Q(MemToReg_2), .clk(CLK));  // open: clr
  Register #(.width(1), .trigger("rising"), .Select("low")) register_3 (
    .D(multiplexer_3_out), .en(not_1_out), .Q(MemWrite_2), .clk(CLK));  // open: clr
  Register #(.width(1), .trigger("rising"), .Select("low")) register_4 (
    .D(multiplexer_4_out), .en(not_1_out), .Q(JAL_2), .clk(CLK));  // open: clr
  Register #(.width(32), .trigger("rising"), .Select("low")) register_5 (
    .D(multiplexer_5_out), .en(not_1_out), .Q(PC_4_2), .clk(CLK));  // open: clr
  Register #(.width(32), .trigger("rising"), .Select("low")) register_6 (
    .D(multiplexer_6_out), .en(not_1_out), .Q(AluResult_2), .clk(CLK));  // open: clr
  Register #(.width(32), .trigger("rising"), .Select("low")) register_7 (
    .D(multiplexer_7_out), .en(not_1_out), .Q(WriteData_2), .clk(CLK));  // open: clr
  Register #(.width(5), .trigger("rising"), .Select("low")) register_8 (
    .D(multiplexer_8_out), .en(not_1_out), .Q(WriteReg_num_2), .clk(CLK));  // open: clr
  Register #(.width(1), .trigger("rising"), .Select("low")) register_9 (
    .D(multiplexer_9_out), .en(not_1_out), .Q(\传输out ), .clk(CLK));  // open: clr
  Pull_Resistor #(.pull(0)) pull_resistor_2 (.node(not_1_out));
  Multiplexer #(.select(1), .width(32), .disabled("Z"), .enable("false")) multiplexer_10 (
    .in0(v0), .in1({32{1'b0}}), .out(multiplexer_10_out), .sel(\同步清零 ));
  Multiplexer #(.select(1), .width(1), .disabled("Z"), .enable("false")) multiplexer_11 (
    .in0(Syscall), .in1(1'b0), .out(multiplexer_11_out), .sel(\同步清零 ));
  Multiplexer #(.select(1), .width(32), .disabled("Z"), .enable("false")) multiplexer_12 (
    .in0(PC), .in1({32{1'b0}}), .out(multiplexer_12_out), .sel(\同步清零 ));
  Register #(.width(32), .trigger("rising"), .Select("low")) register_10 (
    .D(multiplexer_10_out), .en(not_1_out), .Q(v0_2), .clk(CLK));  // open: clr
  Register #(.width(1), .trigger("rising"), .Select("low")) register_11 (
    .D(multiplexer_11_out), .en(not_1_out), .Q(Syscall_2), .clk(CLK));  // open: clr
  Register #(.width(32), .trigger("rising"), .Select("low")) register_12 (
    .D(multiplexer_12_out), .en(not_1_out), .Q(PC_2), .clk(CLK));  // open: clr

  // Notes on the sheet:
  //   传输状态in，表明当前传输状态有效
  //   同步清零，气泡，高电平有效
  //   使能端，低电平有效，stall，高电平有效
  //   传输状态out，表明当前传输状态有效
endmodule

module MEM_WB (
  input  JAL,
  input  RegWrite,
  input  MemToReg,
  input  [4:0] WriteReg_num,
  input  [31:0] v0,
  input  [31:0] PC_4,
  input  [31:0] AluResult,
  input  Syscall,
  input  [31:0] RD,
  input  [31:0] PC,
  input  \传输in ,
  input  CLK,
  input  \同步清零 ,
  input  \使能端 ,
  output JAL_2,
  output RegWrite_2,
  output MemToReg_2,
  output [4:0] WriteReg_num_2,
  output [31:0] v0_2,
  output [31:0] PC_4_2,
  output [31:0] AluResult_2,
  output Syscall_2,
  output [31:0] RD_2,
  output [31:0] PC_2,
  output \传输out 
);

  wire multiplexer_1_out, multiplexer_2_out, multiplexer_3_out, multiplexer_8_out, multiplexer_10_out,
       not_1_out;
  wire [4:0] multiplexer_4_out;
  wire [31:0] multiplexer_5_out, multiplexer_6_out, multiplexer_7_out, multiplexer_9_out, multiplexer_11_out,
       undriven;

  Multiplexer #(.select(1), .width(1), .disabled("Z"), .enable("false")) multiplexer_1 (
    .in0(JAL), .in1(1'b0), .out(multiplexer_1_out), .sel(\同步清零 ));
  Multiplexer #(.select(1), .width(1), .disabled("Z"), .enable("false")) multiplexer_2 (
    .in0(RegWrite), .in1(1'b0), .out(multiplexer_2_out), .sel(\同步清零 ));
  Multiplexer #(.select(1), .width(1), .disabled("Z"), .enable("false")) multiplexer_3 (
    .in0(MemToReg), .in1(1'b0), .out(multiplexer_3_out), .sel(\同步清零 ));
  Multiplexer #(.select(1), .width(5), .disabled("Z"), .enable("false")) multiplexer_4 (
    .in0(WriteReg_num), .in1({5{1'b0}}), .out(multiplexer_4_out), .sel(\同步清零 ));
  Multiplexer #(.select(1), .width(32), .disabled("Z"), .enable("false")) multiplexer_5 (
    .in0(PC_4), .in1({32{1'b0}}), .out(multiplexer_5_out), .sel(\同步清零 ));
  Multiplexer #(.select(1), .width(32), .disabled("Z"), .enable("false")) multiplexer_6 (
    .in0(AluResult), .in1({32{1'b0}}), .out(multiplexer_6_out), .sel(\同步清零 ));
  Multiplexer #(.select(1), .width(32), .disabled("Z"), .enable("false")) multiplexer_7 (
    .in0(RD), .in1(undriven), .out(multiplexer_7_out), .sel(\同步清零 ));
  Multiplexer #(.select(1), .width(1), .disabled("Z"), .enable("false")) multiplexer_8 (
    .in0(\传输in ), .in1(1'b0), .out(multiplexer_8_out), .sel(\同步清零 ));
  Pull_Resistor #(.pull(0)) pull_resistor_1 (.node(\同步清零 ));
  not not_1 (not_1_out, \使能端 );
  Register #(.width(1), .trigger("rising"), .Select("low")) register_1 (
    .D(multiplexer_1_out), .en(not_1_out), .Q(JAL_2), .clk(CLK));  // open: clr
  Register #(.width(1), .trigger("rising"), .Select("low")) register_2 (
    .D(multiplexer_2_out), .en(not_1_out), .Q(RegWrite_2), .clk(CLK));  // open: clr
  Register #(.width(1), .trigger("rising"), .Select("low")) register_3 (
    .D(multiplexer_3_out), .en(not_1_out), .Q(MemToReg_2), .clk(CLK));  // open: clr
  Register #(.width(5), .trigger("rising"), .Select("low")) register_4 (
    .D(multiplexer_4_out), .en(not_1_out), .Q(WriteReg_num_2), .clk(CLK));  // open: clr
  Register #(.width(32), .trigger("rising"), .Select("low")) register_5 (
    .D(multiplexer_5_out), .en(not_1_out), .Q(PC_4_2), .clk(CLK));  // open: clr
  Register #(.width(32), .trigger("rising"), .Select("low")) register_6 (
    .D(multiplexer_6_out), .en(not_1_out), .Q(AluResult_2), .clk(CLK));  // open: clr
  Register #(.width(32), .trigger("rising"), .Select("low")) register_7 (
    .D(multiplexer_7_out), .en(not_1_out), .Q(RD_2), .clk(CLK));  // open: clr
  Register #(.width(1), .trigger("rising"), .Select("low")) register_8 (
    .D(multiplexer_8_out), .en(not_1_out), .Q(\传输out ), .clk(CLK));  // open: clr
  Pull_Resistor #(.pull(0)) pull_resistor_2 (.node(not_1_out));
  Multiplexer #(.select(1), .width(32), .disabled("Z"), .enable("false")) multiplexer_9 (
    .in0(v0), .in1({32{1'b0}}), .out(multiplexer_9_out), .sel(\同步清零 ));
  Multiplexer #(.select(1), .width(1), .disabled("Z"), .enable("false")) multiplexer_10 (
    .in0(Syscall), .in1(1'b0), .out(multiplexer_10_out), .sel(\同步清零 ));
  Multiplexer #(.select(1), .width(32), .disabled("Z"), .enable("false")) multiplexer_11 (
    .in0(PC), .in1({32{1'b0}}), .out(multiplexer_11_out), .sel(\同步清零 ));
  Register #(.width(32), .trigger("rising"), .Select("low")) register_9 (
    .D(multiplexer_9_out), .en(not_1_out), .Q(v0_2), .clk(CLK));  // open: clr
  Register #(.width(1), .trigger("rising"), .Select("low")) register_10 (
    .D(multiplexer_10_out), .en(not_1_out), .Q(Syscall_2), .clk(CLK));  // open: clr
  Register #(.width(32), .trigger("rising"), .Select("low")) register_11 (
    .D(multiplexer_11_out), .en(not_1_out), .Q(PC_2), .clk(CLK));  // open: clr

  // Notes on the sheet:
  //   传输状态in，表明当前传输状态有效
  //   同步清零，气泡，高电平有效
  //   使能端，低电平有效，stall，高电平有效
  //   传输状态out，表明当前传输状态有效
endmodule

module IF_ID_test (
  input  [31:0] IR,
  input  [31:0] PC,
  input  \传输in ,
  input  CLK,
  input  \同步清零 ,
  input  \使能端 ,
  output [31:0] IR_2,
  output [31:0] PC_2,
  output \传输out 
);

  wire multiplexer_3_out, not_1_out;
  wire [31:0] multiplexer_1_out, multiplexer_2_out;

  Multiplexer #(.select(1), .width(32), .disabled("Z"), .enable("false")) multiplexer_1 (
    .in0(IR), .in1({32{1'b0}}), .out(multiplexer_1_out), .sel(\同步清零 ));
  Multiplexer #(.select(1), .width(32), .disabled("Z"), .enable("false")) multiplexer_2 (
    .in0(PC), .in1({32{1'b0}}), .out(multiplexer_2_out), .sel(\同步清零 ));
  Multiplexer #(.select(1), .width(1), .disabled("Z"), .enable("false")) multiplexer_3 (
    .in0(\传输in ), .in1(1'b0), .out(multiplexer_3_out), .sel(\同步清零 ));
  Pull_Resistor #(.pull(0)) pull_resistor_1 (.node(\同步清零 ));
  not not_1 (not_1_out, \使能端 );
  Register #(.width(32), .trigger("rising"), .Select("low")) register_1 (
    .D(multiplexer_1_out), .en(not_1_out), .Q(IR_2), .clk(CLK));  // open: clr
  Register #(.width(32), .trigger("rising"), .Select("low")) register_2 (
    .D(multiplexer_2_out), .en(not_1_out), .Q(PC_2), .clk(CLK));  // open: clr
  Register #(.width(1), .trigger("rising"), .Select("low")) register_3 (
    .D(multiplexer_3_out), .en(not_1_out), .Q(\传输out ), .clk(CLK));  // open: clr
  Pull_Resistor #(.pull(0)) pull_resistor_2 (.node(not_1_out));

  // Notes on the sheet:
  //   传输状态in，表明当前传输状态有效
  //   内部为组合逻辑电路
  //   同步清零，气泡，高电平有效
  //   IF/ID流水寄存器所存指令字中的OP和FUNCT字段
  //   输出为7个控制信号，其中RegDst为ID段使用，后面六个输出到ID/EX中
  //   使能端，低电平有效，stall，高电平有效
  //   传输状态out，表明当前传输状态有效
endmodule

module ID_EX_test (
  input  RegWrite,
  input  MemToReg,
  input  MemWrite,
  input  [3:0] AluOp,
  input  AluSrc,
  input  [31:0] PC,
  input  [31:0] RS,
  input  JMP,
  input  [31:0] RT,
  input  JAL,
  input  [4:0] WriteReg_num,
  input  JR,
  input  [31:0] \符号拓展 ,
  input  beq,
  input  \传输in ,
  input  bne,
  input  CLK,
  input  \同步清零 ,
  input  \使能端 ,
  output RegWrite_2,
  output MemToReg_2,
  output MemWrite_2,
  output [3:0] AluOp_2,
  output AluSrc_2,
  output [31:0] PC_2,
  output [31:0] RS_2,
  output JMP_2,
  output [31:0] RT_2,
  output JAL_2,
  output [4:0] WriteReg_num_2,
  output JR_2,
  output [31:0] \符号拓展_2 ,
  output beq_2,
  output \传输out ,
  output bne_2
);

  wire multiplexer_1_out, multiplexer_2_out, multiplexer_3_out, multiplexer_5_out, multiplexer_11_out,
       multiplexer_12_out, multiplexer_13_out, multiplexer_14_out, multiplexer_15_out, multiplexer_16_out,
       pull_resistor_2_node;
  wire [3:0] multiplexer_4_out;
  wire [4:0] multiplexer_9_out;
  wire [31:0] multiplexer_6_out, multiplexer_7_out, multiplexer_8_out, multiplexer_10_out;

  Pull_Resistor #(.pull(0)) pull_resistor_1 (.node(\同步清零 ));
  Multiplexer #(.select(1), .width(1), .disabled("Z"), .enable("false")) multiplexer_1 (
    .in0(RegWrite), .in1(1'b0), .out(multiplexer_1_out), .sel(\同步清零 ));
  Multiplexer #(.select(1), .width(1), .disabled("Z"), .enable("false")) multiplexer_2 (
    .in0(MemToReg), .in1(1'b0), .out(multiplexer_2_out), .sel(\同步清零 ));
  Multiplexer #(.select(1), .width(1), .disabled("Z"), .enable("false")) multiplexer_3 (
    .in0(MemWrite), .in1(1'b0), .out(multiplexer_3_out), .sel(\同步清零 ));
  Multiplexer #(.select(1), .width(4), .disabled("Z"), .enable("false")) multiplexer_4 (
    .in0(AluOp), .in1(4'b0000), .out(multiplexer_4_out), .sel(\同步清零 ));
  Multiplexer #(.select(1), .width(1), .disabled("Z"), .enable("false")) multiplexer_5 (
    .in0(AluSrc), .in1(1'b0), .out(multiplexer_5_out), .sel(\同步清零 ));
  Multiplexer #(.select(1), .width(32), .disabled("Z"), .enable("false")) multiplexer_6 (
    .in0(PC), .in1({32{1'b0}}), .out(multiplexer_6_out), .sel(\同步清零 ));
  Multiplexer #(.select(1), .width(32), .disabled("Z"), .enable("false")) multiplexer_7 (
    .in0(RS), .in1({32{1'b0}}), .out(multiplexer_7_out), .sel(\同步清零 ));
  Multiplexer #(.select(1), .width(32), .disabled("Z"), .enable("false")) multiplexer_8 (
    .in0(RT), .in1({32{1'b0}}), .out(multiplexer_8_out), .sel(\同步清零 ));
  Multiplexer #(.select(1), .width(5), .disabled("Z"), .enable("false")) multiplexer_9 (
    .in0(WriteReg_num), .in1({5{1'b0}}), .out(multiplexer_9_out), .sel(\同步清零 ));
  Multiplexer #(.select(1), .width(32), .disabled("Z"), .enable("false")) multiplexer_10 (
    .in0(\符号拓展 ), .in1({32{1'b0}}), .out(multiplexer_10_out), .sel(\同步清零 ));
  Multiplexer #(.select(1), .width(1), .disabled("Z"), .enable("false")) multiplexer_11 (
    .in0(\传输in ), .in1(1'b0), .out(multiplexer_11_out), .sel(\同步清零 ));
  Register #(.width(1), .trigger("rising"), .Select("low")) register_1 (
    .D(multiplexer_1_out), .en(pull_resistor_2_node), .Q(RegWrite_2), .clk(CLK));  // open: clr
  Register #(.width(1), .trigger("rising"), .Select("low")) register_2 (
    .D(multiplexer_2_out), .en(pull_resistor_2_node), .Q(MemToReg_2), .clk(CLK));  // open: clr
  Register #(.width(1), .trigger("rising"), .Select("low")) register_3 (
    .D(multiplexer_3_out), .en(pull_resistor_2_node), .Q(MemWrite_2), .clk(CLK));  // open: clr
  Register #(.width(4), .trigger("rising"), .Select("low")) register_4 (
    .D(multiplexer_4_out), .en(pull_resistor_2_node), .Q(AluOp_2), .clk(CLK));  // open: clr
  Register #(.width(1), .trigger("rising"), .Select("low")) register_5 (
    .D(multiplexer_5_out), .en(pull_resistor_2_node), .Q(AluSrc_2), .clk(CLK));  // open: clr
  Register #(.width(32), .trigger("rising"), .Select("low")) register_6 (
    .D(multiplexer_6_out), .en(pull_resistor_2_node), .Q(PC_2), .clk(CLK));  // open: clr
  Register #(.width(32), .trigger("rising"), .Select("low")) register_7 (
    .D(multiplexer_7_out), .en(pull_resistor_2_node), .Q(RS_2), .clk(CLK));  // open: clr
  Register #(.width(32), .trigger("rising"), .Select("low")) register_8 (
    .D(multiplexer_8_out), .en(pull_resistor_2_node), .Q(RT_2), .clk(CLK));  // open: clr
  Register #(.width(5), .trigger("rising"), .Select("low")) register_9 (
    .D(multiplexer_9_out), .en(pull_resistor_2_node), .Q(WriteReg_num_2), .clk(CLK));  // open: clr
  Register #(.width(32), .trigger("rising"), .Select("low")) register_10 (
    .D(multiplexer_10_out), .en(pull_resistor_2_node), .Q(\符号拓展_2 ), .clk(CLK));  // open: clr
  Register #(.width(1), .trigger("rising"), .Select("low")) register_11 (
    .D(multiplexer_11_out), .en(pull_resistor_2_node), .Q(\传输out ), .clk(CLK));  // open: clr
  Pull_Resistor #(.pull(0)) pull_resistor_2 (.node(pull_resistor_2_node));
  not not_1 (pull_resistor_2_node, \使能端 );
  Multiplexer #(.select(1), .width(1), .disabled("Z"), .enable("false")) multiplexer_12 (
    .in0(JMP), .in1(1'b0), .out(multiplexer_12_out), .sel(\同步清零 ));
  Multiplexer #(.select(1), .width(1), .disabled("Z"), .enable("false")) multiplexer_13 (
    .in0(JAL), .in1(1'b0), .out(multiplexer_13_out), .sel(\同步清零 ));
  Multiplexer #(.select(1), .width(1), .disabled("Z"), .enable("false")) multiplexer_14 (
    .in0(JR), .in1(1'b0), .out(multiplexer_14_out), .sel(\同步清零 ));
  Multiplexer #(.select(1), .width(1), .disabled("Z"), .enable("false")) multiplexer_15 (
    .in0(beq), .in1(1'b0), .out(multiplexer_15_out), .sel(\同步清零 ));
  Multiplexer #(.select(1), .width(1), .disabled("Z"), .enable("false")) multiplexer_16 (
    .in0(bne), .in1(1'b0), .out(multiplexer_16_out), .sel(\同步清零 ));
  Register #(.width(1), .trigger("rising"), .Select("low")) register_12 (
    .D(multiplexer_12_out), .en(pull_resistor_2_node), .Q(JMP_2), .clk(CLK));  // open: clr
  Register #(.width(1), .trigger("rising"), .Select("low")) register_13 (
    .D(multiplexer_13_out), .en(pull_resistor_2_node), .Q(JAL_2), .clk(CLK));  // open: clr
  Register #(.width(1), .trigger("rising"), .Select("low")) register_14 (
    .D(multiplexer_14_out), .en(pull_resistor_2_node), .Q(JR_2));  // open: clk, clr
  Register #(.width(1), .trigger("rising"), .Select("low")) register_15 (
    .D(multiplexer_15_out), .en(pull_resistor_2_node), .Q(beq_2), .clk(CLK));  // open: clr
  Register #(.width(1), .trigger("rising"), .Select("low")) register_16 (
    .D(multiplexer_16_out), .en(pull_resistor_2_node), .Q(bne_2), .clk(CLK));  // open: clr

  // Notes on the sheet:
  //   传输状态in，表明当前传输状态有效
  //   同步清零，气泡，高电平有效
  //   使能端，低电平有效，stall，高电平有效
  //   传输状态out，表明当前传输状态有效
endmodule

module EX_MEM_TEST (
  input  RegWrite,
  input  MemToReg,
  input  MemWrite,
  input  [5:0] OP,
  input  [31:0] PC,
  input  [31:0] AluResult,
  input  [31:0] WriteData,
  input  [5:0] FUNCT,
  input  [4:0] WriteReg_num,
  input  \传输in ,
  input  CLK,
  input  \同步清零 ,
  input  \使能端 ,
  output RegWrite_2,
  output MemToReg_2,
  output MemWrite_2,
  output [31:0] PC_2,
  output [31:0] AluResult_2,
  output [31:0] WriteData_2,
  output [4:0] WriteReg_num_2,
  output \传输out 
);

  wire multiplexer_1_out, multiplexer_2_out, multiplexer_3_out, multiplexer_8_out, not_1_out;
  wire [4:0] multiplexer_7_out;
  wire [31:0] multiplexer_4_out, multiplexer_5_out, multiplexer_6_out;

  Multiplexer #(.select(1), .width(1), .disabled("Z"), .enable("false")) multiplexer_1 (
    .in0(RegWrite), .in1(1'b0), .out(multiplexer_1_out), .sel(\同步清零 ));
  Multiplexer #(.select(1), .width(1), .disabled("Z"), .enable("false")) multiplexer_2 (
    .in0(MemToReg), .in1(1'b0), .out(multiplexer_2_out), .sel(\同步清零 ));
  Multiplexer #(.select(1), .width(1), .disabled("Z"), .enable("false")) multiplexer_3 (
    .in0(MemWrite), .in1(1'b0), .out(multiplexer_3_out), .sel(\同步清零 ));
  Multiplexer #(.select(1), .width(32), .disabled("Z"), .enable("false")) multiplexer_4 (
    .in0(PC), .in1({32{1'b0}}), .out(multiplexer_4_out), .sel(\同步清零 ));
  Multiplexer #(.select(1), .width(32), .disabled("Z"), .enable("false")) multiplexer_5 (
    .in0(AluResult), .in1({32{1'b0}}), .out(multiplexer_5_out), .sel(\同步清零 ));
  Multiplexer #(.select(1), .width(32), .disabled("Z"), .enable("false")) multiplexer_6 (
    .in0(WriteData), .in1({32{1'b0}}), .out(multiplexer_6_out), .sel(\同步清零 ));
  Multiplexer #(.select(1), .width(5), .disabled("Z"), .enable("false")) multiplexer_7 (
    .in0(WriteReg_num), .in1({5{1'b0}}), .out(multiplexer_7_out), .sel(\同步清零 ));
  Multiplexer #(.select(1), .width(1), .disabled("Z"), .enable("false")) multiplexer_8 (
    .in0(\传输in ), .in1(1'b0), .out(multiplexer_8_out), .sel(\同步清零 ));
  Pull_Resistor #(.pull(0)) pull_resistor_1 (.node(\同步清零 ));
  not not_1 (not_1_out, \使能端 );
  Register #(.width(1), .trigger("rising"), .Select("low")) register_1 (
    .D(multiplexer_1_out), .en(not_1_out), .Q(RegWrite_2), .clk(CLK));  // open: clr
  Register #(.width(1), .trigger("rising"), .Select("low")) register_2 (
    .D(multiplexer_2_out), .en(not_1_out), .Q(MemToReg_2), .clk(CLK));  // open: clr
  Register #(.width(1), .trigger("rising"), .Select("low")) register_3 (
    .D(multiplexer_3_out), .en(not_1_out), .Q(MemWrite_2), .clk(CLK));  // open: clr
  Register #(.width(32), .trigger("rising"), .Select("low")) register_4 (
    .D(multiplexer_4_out), .en(not_1_out), .Q(PC_2), .clk(CLK));  // open: clr
  Register #(.width(32), .trigger("rising"), .Select("low")) register_5 (
    .D(multiplexer_5_out), .en(not_1_out), .Q(AluResult_2), .clk(CLK));  // open: clr
  Register #(.width(32), .trigger("rising"), .Select("low")) register_6 (
    .D(multiplexer_6_out), .en(not_1_out), .Q(WriteData_2), .clk(CLK));  // open: clr
  Register #(.width(5), .trigger("rising"), .Select("low")) register_7 (
    .D(multiplexer_7_out), .en(not_1_out), .Q(WriteReg_num_2), .clk(CLK));  // open: clr
  Register #(.width(1), .trigger("rising"), .Select("low")) register_8 (
    .D(multiplexer_8_out), .en(not_1_out), .Q(\传输out ), .clk(CLK));  // open: clr
  Pull_Resistor #(.pull(0)) pull_resistor_2 (.node(not_1_out));

  // Notes on the sheet:
  //   传输状态in，表明当前传输状态有效
  //   同步清零，气泡，高电平有效
  //   使能端，低电平有效，stall，高电平有效
  //   传输状态out，表明当前传输状态有效
endmodule

module R1_R2_USED (
  input  OP0,
  input  OP1,
  input  OP2,
  input  OP3,
  input  OP4,
  input  OP5,
  input  F0,
  input  F1,
  input  F2,
  input  F3,
  input  F4,
  input  F5,
  output R1_USED,
  output R2_USED
);

  wire and_1_out, and_2_out, and_3_out, and_4_out, and_5_out, and_6_out, and_7_out, and_8_out, and_9_out,
       and_10_out, and_11_out, and_12_out, and_13_out, and_14_out, and_15_out, and_16_out, and_17_out,
       and_18_out, and_19_out, and_20_out, and_21_out, and_22_out, and_23_out, and_24_out, and_25_out,
       and_26_out, and_27_out, and_28_out, and_29_out, and_30_out, and_31_out, and_32_out, and_33_out,
       and_34_out, not_1_out, not_2_out, not_3_out, not_4_out, not_5_out, not_6_out, not_7_out, not_8_out,
       not_9_out, not_10_out, not_11_out, not_12_out, not_13_out, not_14_out, not_15_out, not_16_out,
       not_17_out, not_18_out, not_19_out, not_20_out, not_21_out, not_22_out, not_23_out, not_24_out,
       not_25_out, not_26_out, not_27_out, not_28_out, not_29_out, not_30_out, not_31_out, not_32_out,
       not_33_out, not_34_out, not_35_out, not_36_out, not_37_out, not_38_out, not_39_out, not_40_out,
       not_41_out, not_42_out, not_43_out, not_44_out, not_45_out, not_46_out, not_47_out, not_48_out,
       not_49_out, not_50_out, not_51_out, not_52_out, not_53_out, not_54_out, not_55_out, not_56_out,
       not_57_out, not_58_out, not_59_out, not_60_out, not_61_out, not_62_out, not_63_out, not_64_out,
       not_65_out, not_66_out, not_67_out, not_68_out, not_69_out, not_70_out, not_71_out, not_72_out,
       not_73_out, not_74_out, not_75_out, not_76_out, not_77_out, not_78_out, not_79_out, not_80_out,
       not_81_out, not_82_out, not_83_out, not_84_out, not_85_out, not_86_out, not_87_out, not_88_out,
       not_89_out, not_90_out, not_91_out, not_92_out, not_93_out, not_94_out, not_95_out, not_96_out,
       not_97_out, not_98_out, not_99_out, not_100_out, not_101_out, not_102_out, not_103_out, not_104_out,
       not_105_out, not_106_out, not_107_out, not_108_out, not_109_out, not_110_out, not_111_out,
       not_112_out, not_113_out, not_114_out, not_115_out, not_116_out, not_117_out, not_118_out,
       not_119_out, not_120_out, not_121_out, not_122_out, not_123_out, not_124_out, not_125_out,
       not_126_out, not_127_out, not_128_out, not_129_out, not_130_out, not_131_out, not_132_out,
       not_133_out, not_134_out, not_135_out, not_136_out, not_137_out, not_138_out, not_139_out,
       not_140_out, not_141_out, not_142_out, not_143_out, not_144_out, not_145_out, not_146_out,
       not_147_out, not_148_out, not_149_out, not_150_out, not_151_out, not_152_out, not_153_out,
       not_154_out, not_155_out, not_156_out, not_157_out, not_158_out, not_159_out, not_160_out,
       not_161_out, not_162_out, not_163_out, not_164_out, not_165_out, not_166_out, not_167_out,
       not_168_out, not_169_out, not_170_out, not_171_out, not_172_out, not_173_out, not_174_out,
       not_175_out, not_176_out, not_177_out, not_178_out, not_179_out, not_180_out, not_181_out,
       not_182_out, not_183_out, not_184_out, not_185_out, not_186_out, not_187_out, not_188_out,
       not_189_out, not_190_out, not_191_out, not_192_out, not_193_out, not_194_out, not_195_out,
       not_196_out, not_197_out, not_198_out, not_199_out, not_200_out, not_201_out, not_202_out,
       not_203_out, not_204_out, not_205_out, not_206_out, not_207_out, not_208_out, not_209_out,
       not_210_out, not_211_out, not_212_out, not_213_out, not_214_out, not_215_out, not_216_out,
       not_217_out, not_218_out, not_219_out, not_220_out, not_221_out, not_222_out, not_223_out,
       not_224_out, not_225_out, not_226_out, not_227_out, not_228_out, not_229_out, not_230_out,
       not_231_out, not_232_out, not_233_out, not_234_out, not_235_out, not_236_out, not_237_out,
       not_238_out, not_239_out, not_240_out, not_241_out, not_242_out, not_243_out, not_244_out,
       not_245_out, not_246_out, not_247_out, not_248_out, not_249_out, not_250_out, not_251_out,
       not_252_out, not_253_out, not_254_out, not_255_out, not_256_out, not_257_out, not_258_out, not_259_out;

  not not_1 (not_1_out, OP5);
  not not_2 (not_2_out, OP4);
  not not_3 (not_3_out, OP3);
  not not_4 (not_4_out, OP2);
  not not_5 (not_5_out, OP1);
  not not_6 (not_6_out, OP0);
  not not_7 (not_7_out, F4);
  not not_8 (not_8_out, F3);
  not not_9 (not_9_out, F2);
  not not_10 (not_10_out, F1);
  not not_11 (not_11_out, F0);
  not not_12 (not_12_out, OP5);
  not not_13 (not_13_out, OP4);
  not not_14 (not_14_out, OP3);
  not not_15 (not_15_out, OP2);
  not not_16 (not_16_out, OP1);
  not not_17 (not_17_out, OP0);
  not not_18 (not_18_out, F4);
  not not_19 (not_19_out, F3);
  not not_20 (not_20_out, F2);
  not not_21 (not_21_out, F1);
  not not_22 (not_22_out, OP5);
  not not_23 (not_23_out, OP4);
  not not_24 (not_24_out, OP3);
  not not_25 (not_25_out, OP2);
  not not_26 (not_26_out, OP1);
  not not_27 (not_27_out, OP0);
  not not_28 (not_28_out, F4);
  not not_29 (not_29_out, F3);
  not not_30 (not_30_out, F2);
  not not_31 (not_31_out, F0);
  not not_32 (not_32_out, OP5);
  not not_33 (not_33_out, OP4);
  not not_34 (not_34_out, OP3);
  not not_35 (not_35_out, OP2);
  not not_36 (not_36_out, OP1);
  not not_37 (not_37_out, OP0);
  not not_38 (not_38_out, F4);
  not not_39 (not_39_out, F3);
  not not_40 (not_40_out, F1);
  not not_41 (not_41_out, F0);
  not not_42 (not_42_out, OP5);
  not not_43 (not_43_out, OP4);
  not not_44 (not_44_out, OP3);
  not not_45 (not_45_out, OP2);
  not not_46 (not_46_out, OP1);
  not not_47 (not_47_out, OP0);
  not not_48 (not_48_out, F4);
  not not_49 (not_49_out, F3);
  not not_50 (not_50_out, F1);
  not not_51 (not_51_out, OP5);
  not not_52 (not_52_out, OP4);
  not not_53 (not_53_out, OP3);
  not not_54 (not_54_out, OP2);
  not not_55 (not_55_out, OP1);
  not not_56 (not_56_out, OP0);
  not not_57 (not_57_out, F4);
  not not_58 (not_58_out, F3);
  not not_59 (not_59_out, OP5);
  not not_60 (not_60_out, OP4);
  not not_61 (not_61_out, OP3);
  not not_62 (not_62_out, OP2);
  not not_63 (not_63_out, OP1);
  not not_64 (not_64_out, OP0);
  not not_65 (not_65_out, F4);
  not not_66 (not_66_out, F2);
  not not_67 (not_67_out, F0);
  not not_68 (not_68_out, OP5);
  not not_69 (not_69_out, OP4);
  not not_70 (not_70_out, OP3);
  not not_71 (not_71_out, OP2);
  not not_72 (not_72_out, OP1);
  not not_73 (not_73_out, OP0);
  not not_74 (not_74_out, F4);
  not not_75 (not_75_out, F2);
  not not_76 (not_76_out, OP5);
  not not_77 (not_77_out, OP4);
  not not_78 (not_78_out, OP3);
  not not_79 (not_79_out, OP2);
  not not_80 (not_80_out, OP1);
  not not_81 (not_81_out, OP0);
  not not_82 (not_82_out, F5);
  not not_83 (not_83_out, F4);
  not not_84 (not_84_out, F2);
  not not_85 (not_85_out, F1);
  not not_86 (not_86_out, F0);
  not not_87 (not_87_out, OP5);
  not not_88 (not_88_out, OP4);
  not not_89 (not_89_out, OP3);
  not not_90 (not_90_out, OP2);
  not not_91 (not_91_out, OP1);
  not not_92 (not_92_out, OP0);
  not not_93 (not_93_out, F5);
  not not_94 (not_94_out, F4);
  not not_95 (not_95_out, F1);
  not not_96 (not_96_out, F0);
  not not_97 (not_97_out, OP5);
  not not_98 (not_98_out, OP4);
  not not_99 (not_99_out, OP3);
  not not_100 (not_100_out, OP1);
  not not_101 (not_101_out, OP0);
  not not_102 (not_102_out, OP5);
  not not_103 (not_103_out, OP4);
  not not_104 (not_104_out, OP3);
  not not_105 (not_105_out, OP1);
  not not_106 (not_106_out, OP5);
  not not_107 (not_107_out, OP4);
  not not_108 (not_108_out, OP2);
  not not_109 (not_109_out, OP1);
  not not_110 (not_110_out, OP0);
  not not_111 (not_111_out, OP5);
  not not_112 (not_112_out, OP4);
  not not_113 (not_113_out, OP1);
  not not_114 (not_114_out, OP0);
  not not_115 (not_115_out, OP5);
  not not_116 (not_116_out, OP4);
  not not_117 (not_117_out, OP2);
  not not_118 (not_118_out, OP1);
  not not_119 (not_119_out, OP5);
  not not_120 (not_120_out, OP4);
  not not_121 (not_121_out, OP2);
  not not_122 (not_122_out, OP0);
  not not_123 (not_123_out, OP5);
  not not_124 (not_124_out, OP4);
  not not_125 (not_125_out, OP1);
  not not_126 (not_126_out, OP4);
  not not_127 (not_127_out, OP3);
  not not_128 (not_128_out, OP2);
  not not_129 (not_129_out, OP4);
  not not_130 (not_130_out, OP2);
  not not_131 (not_131_out, OP5);
  not not_132 (not_132_out, OP4);
  not not_133 (not_133_out, OP3);
  not not_134 (not_134_out, OP2);
  not not_135 (not_135_out, OP1);
  not not_136 (not_136_out, OP0);
  not not_137 (not_137_out, F5);
  not not_138 (not_138_out, F4);
  not not_139 (not_139_out, F3);
  not not_140 (not_140_out, F2);
  not not_141 (not_141_out, F1);
  not not_142 (not_142_out, F0);
  not not_143 (not_143_out, OP5);
  not not_144 (not_144_out, OP4);
  not not_145 (not_145_out, OP3);
  not not_146 (not_146_out, OP2);
  not not_147 (not_147_out, OP1);
  not not_148 (not_148_out, OP0);
  not not_149 (not_149_out, F5);
  not not_150 (not_150_out, F4);
  not not_151 (not_151_out, F3);
  not not_152 (not_152_out, F2);
  not not_153 (not_153_out, OP5);
  not not_154 (not_154_out, OP4);
  not not_155 (not_155_out, OP3);
  not not_156 (not_156_out, OP2);
  not not_157 (not_157_out, OP1);
  not not_158 (not_158_out, OP0);
  not not_159 (not_159_out, F5);
  not not_160 (not_160_out, F4);
  not not_161 (not_161_out, F3);
  not not_162 (not_162_out, F2);
  not not_163 (not_163_out, F0);
  not not_164 (not_164_out, OP5);
  not not_165 (not_165_out, OP4);
  not not_166 (not_166_out, OP3);
  not not_167 (not_167_out, OP2);
  not not_168 (not_168_out, OP1);
  not not_169 (not_169_out, OP0);
  not not_170 (not_170_out, F4);
  not not_171 (not_171_out, F3);
  not not_172 (not_172_out, F2);
  not not_173 (not_173_out, F1);
  not not_174 (not_174_out, F0);
  not not_175 (not_175_out, OP5);
  not not_176 (not_176_out, OP4);
  not not_177 (not_177_out, OP3);
  not not_178 (not_178_out, OP2);
  not not_179 (not_179_out, OP1);
  not not_180 (not_180_out, OP0);
  not not_181 (not_181_out, F4);
  not not_182 (not_182_out, F3);
  not not_183 (not_183_out, F2);
  not not_184 (not_184_out, F1);
  not not_185 (not_185_out, OP5);
  not not_186 (not_186_out, OP4);
  not not_187 (not_187_out, OP3);
  not not_188 (not_188_out, OP2);
  not not_189 (not_189_out, OP1);
  not not_190 (not_190_out, OP0);
  not not_191 (not_191_out, F4);
  not not_192 (not_192_out, F3);
  not not_193 (not_193_out, F2);
  not not_194 (not_194_out, F0);
  not not_195 (not_195_out, OP5);
  not not_196 (not_196_out, OP4);
  not not_197 (not_197_out, OP3);
  not not_198 (not_198_out, OP2);
  not not_199 (not_199_out, OP1);
  not not_200 (not_200_out, OP0);
  not not_201 (not_201_out, F4);
  not not_202 (not_202_out, F3);
  not not_203 (not_203_out, F1);
  not not_204 (not_204_out, F0);
  not not_205 (not_205_out, OP5);
  not not_206 (not_206_out, OP4);
  not not_207 (not_207_out, OP3);
  not not_208 (not_208_out, OP2);
  not not_209 (not_209_out, OP1);
  not not_210 (not_210_out, OP0);
  not not_211 (not_211_out, F4);
  not not_212 (not_212_out, F3);
  not not_213 (not_213_out, F1);
  not not_214 (not_214_out, OP5);
  not not_215 (not_215_out, OP4);
  not not_216 (not_216_out, OP3);
  not not_217 (not_217_out, OP2);
  not not_218 (not_218_out, OP1);
  not not_219 (not_219_out, OP0);
  not not_220 (not_220_out, F4);
  not not_221 (not_221_out, F3);
  not not_222 (not_222_out, OP5);
  not not_223 (not_223_out, OP4);
  not not_224 (not_224_out, OP3);
  not not_225 (not_225_out, OP2);
  not not_226 (not_226_out, OP1);
  not not_227 (not_227_out, OP0);
  not not_228 (not_228_out, F4);
  not not_229 (not_229_out, F2);
  not not_230 (not_230_out, F0);
  not not_231 (not_231_out, OP5);
  not not_232 (not_232_out, OP4);
  not not_233 (not_233_out, OP3);
  not not_234 (not_234_out, OP2);
  not not_235 (not_235_out, OP1);
  not not_236 (not_236_out, OP0);
  not not_237 (not_237_out, F4);
  not not_238 (not_238_out, F2);
  not not_239 (not_239_out, OP5);
  not not_240 (not_240_out, OP4);
  not not_241 (not_241_out, OP3);
  not not_242 (not_242_out, OP2);
  not not_243 (not_243_out, OP1);
  not not_244 (not_244_out, OP0);
  not not_245 (not_245_out, F5);
  not not_246 (not_246_out, F4);
  not not_247 (not_247_out, F1);
  not not_248 (not_248_out, F0);
  not not_249 (not_249_out, OP5);
  not not_250 (not_250_out, OP4);
  not not_251 (not_251_out, OP3);
  not not_252 (not_252_out, OP1);
  not not_253 (not_253_out, OP0);
  not not_254 (not_254_out, OP5);
  not not_255 (not_255_out, OP4);
  not not_256 (not_256_out, OP3);
  not not_257 (not_257_out, OP1);
  not not_258 (not_258_out, OP4);
  not not_259 (not_259_out, OP2);
  and and_1 (and_1_out, not_1_out, not_2_out, not_3_out, not_4_out, not_5_out, not_6_out, F5, not_7_out, not_8_out, not_9_out, not_10_out, not_11_out);
  and and_2 (and_2_out, not_12_out, not_13_out, not_14_out, not_15_out, not_16_out, not_17_out, F5, not_18_out, not_19_out, not_20_out, not_21_out, F0);
  and and_3 (and_3_out, not_22_out, not_23_out, not_24_out, not_25_out, not_26_out, not_27_out, F5, not_28_out, not_29_out, not_30_out, F1, not_31_out);
  and and_4 (and_4_out, not_32_out, not_33_out, not_34_out, not_35_out, not_36_out, not_37_out, F5, not_38_out, not_39_out, F2, not_40_out, not_41_out);
  and and_5 (and_5_out, not_42_out, not_43_out, not_44_out, not_45_out, not_46_out, not_47_out, F5, not_48_out, not_49_out, F2, not_50_out, F0);
  and and_6 (and_6_out, not_51_out, not_52_out, not_53_out, not_54_out, not_55_out, not_56_out, F5, not_57_out, not_58_out, F2, F1, F0);
  and and_7 (and_7_out, not_59_out, not_60_out, not_61_out, not_62_out, not_63_out, not_64_out, F5, not_65_out, F3, not_66_out, F1, not_67_out);
  and and_8 (and_8_out, not_68_out, not_69_out, not_70_out, not_71_out, not_72_out, not_73_out, F5, not_74_out, F3, not_75_out, F1, F0);
  and and_9 (and_9_out, not_76_out, not_77_out, not_78_out, not_79_out, not_80_out, not_81_out, not_82_out, not_83_out, F3, not_84_out, not_85_out, not_86_out);
  and and_10 (and_10_out, not_87_out, not_88_out, not_89_out, not_90_out, not_91_out, not_92_out, not_93_out, not_94_out, F3, F2, not_95_out, not_96_out);
  and and_11 (and_11_out, not_97_out, not_98_out, not_99_out, OP2, not_100_out, not_101_out);
  and and_12 (and_12_out, not_102_out, not_103_out, not_104_out, OP2, not_105_out, OP0);
  and and_13 (and_13_out, not_106_out, not_107_out, OP3, not_108_out, not_109_out, not_110_out);
  and and_14 (and_14_out, not_111_out, not_112_out, OP3, OP2, not_113_out, not_114_out);
  and and_15 (and_15_out, not_115_out, not_116_out, OP3, not_117_out, not_118_out, OP0);
  and and_16 (and_16_out, not_119_out, not_120_out, OP3, not_121_out, OP1, not_122_out);
  and and_17 (and_17_out, not_123_out, not_124_out, OP3, OP2, not_125_out, OP0);
  and and_18 (and_18_out, OP5, not_126_out, not_127_out, not_128_out, OP1, OP0);
  and and_19 (and_19_out, OP5, not_129_out, OP3, not_130_out, OP1, OP0);
  and and_20 (and_20_out, not_131_out, not_132_out, not_133_out, not_134_out, not_135_out, not_136_out, not_137_out, not_138_out, not_139_out, not_140_out, not_141_out, not_142_out);
  and and_21 (and_21_out, not_143_out, not_144_out, not_145_out, not_146_out, not_147_out, not_148_out, not_149_out, not_150_out, not_151_out, not_152_out, F1, F0);
  and and_22 (and_22_out, not_153_out, not_154_out, not_155_out, not_156_out, not_157_out, not_158_out, not_159_out, not_160_out, not_161_out, not_162_out, F1, not_163_out);
  and and_23 (and_23_out, not_164_out, not_165_out, not_166_out, not_167_out, not_168_out, not_169_out, F5, not_170_out, not_171_out, not_172_out, not_173_out, not_174_out);
  and and_24 (and_24_out, not_175_out, not_176_out, not_177_out, not_178_out, not_179_out, not_180_out, F5, not_181_out, not_182_out, not_183_out, not_184_out, F0);
  and and_25 (and_25_out, not_185_out, not_186_out, not_187_out, not_188_out, not_189_out, not_190_out, F5, not_191_out, not_192_out, not_193_out, F1, not_194_out);
  and and_26 (and_26_out, not_195_out, not_196_out, not_197_out, not_198_out, not_199_out, not_200_out, F5, not_201_out, not_202_out, F2, not_203_out, not_204_out);
  and and_27 (and_27_out, not_205_out, not_206_out, not_207_out, not_208_out, not_209_out, not_210_out, F5, not_211_out, not_212_out, F2, not_213_out, F0);
  and and_28 (and_28_out, not_214_out, not_215_out, not_216_out, not_217_out, not_218_out, not_219_out, F5, not_220_out, not_221_out, F2, F1, F0);
  and and_29 (and_29_out, not_222_out, not_223_out, not_224_out, not_225_out, not_226_out, not_227_out, F5, not_228_out, F3, not_229_out, F1, not_230_out);
  and and_30 (and_30_out, not_231_out, not_232_out, not_233_out, not_234_out, not_235_out, not_236_out, F5, not_237_out, F3, not_238_out, F1, F0);
  and and_31 (and_31_out, not_239_out, not_240_out, not_241_out, not_242_out, not_243_out, not_244_out, not_245_out, not_246_out, F3, F2, not_247_out, not_248_out);
  and and_32 (and_32_out, not_249_out, not_250_out, not_251_out, OP2, not_252_out, not_253_out);
  and and_33 (and_33_out, not_254_out, not_255_out, not_256_out, OP2, not_257_out, OP0);
  and and_34 (and_34_out, OP5, not_258_out, OP3, not_259_out, OP1, OP0);
  or or_1 (R1_USED, and_1_out, and_2_out, and_3_out, and_4_out, and_5_out, and_6_out, and_7_out, and_8_out, and_9_out, and_10_out, and_11_out, and_12_out, and_13_out, and_14_out, and_15_out, and_16_out, and_17_out, and_18_out, and_19_out);
  or or_2 (R2_USED, and_20_out, and_21_out, and_22_out, and_23_out, and_24_out, and_25_out, and_26_out, and_27_out, and_28_out, and_29_out, and_30_out, and_31_out, and_32_out, and_33_out, and_34_out);
endmodule

module \数据检测  (
  input  [4:0] EX_WriteReg_num,
  input  R1_USED,
  input  [4:0] R1_num,
  input  EX_RegWrite,
  input  R2_USED,
  input  [4:0] R2_num,
  input  [4:0] MEM_WriteReg_num,
  input  MEM_RegWrite,
  output EX_CONFLICT,
  output DataHazzard,
  output MEM_CONFLICT
);

  wire and_1_out, and_2_out, and_3_out, and_4_out, comparator_1_eq, comparator_2_eq, comparator_3_eq,
       comparator_4_eq, comparator_5_eq, comparator_6_eq, comparator_7_eq, comparator_8_eq, not_1_out,
       not_2_out, not_3_out, not_4_out, or_1_out, or_2_out;

  Comparator #(.width(5), .mode("twosComplement")) comparator_1 (
    .a(EX_WriteReg_num), .b(R1_num), .eq(comparator_1_eq));  // open: gt, lt
  Comparator #(.width(5), .mode("twosComplement")) comparator_2 (
    .a(R1_num), .b({5{1'b0}}), .eq(comparator_2_eq));  // open: gt, lt
  Comparator #(.width(5), .mode("twosComplement")) comparator_3 (
    .a(R2_num), .b({5{1'b0}}), .eq(comparator_3_eq));  // open: gt, lt
  Comparator #(.width(5), .mode("twosComplement")) comparator_4 (
    .a(R2_num), .b(EX_WriteReg_num), .eq(comparator_4_eq));  // open: gt, lt
  Comparator #(.width(5), .mode("twosComplement")) comparator_5 (
    .a(MEM_WriteReg_num), .b(R1_num), .eq(comparator_5_eq));  // open: gt, lt
  Comparator #(.width(5), .mode("twosComplement")) comparator_6 (
    .a(R1_num), .b({5{1'b0}}), .eq(comparator_6_eq));  // open: gt, lt
  Comparator #(.width(5), .mode("twosComplement")) comparator_7 (
    .a(R2_num), .b({5{1'b0}}), .eq(comparator_7_eq));  // open: gt, lt
  Comparator #(.width(5), .mode("twosComplement")) comparator_8 (
    .a(R2_num), .b(MEM_WriteReg_num), .eq(comparator_8_eq));  // open: gt, lt
  and and_1 (and_1_out, R1_USED, comparator_1_eq, not_1_out);
  not not_1 (not_1_out, comparator_2_eq);
  and and_2 (and_2_out, R2_USED, comparator_4_eq, not_2_out);
  not not_2 (not_2_out, comparator_3_eq);
  and and_3 (and_3_out, R1_USED, comparator_5_eq, not_3_out);
  not not_3 (not_3_out, comparator_6_eq);
  and and_4 (and_4_out, R2_USED, comparator_8_eq, not_4_out);
  not not_4 (not_4_out, comparator_7_eq);
  or or_1 (or_1_out, and_1_out, and_2_out);
  or or_2 (or_2_out, and_3_out, and_4_out);
  and and_5 (EX_CONFLICT, EX_RegWrite, or_1_out);
  and and_6 (MEM_CONFLICT, MEM_RegWrite, or_2_out);
  or or_3 (DataHazzard, EX_CONFLICT, MEM_CONFLICT);
endmodule

module LoadUse_RsRTForward (
  input  R1_USED,
  input  [4:0] R1_num,
  input  [4:0] EX_WriteReg_num,
  input  EX_MemToReg,
  input  R2_USED,
  input  [4:0] R2_num,
  input  EX_RegWrite,
  input  [4:0] MEM_WriteReg_num,
  input  MEM_RegWrite,
  output LoadUse,
  output [1:0] RsForward,
  output [1:0] RtForward
);

  wire and_1_out, and_2_out, and_3_out, and_4_out, and_5_out, and_6_out, comparator_1_eq, comparator_2_eq,
       comparator_3_eq, comparator_4_eq, comparator_5_eq, comparator_6_eq, comparator_7_eq, comparator_8_eq,
       comparator_9_eq, comparator_10_eq, comparator_11_eq, comparator_12_eq, not_1_out, not_2_out,
       not_3_out, not_4_out, not_5_out, not_6_out, or_1_out;
  wire [1:0] and_9_out, and_11_out;

  Comparator #(.width(5), .mode("twosComplement")) comparator_1 (
    .a(R1_num), .b({5{1'b0}}), .eq(comparator_1_eq));  // open: gt, lt
  Comparator #(.width(5), .mode("twosComplement")) comparator_2 (
    .a(R1_num), .b(EX_WriteReg_num), .eq(comparator_2_eq));  // open: gt, lt
  Comparator #(.width(5), .mode("twosComplement")) comparator_3 (
    .a(R2_num), .b({5{1'b0}}), .eq(comparator_3_eq));  // open: gt, lt
  Comparator #(.width(5), .mode("twosComplement")) comparator_4 (
    .a(R2_num), .b(EX_WriteReg_num), .eq(comparator_4_eq));  // open: gt, lt
  not not_1 (not_1_out, comparator_1_eq);
  not not_2 (not_2_out, comparator_3_eq);
  Comparator #(.width(5), .mode("twosComplement")) comparator_5 (
    .a(R1_num), .b({5{1'b0}}), .eq(comparator_5_eq));  // open: gt, lt
  Comparator #(.width(5), .mode("twosComplement")) comparator_6 (
    .a(R1_num), .b({5{1'b0}}), .eq(comparator_6_eq));  // open: gt, lt
  Comparator #(.width(5), .mode("twosComplement")) comparator_7 (
    .a(R2_num), .b({5{1'b0}}), .eq(comparator_7_eq));  // open: gt, lt
  Comparator #(.width(5), .mode("twosComplement")) comparator_8 (
    .a(R2_num), .b(EX_WriteReg_num), .eq(comparator_8_eq));  // open: gt, lt
  Comparator #(.width(5), .mode("twosComplement")) comparator_9 (
    .a(R2_num), .b({5{1'b0}}), .eq(comparator_9_eq));  // open: gt, lt
  Comparator #(.width(5), .mode("twosComplement")) comparator_10 (
    .a(R2_num), .b(MEM_WriteReg_num), .eq(comparator_10_eq));  // open: gt, lt
  and and_1 (and_1_out, R1_USED, not_1_out, comparator_2_eq);
  and and_2 (and_2_out, R2_USED, not_2_out, comparator_4_eq);
  Comparator #(.width(5), .mode("twosComplement")) comparator_11 (
    .a(EX_WriteReg_num), .b(R1_num), .eq(comparator_11_eq));  // open: gt, lt
  not not_3 (not_3_out, comparator_5_eq);
  Comparator #(.width(5), .mode("twosComplement")) comparator_12 (
    .a(MEM_WriteReg_num), .b(R1_num), .eq(comparator_12_eq));  // open: gt, lt
  not not_4 (not_4_out, comparator_6_eq);
  and and_3 (and_3_out, R2_USED, comparator_8_eq, not_5_out);
  not not_5 (not_5_out, comparator_7_eq);
  and and_4 (and_4_out, R2_USED, comparator_10_eq, not_6_out);
  not not_6 (not_6_out, comparator_9_eq);
  or or_1 (or_1_out, and_1_out, and_2_out);
  and and_5 (and_5_out, R1_USED, comparator_11_eq, not_3_out);
  and and_6 (and_6_out, R1_USED, comparator_12_eq, not_4_out);
  and and_7 (LoadUse, or_1_out, EX_MemToReg);
  and and_8 (and_9_out[1], EX_RegWrite, and_5_out);
  and and_9 (and_9_out[0], MEM_RegWrite, and_6_out);
  and and_10 (and_11_out[1], EX_RegWrite, and_3_out);
  and and_11 (and_11_out[0], MEM_RegWrite, and_4_out);
  Multiplexer #(.select(2), .width(2), .disabled("Z"), .enable("false")) multiplexer_1 (
    .in0(2'b00), .in1(2'b01), .in2(2'b10), .in3(2'b10), .out(RsForward), .sel(and_9_out));
  Multiplexer #(.select(2), .width(2), .disabled("Z"), .enable("false")) multiplexer_2 (
    .in0(2'b00), .in1(2'b01), .in2(2'b10), .in3(2'b10), .out(RtForward), .sel(and_11_out));
endmodule
